// Logisim project cpu24.circ as structural Verilog: 25 circuits, main circuit ◇单周期MIPS
module \单周期MIPS  (
  input  IR1,
  input  IR2,
  input  IR3,
  output RegWrite,
  output MemWrite,
  output [31:0] PC,
  output [31:0] IR,
  output [31:0] RDin,
  output [31:0] MDin,
  output [31:0] LedData
);

  wire and_1_out, and_2_out, and_3_out, and_4_out, CLK, clock_2_out, comparator_1_eq, comparator_1_lt,
       d_ff_1_q, En, Go, IR1_t, IR2_t, IR3_t, IRA, IRB, IRC, JAL, JR, Led, mips_alu_1_equal, nand_1_out,
       or_4_out, register_2_q, SignedExt, SYSCALL, W1, W2, W3, \单周期硬布线控制器_1_alu_src , \单周期硬布线控制器_1_beq ,
       \单周期硬布线控制器_1_bne , \单周期硬布线控制器_1_jmp , \单周期硬布线控制器_1_memtoreg , \单周期硬布线控制器_1_regdst ;
  wire [3:0] \单周期硬布线控制器_1_alu_op ;
  wire [4:0] multiplexer_4_out, multiplexer_5_out, multiplexer_6_out, multiplexer_7_out;
  wire [12:0] CNT_num;
  wire [15:0] \总周期数 ;
  wire [31:0] A, adder_1_out, adder_2_out, bit_extender_1_out, bit_extender_2_out, bit_extender_3_out,
       mips_alu_1_result, multiplexer_1_out, multiplexer_2_out, multiplexer_3_out, multiplexer_8_out,
       multiplexer_10_out, multiplexer_11_out, ram_1_data, shifter_1_out, shifter_2_out;

  Clock #(.highDuration(1), .lowDuration(1)) clock_1 ();  // open: out
  Button _1 (.out(IRA));
  Button _2 (.out(IRB));
  Button _3 (.out(IRC));
  Button \u_继续运行  (.out(Go));
  LED #(.active("true")) led_1 (.in(W1));
  LED #(.active("true")) led_2 (.in(W2));
  LED #(.active("true")) led_3 (.in(W3));
  Hex_Digit_Display hex_digit_display_1 (.value(LedData[31:28]));  // open: dp
  D_Flip_Flop #(.trigger("high"), .Pre_Clr_Positions("LEGACY"), .NegatePresetClear("false"), .enable("true"), .NewFFLayout("false")) d_ff_1 (.Q(d_ff_1_q));  // open: clk, D, Qn, preset, en, reset
  // Probe on 13'h608
  Hex_Digit_Display hex_digit_display_2 (.value(LedData[27:24]));  // open: dp
  Hex_Digit_Display hex_digit_display_3 (.value(LedData[23:20]));  // open: dp
  Comparator #(.width(13), .mode("twosComplement")) comparator_1 (
    .a(CNT_num), .b(13'h608), .eq(comparator_1_eq), .lt(comparator_1_lt));  // open: gt
  Clock #(.highDuration(1), .lowDuration(1)) clock_2 (.out(clock_2_out));
  Multiplexer #(.select(1), .width(32), .disabled("Z"), .enable("false")) multiplexer_1 (
    .in0(adder_1_out), .in1(adder_2_out), .out(multiplexer_1_out), .sel(or_4_out));
  Multiplexer #(.select(1), .width(32), .disabled("Z"), .enable("false")) multiplexer_2 (
    .in0(multiplexer_1_out), .in1(multiplexer_3_out), .out(multiplexer_2_out), .sel(\单周期硬布线控制器_1_jmp ));
  Hex_Digit_Display hex_digit_display_4 (.value(LedData[15:12]));  // open: dp
  Hex_Digit_Display hex_digit_display_5 (.value(LedData[19:16]));  // open: dp
  Counter #(.width(13), .max('h1fff), .ongoal("stay"), .trigger("rising"), .behavior("old")) counter_1 (
    .count(comparator_1_lt), .Q(CNT_num), .clk(clock_2_out));  // open: load, D, carry, clr, preset
  Register #(.width(32), .trigger("rising"), .Select("low")) u_PC (
    .D(multiplexer_2_out), .en(En), .Q(PC), .clk(CLK));  // open: clr
  Hex_Digit_Display hex_digit_display_6 (.value(LedData[11:8]));  // open: dp
  Hex_Digit_Display hex_digit_display_7 (.value(LedData[7:4]));  // open: dp
  // Probe on \总周期数 
  nand nand_1 (nand_1_out, d_ff_1_q, comparator_1_eq);
  Multiplexer #(.select(1), .width(32), .disabled("Z"), .enable("false")) multiplexer_3 (
    .in0(shifter_1_out), .in1(A), .out(multiplexer_3_out), .sel(JR));
  Hex_Digit_Display hex_digit_display_8 (.value(LedData[3:0]));  // open: dp
  assign CLK = nand_1_out ? clock_2_out : 1'bz;  // Controlled_Buffer controlled_buffer_1
  Pull_Resistor #(.pull(1)) pull_resistor_1 (.node(CLK));
  Adder #(.width(32)) adder_1 (.a(PC), .b(32'h4), .out(adder_1_out));  // open: cin, cout
  ROM #(.addrWidth(10), .dataWidth(32), .Select("high")) rom_1 (.addr(PC[11:2]), .data(IR));
  or or_1 (IR1_t, IR1, IRA);
  // Mips_Probe mips_probe_1: pin names not known; wires that end beside it: IR
  or or_2 (IR2_t, IR2, IRB);
  Multiplexer #(.select(1), .width(5), .disabled("Z"), .enable("false")) multiplexer_4 (
    .in0(IR[20:16]), .in1(IR[15:11]), .out(multiplexer_4_out), .sel(\单周期硬布线控制器_1_regdst ));
  Multiplexer #(.select(1), .width(5), .disabled("Z"), .enable("false")) multiplexer_5 (
    .in0(IR[25:21]), .in1(5'b00100), .out(multiplexer_5_out), .sel(SYSCALL));
  Multiplexer #(.select(1), .width(5), .disabled("Z"), .enable("false")) multiplexer_6 (
    .in0(IR[20:16]), .in1(5'b00010), .out(multiplexer_6_out), .sel(SYSCALL));
  Multiplexer #(.select(1), .width(5), .disabled("Z"), .enable("false")) multiplexer_7 (
    .in0(multiplexer_4_out), .in1({5{1'b1}}), .out(multiplexer_7_out), .sel(JAL));
  assign bit_extender_1_out = {{16{1'b0}}, IR[15:0]};  // Bit_Extender bit_extender_1
  assign bit_extender_2_out = {{16{IR[15]}}, IR[15:0]};  // Bit_Extender bit_extender_2
  assign bit_extender_3_out = {{6{IR[25]}}, IR[25:0]};  // Bit_Extender bit_extender_3
  or or_3 (IR3_t, IR3, IRC);
  \单周期硬布线控制器  \u_单周期硬布线控制器_1  (
    .Func(IR[5:0]), .OP(IR[31:26]), .ALU_OP(\单周期硬布线控制器_1_alu_op ), .MemToReg(\单周期硬布线控制器_1_memtoreg ),
    .MemWrite(MemWrite), .ALU_SRC(\单周期硬布线控制器_1_alu_src ), .RegWrite(RegWrite), .SysCALL(SYSCALL),
    .SignedExt(SignedExt), .RegDst(\单周期硬布线控制器_1_regdst ), .JR(JR), .JMP(\单周期硬布线控制器_1_jmp ),
    .Beq(\单周期硬布线控制器_1_beq ), .JAL(JAL), .Bne(\单周期硬布线控制器_1_bne ));  // open: SLLV, LUI, SB, BGTZ, in_3, MFC0, MTC0
  Multiplexer #(.select(1), .width(32), .disabled("Z"), .enable("false")) multiplexer_8 (
    .in0(bit_extender_1_out), .in1(bit_extender_2_out), .out(multiplexer_8_out), .sel(SignedExt));
  Multiplexer #(.select(1), .width(32), .disabled("Z"), .enable("false")) multiplexer_9 (
    .in0(multiplexer_11_out), .in1(adder_1_out), .out(RDin), .sel(JAL));
  Shifter #(.width(32), .shift("ll")) shifter_1 (.in(bit_extender_3_out), .\dist (5'b00010), .out(shifter_1_out));
  and and_1 (and_1_out, Led, SYSCALL);
  Register #(.width(32), .trigger("rising"), .Select("low")) register_1 (
    .D(A), .en(and_1_out), .Q(LedData), .clk(CLK));  // open: clr
  and and_2 (and_2_out, \单周期硬布线控制器_1_beq , mips_alu_1_equal);
  MIPS_Regifile mips_regifile_1 (
    .Din(RDin), .Clk(CLK), .R1(A), .R2(MDin), .WE(RegWrite), .W_num(multiplexer_7_out),
    .R1_num(multiplexer_5_out), .R2_num(multiplexer_6_out));
  and and_3 (and_3_out, \单周期硬布线控制器_1_bne , ~mips_alu_1_equal);  // AND_Gate
  Multiplexer #(.select(1), .width(32), .disabled("Z"), .enable("false")) multiplexer_10 (
    .in0(MDin), .in1(multiplexer_8_out), .out(multiplexer_10_out), .sel(\单周期硬布线控制器_1_alu_src ));
  or or_4 (or_4_out, and_2_out, and_3_out);
  Comparator #(.width(32), .mode("twosComplement")) comparator_2 (.a(32'h22), .b(MDin), .eq(Led));  // open: gt, lt
  Shifter #(.width(32), .shift("ll")) shifter_2 (.in(multiplexer_8_out), .\dist (5'b00010), .out(shifter_2_out));
  Counter #(.width(16), .max('hffff), .ongoal("wrap"), .trigger("rising"), .behavior("new")) counter_2 (
    .Q(\总周期数 ), .clk(CLK), .down(En));  // open: load, D, count, carry, clr, preset
  MIPS_ALU mips_alu_1 (
    .X(A), .Y(multiplexer_10_out), .AluOP(\单周期硬布线控制器_1_alu_op ), .Equal(mips_alu_1_equal),
    .Result(mips_alu_1_result), .shamt(IR[10:6]));  // open: Result_2
  Adder #(.width(32)) adder_2 (.a(shifter_2_out), .b(adder_1_out), .out(adder_2_out));  // open: cin, cout
  and and_4 (and_4_out, SYSCALL, ~Led);  // AND_Gate
  Register #(.width(1), .trigger("rising"), .Select("low")) register_2 (
    .D(SYSCALL), .en(and_4_out), .Q(register_2_q), .clk(CLK), .clr(Go));
  Multiplexer #(.select(1), .width(32), .disabled("Z"), .enable("false")) multiplexer_11 (
    .in0(mips_alu_1_result), .in1(ram_1_data), .out(multiplexer_11_out), .sel(\单周期硬布线控制器_1_memtoreg ));
  RAM #(.addrWidth(10), .dataWidth(32), .bus("separate"), .Select("high")) ram_1 (
    .addr(mips_alu_1_result[11:2]), .din(MDin), .data(ram_1_data), .str(MemWrite), .clk(CLK), .ld(1'b1));  // open: sel, clr
  not not_1 (En, register_2_q);

  // Notes on the sheet:
  //   中断源
  //   中断等待指示
  //   总复位信号应将除ROM以外所有存储组件全部清零
  //   控制位
  //   暂停节拍，不能为0
  //   戳工具置1进入计数暂停模式，ctrl+k时钟自动运行到对应节拍暂停
  //   ctrl+k关闭时钟连续运行，将控制位置零，进入单步调试模式调试
  //   用这个时钟源需要去掉电路中的其他时钟源
  //   数码管输出
  //   数码管输出应该用寄存器锁存，否则显示数据只能一闪而过
  //   可计数暂停的时钟源
  //   指令存储器
  //   contents of rom_1 (hex, n*v repeats v):
  //   20110001 8000c05 20110001 20120002 20130003 8000c09 20110001 20120002 20130003 8000c0d 20110001
  //   20120002 20130003 8000c11 20110001 20120002 20130003 c000cb8 20100001 20110001 118fc0 112020
  //   20020022 c 118882 12200001 8000c15 112020 20020022 c 20110001 118880 112020 20020022 c 12200001
  //   8000c1f 20110001 118fc0 112020 20020022 c 1188c3 112020 20020022 c 118903 112020 20020022 c 118903
  //   112020 20020022 c 118903 112020 20020022 c 118903 112020 20020022 c 118903 112020 20020022 c 118903
  //   112020 20020022 c 118903 112020 20020022 c 20100001 109fc0 139fc3 8021 2012000c 24160003 26100001
  //   3210000f 20080008 20090001 139900 2709825 132020 20020022 c 1094022 1500fff9 22100001 2018000f
  //   2188024 108700 20080008 20090001 139902 2709825 132021 20020022 c 1094022 1500fff9 108702 2c9b022
  //   12c00001 8000c50 4020 1084027 84400 3508ffff 82021 20020022 c 2010ffff 20110000 ae300000 22100001
  //   22310004 ae300000 22100001 22310004 ae300000 22100001 22310004 ae300000 22100001 22310004 ae300000
  //   22100001 22310004 ae300000 22100001 22310004 ae300000 22100001 22310004 ae300000 22100001 22310004
  //   ae300000 22100001 22310004 ae300000 22100001 22310004 ae300000 22100001 22310004 ae300000 22100001
  //   22310004 ae300000 22100001 22310004 ae300000 22100001 22310004 ae300000 22100001 22310004 ae300000
  //   22100001 22310004 22100001 8020 2011003c 8e130000 8e340000 274402a 11000002 ae330000 ae140000
  //   2231fffc 1611fff8 102020 20020022 c 22100004 2011003c 1611fff2 20020032 c 20100000 22100001 102020
  //   20020022 c 22100002 102020 20020022 c 22100003 102020 20020022 c 22100004 102020 20020022 c 22100005
  //   102020 20020022 c 22100006 102020 20020022 c 22100007 102020 20020022 c 22100008 102020 20020022
  //   20020022 c 3e00008
  //   OP
  //   Func
  //   rs
  //   指令字
  //   rt
  //   rd
  //   JMP
  //   JR
  //   OP
  //   Func
  //   Beq
  //   Bne
  //   MemToReg
  //   MemWrite
  //   AluOP
  //   AluSrcB
  //   RegWrite
  //   JAL
  //   RegDst
  //   Syscall
  //   为方便自动评测，需要输出PC，IR，寄存器堆写如数据RDin
  //   RAM写使能MemWrite、RAM写入数据MDin等信号
endmodule

// 单周期硬布线控制器
module \单周期硬布线控制器  (
  input  [5:0] OP,
  input  [5:0] Func,
  input  [4:0] in_3,
  output [3:0] ALU_OP,
  output MemToReg,
  output MemWrite,
  output ALU_SRC,
  output RegWrite,
  output SysCALL,
  output SignedExt,
  output RegDst,
  output Beq,
  output Bne,
  output JR,
  output JMP,
  output JAL,
  output SLLV,
  output LUI,
  output SB,
  output BGTZ,
  output MFC0,
  output MTC0
);

  \运算控制器自动生成  \u_运算控制器自动生成_1  (
    .OP0(OP[0]), .OP1(OP[1]), .OP2(OP[2]), .OP3(OP[3]), .OP4(OP[4]), .OP5(OP[5]), .F0(Func[0]), .F1(Func[1]),
    .F2(Func[2]), .F3(Func[3]), .F4(Func[4]), .F5(Func[5]), .S0(ALU_OP[0]), .S1(ALU_OP[1]), .S2(ALU_OP[2]),
    .S3(ALU_OP[3]));
  \控制信号自动生成  \u_控制信号自动生成_1  (
    .OP0(OP[0]), .OP1(OP[1]), .OP2(OP[2]), .OP3(OP[3]), .OP4(OP[4]), .OP5(OP[5]), .F0(Func[0]), .F1(Func[1]),
    .F2(Func[2]), .F3(Func[3]), .F4(Func[4]), .F5(Func[5]), .MemToReg(MemToReg), .MemWrite(MemWrite),
    .ALU_SRC(ALU_SRC), .RegWrite(RegWrite), .SysCALL(SysCALL), .SignedExt(SignedExt), .RegDst(RegDst),
    .BEQ(Beq), .BNE(Bne), .JR(JR), .JUMP(JMP), .JAL(JAL), .SLLV(SLLV), .LUI(LUI), .SB(SB), .BGTZ(BGTZ));
  and and_1 (MFC0, ~OP[0], ~OP[1], ~OP[2], ~OP[3], OP[4], ~OP[5], ~in_3[0], ~in_3[1], ~in_3[2], ~in_3[3], ~in_3[4]);  // AND_Gate
  and and_2 (MTC0, ~OP[0], ~OP[1], ~OP[2], ~OP[3], OP[4], ~OP[5], ~in_3[0], ~in_3[1], in_3[2], ~in_3[3], ~in_3[4]);  // AND_Gate

  // Other names for the same wires on the sheet: OP_CODE[5:0] = OP

  // Notes on the sheet:
  //   运算器控制器，根据指令生成运算器功能选择信号
  //   控制信号生成，产生数据通路需要的其他控制信号
endmodule

// 运算器控制器
module \运算控制器自动生成  (
  input  OP0,
  input  OP1,
  input  OP2,
  input  OP3,
  input  OP4,
  input  OP5,
  input  F0,
  input  F1,
  input  F2,
  input  F3,
  input  F4,
  input  F5,
  output S0,
  output S1,
  output S2,
  output S3
);

  wire and_1_out, and_2_out, and_3_out, and_4_out, and_5_out, and_6_out, and_7_out, and_8_out, and_9_out,
       and_10_out, and_11_out, and_12_out, and_13_out, and_14_out, and_15_out, and_16_out, and_17_out,
       and_18_out, and_19_out, and_20_out, and_21_out, and_22_out, and_23_out, and_24_out, and_25_out,
       and_26_out, and_27_out, and_28_out, and_29_out, and_30_out, and_31_out, and_32_out, and_33_out,
       and_34_out, and_35_out, and_36_out, not_1_out, not_2_out, not_3_out, not_4_out, not_5_out, not_6_out,
       not_7_out, not_8_out, not_9_out, not_10_out, not_11_out, not_12_out, not_13_out, not_14_out,
       not_15_out, not_16_out, not_17_out, not_18_out, not_19_out, not_20_out, not_21_out, not_22_out,
       not_23_out, not_24_out, not_25_out, not_26_out, not_27_out, not_28_out, not_29_out, not_30_out,
       not_31_out, not_32_out, not_33_out, not_34_out, not_35_out, not_36_out, not_37_out, not_38_out,
       not_39_out, not_40_out, not_41_out, not_42_out, not_43_out, not_44_out, not_45_out, not_46_out,
       not_47_out, not_48_out, not_49_out, not_50_out, not_51_out, not_52_out, not_53_out, not_54_out,
       not_55_out, not_56_out, not_57_out, not_58_out, not_59_out, not_60_out, not_61_out, not_62_out,
       not_63_out, not_64_out, not_65_out, not_66_out, not_67_out, not_68_out, not_69_out, not_70_out,
       not_71_out, not_72_out, not_73_out, not_74_out, not_75_out, not_76_out, not_77_out, not_78_out,
       not_79_out, not_80_out, not_81_out, not_82_out, not_83_out, not_84_out, not_85_out, not_86_out,
       not_87_out, not_88_out, not_89_out, not_90_out, not_91_out, not_92_out, not_93_out, not_94_out,
       not_95_out, not_96_out, not_97_out, not_98_out, not_99_out, not_100_out, not_101_out, not_102_out,
       not_103_out, not_104_out, not_105_out, not_106_out, not_107_out, not_108_out, not_109_out,
       not_110_out, not_111_out, not_112_out, not_113_out, not_114_out, not_115_out, not_116_out,
       not_117_out, not_118_out, not_119_out, not_120_out, not_121_out, not_122_out, not_123_out,
       not_124_out, not_125_out, not_126_out, not_127_out, not_128_out, not_129_out, not_130_out,
       not_131_out, not_132_out, not_133_out, not_134_out, not_135_out, not_136_out, not_137_out,
       not_138_out, not_139_out, not_140_out, not_141_out, not_142_out, not_143_out, not_144_out,
       not_145_out, not_146_out, not_147_out, not_148_out, not_149_out, not_150_out, not_151_out,
       not_152_out, not_153_out, not_154_out, not_155_out, not_156_out, not_157_out, not_158_out,
       not_159_out, not_160_out, not_161_out, not_162_out, not_163_out, not_164_out, not_165_out,
       not_166_out, not_167_out, not_168_out, not_169_out, not_170_out, not_171_out, not_172_out,
       not_173_out, not_174_out, not_175_out, not_176_out, not_177_out, not_178_out, not_179_out,
       not_180_out, not_181_out, not_182_out, not_183_out, not_184_out, not_185_out, not_186_out,
       not_187_out, not_188_out, not_189_out, not_190_out, not_191_out, not_192_out, not_193_out,
       not_194_out, not_195_out, not_196_out, not_197_out, not_198_out, not_199_out, not_200_out,
       not_201_out, not_202_out, not_203_out, not_204_out, not_205_out, not_206_out, not_207_out,
       not_208_out, not_209_out, not_210_out, not_211_out, not_212_out, not_213_out, not_214_out,
       not_215_out, not_216_out, not_217_out, not_218_out, not_219_out, not_220_out, not_221_out,
       not_222_out, not_223_out, not_224_out, not_225_out, not_226_out, not_227_out, not_228_out,
       not_229_out, not_230_out, not_231_out, not_232_out, not_233_out, not_234_out, not_235_out,
       not_236_out, not_237_out, not_238_out, not_239_out, not_240_out, not_241_out, not_242_out,
       not_243_out, not_244_out;

  not not_1 (not_1_out, OP5);
  not not_2 (not_2_out, OP4);
  not not_3 (not_3_out, OP3);
  not not_4 (not_4_out, OP2);
  not not_5 (not_5_out, OP1);
  not not_6 (not_6_out, OP0);
  not not_7 (not_7_out, F5);
  not not_8 (not_8_out, F4);
  not not_9 (not_9_out, F3);
  not not_10 (not_10_out, F2);
  not not_11 (not_11_out, OP5);
  not not_12 (not_12_out, OP4);
  not not_13 (not_13_out, OP3);
  not not_14 (not_14_out, OP2);
  not not_15 (not_15_out, OP1);
  not not_16 (not_16_out, OP0);
  not not_17 (not_17_out, F4);
  not not_18 (not_18_out, F3);
  not not_19 (not_19_out, F2);
  not not_20 (not_20_out, F1);
  not not_21 (not_21_out, F0);
  not not_22 (not_22_out, OP5);
  not not_23 (not_23_out, OP4);
  not not_24 (not_24_out, OP3);
  not not_25 (not_25_out, OP2);
  not not_26 (not_26_out, OP1);
  not not_27 (not_27_out, OP0);
  not not_28 (not_28_out, F4);
  not not_29 (not_29_out, F3);
  not not_30 (not_30_out, F2);
  not not_31 (not_31_out, F1);
  not not_32 (not_32_out, OP5);
  not not_33 (not_33_out, OP4);
  not not_34 (not_34_out, OP3);
  not not_35 (not_35_out, OP2);
  not not_36 (not_36_out, OP1);
  not not_37 (not_37_out, OP0);
  not not_38 (not_38_out, F4);
  not not_39 (not_39_out, F3);
  not not_40 (not_40_out, F1);
  not not_41 (not_41_out, F0);
  not not_42 (not_42_out, OP5);
  not not_43 (not_43_out, OP4);
  not not_44 (not_44_out, OP3);
  not not_45 (not_45_out, OP2);
  not not_46 (not_46_out, OP1);
  not not_47 (not_47_out, OP0);
  not not_48 (not_48_out, F4);
  not not_49 (not_49_out, F2);
  not not_50 (not_50_out, F0);
  not not_51 (not_51_out, OP5);
  not not_52 (not_52_out, OP4);
  not not_53 (not_53_out, OP2);
  not not_54 (not_54_out, OP1);
  not not_55 (not_55_out, OP0);
  not not_56 (not_56_out, OP5);
  not not_57 (not_57_out, OP4);
  not not_58 (not_58_out, OP1);
  not not_59 (not_59_out, OP0);
  not not_60 (not_60_out, OP5);
  not not_61 (not_61_out, OP4);
  not not_62 (not_62_out, OP2);
  not not_63 (not_63_out, OP1);
  not not_64 (not_64_out, OP5);
  not not_65 (not_65_out, OP4);
  not not_66 (not_66_out, OP2);
  not not_67 (not_67_out, OP0);
  not not_68 (not_68_out, OP4);
  not not_69 (not_69_out, OP3);
  not not_70 (not_70_out, OP2);
  not not_71 (not_71_out, OP4);
  not not_72 (not_72_out, OP2);
  not not_73 (not_73_out, OP4);
  not not_74 (not_74_out, OP2);
  not not_75 (not_75_out, OP1);
  not not_76 (not_76_out, OP0);
  not not_77 (not_77_out, OP5);
  not not_78 (not_78_out, OP4);
  not not_79 (not_79_out, OP3);
  not not_80 (not_80_out, OP2);
  not not_81 (not_81_out, OP1);
  not not_82 (not_82_out, OP0);
  not not_83 (not_83_out, F5);
  not not_84 (not_84_out, F4);
  not not_85 (not_85_out, F3);
  not not_86 (not_86_out, F2);
  not not_87 (not_87_out, F0);
  not not_88 (not_88_out, OP5);
  not not_89 (not_89_out, OP4);
  not not_90 (not_90_out, OP3);
  not not_91 (not_91_out, OP2);
  not not_92 (not_92_out, OP1);
  not not_93 (not_93_out, OP0);
  not not_94 (not_94_out, F4);
  not not_95 (not_95_out, F3);
  not not_96 (not_96_out, F2);
  not not_97 (not_97_out, F0);
  not not_98 (not_98_out, OP5);
  not not_99 (not_99_out, OP4);
  not not_100 (not_100_out, OP3);
  not not_101 (not_101_out, OP2);
  not not_102 (not_102_out, OP1);
  not not_103 (not_103_out, OP0);
  not not_104 (not_104_out, F4);
  not not_105 (not_105_out, F3);
  not not_106 (not_106_out, F1);
  not not_107 (not_107_out, F0);
  not not_108 (not_108_out, OP5);
  not not_109 (not_109_out, OP4);
  not not_110 (not_110_out, OP3);
  not not_111 (not_111_out, OP2);
  not not_112 (not_112_out, OP1);
  not not_113 (not_113_out, OP0);
  not not_114 (not_114_out, F4);
  not not_115 (not_115_out, F3);
  not not_116 (not_116_out, OP5);
  not not_117 (not_117_out, OP4);
  not not_118 (not_118_out, OP3);
  not not_119 (not_119_out, OP2);
  not not_120 (not_120_out, OP1);
  not not_121 (not_121_out, OP0);
  not not_122 (not_122_out, F4);
  not not_123 (not_123_out, F2);
  not not_124 (not_124_out, F0);
  not not_125 (not_125_out, OP5);
  not not_126 (not_126_out, OP4);
  not not_127 (not_127_out, OP1);
  not not_128 (not_128_out, OP0);
  not not_129 (not_129_out, OP5);
  not not_130 (not_130_out, OP4);
  not not_131 (not_131_out, OP2);
  not not_132 (not_132_out, OP0);
  not not_133 (not_133_out, OP5);
  not not_134 (not_134_out, OP4);
  not not_135 (not_135_out, OP3);
  not not_136 (not_136_out, OP2);
  not not_137 (not_137_out, OP1);
  not not_138 (not_138_out, OP0);
  not not_139 (not_139_out, F4);
  not not_140 (not_140_out, F3);
  not not_141 (not_141_out, F2);
  not not_142 (not_142_out, F1);
  not not_143 (not_143_out, F0);
  not not_144 (not_144_out, OP5);
  not not_145 (not_145_out, OP4);
  not not_146 (not_146_out, OP3);
  not not_147 (not_147_out, OP2);
  not not_148 (not_148_out, OP1);
  not not_149 (not_149_out, OP0);
  not not_150 (not_150_out, F4);
  not not_151 (not_151_out, F3);
  not not_152 (not_152_out, F2);
  not not_153 (not_153_out, F1);
  not not_154 (not_154_out, OP5);
  not not_155 (not_155_out, OP4);
  not not_156 (not_156_out, OP3);
  not not_157 (not_157_out, OP2);
  not not_158 (not_158_out, OP1);
  not not_159 (not_159_out, OP0);
  not not_160 (not_160_out, F4);
  not not_161 (not_161_out, F3);
  not not_162 (not_162_out, F2);
  not not_163 (not_163_out, F0);
  not not_164 (not_164_out, OP5);
  not not_165 (not_165_out, OP4);
  not not_166 (not_166_out, OP3);
  not not_167 (not_167_out, OP2);
  not not_168 (not_168_out, OP1);
  not not_169 (not_169_out, OP0);
  not not_170 (not_170_out, F4);
  not not_171 (not_171_out, F3);
  not not_172 (not_172_out, F1);
  not not_173 (not_173_out, F0);
  not not_174 (not_174_out, OP5);
  not not_175 (not_175_out, OP4);
  not not_176 (not_176_out, OP3);
  not not_177 (not_177_out, OP2);
  not not_178 (not_178_out, OP1);
  not not_179 (not_179_out, OP0);
  not not_180 (not_180_out, F4);
  not not_181 (not_181_out, F2);
  not not_182 (not_182_out, OP5);
  not not_183 (not_183_out, OP4);
  not not_184 (not_184_out, OP2);
  not not_185 (not_185_out, OP1);
  not not_186 (not_186_out, OP0);
  not not_187 (not_187_out, OP5);
  not not_188 (not_188_out, OP4);
  not not_189 (not_189_out, OP1);
  not not_190 (not_190_out, OP0);
  not not_191 (not_191_out, OP5);
  not not_192 (not_192_out, OP4);
  not not_193 (not_193_out, OP2);
  not not_194 (not_194_out, OP1);
  not not_195 (not_195_out, OP4);
  not not_196 (not_196_out, OP3);
  not not_197 (not_197_out, OP2);
  not not_198 (not_198_out, OP4);
  not not_199 (not_199_out, OP2);
  not not_200 (not_200_out, OP4);
  not not_201 (not_201_out, OP2);
  not not_202 (not_202_out, OP1);
  not not_203 (not_203_out, OP0);
  not not_204 (not_204_out, OP5);
  not not_205 (not_205_out, OP4);
  not not_206 (not_206_out, OP3);
  not not_207 (not_207_out, OP2);
  not not_208 (not_208_out, OP1);
  not not_209 (not_209_out, OP0);
  not not_210 (not_210_out, F4);
  not not_211 (not_211_out, F3);
  not not_212 (not_212_out, F1);
  not not_213 (not_213_out, OP5);
  not not_214 (not_214_out, OP4);
  not not_215 (not_215_out, OP3);
  not not_216 (not_216_out, OP2);
  not not_217 (not_217_out, OP1);
  not not_218 (not_218_out, OP0);
  not not_219 (not_219_out, F4);
  not not_220 (not_220_out, F3);
  not not_221 (not_221_out, OP5);
  not not_222 (not_222_out, OP4);
  not not_223 (not_223_out, OP3);
  not not_224 (not_224_out, OP2);
  not not_225 (not_225_out, OP1);
  not not_226 (not_226_out, OP0);
  not not_227 (not_227_out, F4);
  not not_228 (not_228_out, F2);
  not not_229 (not_229_out, F0);
  not not_230 (not_230_out, OP5);
  not not_231 (not_231_out, OP4);
  not not_232 (not_232_out, OP3);
  not not_233 (not_233_out, OP2);
  not not_234 (not_234_out, OP1);
  not not_235 (not_235_out, OP0);
  not not_236 (not_236_out, F4);
  not not_237 (not_237_out, F2);
  not not_238 (not_238_out, OP5);
  not not_239 (not_239_out, OP4);
  not not_240 (not_240_out, OP2);
  not not_241 (not_241_out, OP0);
  not not_242 (not_242_out, OP5);
  not not_243 (not_243_out, OP4);
  not not_244 (not_244_out, OP1);
  and and_1 (and_1_out, not_1_out, not_2_out, not_3_out, not_4_out, not_5_out, not_6_out, not_7_out, not_8_out, not_9_out, not_10_out, F1, F0);
  and and_2 (and_2_out, not_11_out, not_12_out, not_13_out, not_14_out, not_15_out, not_16_out, F5, not_17_out, not_18_out, not_19_out, not_20_out, not_21_out);
  and and_3 (and_3_out, not_22_out, not_23_out, not_24_out, not_25_out, not_26_out, not_27_out, F5, not_28_out, not_29_out, not_30_out, not_31_out, F0);
  and and_4 (and_4_out, not_32_out, not_33_out, not_34_out, not_35_out, not_36_out, not_37_out, F5, not_38_out, not_39_out, F2, not_40_out, not_41_out);
  and and_5 (and_5_out, not_42_out, not_43_out, not_44_out, not_45_out, not_46_out, not_47_out, F5, not_48_out, F3, not_49_out, F1, not_50_out);
  and and_6 (and_6_out, not_51_out, not_52_out, OP3, not_53_out, not_54_out, not_55_out);
  and and_7 (and_7_out, not_56_out, not_57_out, OP3, OP2, not_58_out, not_59_out);
  and and_8 (and_8_out, not_60_out, not_61_out, OP3, not_62_out, not_63_out, OP0);
  and and_9 (and_9_out, not_64_out, not_65_out, OP3, not_66_out, OP1, not_67_out);
  and and_10 (and_10_out, OP5, not_68_out, not_69_out, not_70_out, OP1, OP0);
  and and_11 (and_11_out, OP5, not_71_out, OP3, not_72_out, OP1, OP0);
  and and_12 (and_12_out, OP5, not_73_out, OP3, not_74_out, not_75_out, not_76_out);
  and and_13 (and_13_out, not_77_out, not_78_out, not_79_out, not_80_out, not_81_out, not_82_out, not_83_out, not_84_out, not_85_out, not_86_out, F1, not_87_out);
  and and_14 (and_14_out, not_88_out, not_89_out, not_90_out, not_91_out, not_92_out, not_93_out, F5, not_94_out, not_95_out, not_96_out, F1, not_97_out);
  and and_15 (and_15_out, not_98_out, not_99_out, not_100_out, not_101_out, not_102_out, not_103_out, F5, not_104_out, not_105_out, F2, not_106_out, not_107_out);
  and and_16 (and_16_out, not_108_out, not_109_out, not_110_out, not_111_out, not_112_out, not_113_out, F5, not_114_out, not_115_out, F2, F1, F0);
  and and_17 (and_17_out, not_116_out, not_117_out, not_118_out, not_119_out, not_120_out, not_121_out, F5, not_122_out, F3, not_123_out, F1, not_124_out);
  and and_18 (and_18_out, not_125_out, not_126_out, OP3, OP2, not_127_out, not_128_out);
  and and_19 (and_19_out, not_129_out, not_130_out, OP3, not_131_out, OP1, not_132_out);
  and and_20 (and_20_out, not_133_out, not_134_out, not_135_out, not_136_out, not_137_out, not_138_out, F5, not_139_out, not_140_out, not_141_out, not_142_out, not_143_out);
  and and_21 (and_21_out, not_144_out, not_145_out, not_146_out, not_147_out, not_148_out, not_149_out, F5, not_150_out, not_151_out, not_152_out, not_153_out, F0);
  and and_22 (and_22_out, not_154_out, not_155_out, not_156_out, not_157_out, not_158_out, not_159_out, F5, not_160_out, not_161_out, not_162_out, F1, not_163_out);
  and and_23 (and_23_out, not_164_out, not_165_out, not_166_out, not_167_out, not_168_out, not_169_out, F5, not_170_out, not_171_out, F2, not_172_out, not_173_out);
  and and_24 (and_24_out, not_174_out, not_175_out, not_176_out, not_177_out, not_178_out, not_179_out, F5, not_180_out, F3, not_181_out, F1, F0);
  and and_25 (and_25_out, not_182_out, not_183_out, OP3, not_184_out, not_185_out, not_186_out);
  and and_26 (and_26_out, not_187_out, not_188_out, OP3, OP2, not_189_out, not_190_out);
  and and_27 (and_27_out, not_191_out, not_192_out, OP3, not_193_out, not_194_out, OP0);
  and and_28 (and_28_out, OP5, not_195_out, not_196_out, not_197_out, OP1, OP0);
  and and_29 (and_29_out, OP5, not_198_out, OP3, not_199_out, OP1, OP0);
  and and_30 (and_30_out, OP5, not_200_out, OP3, not_201_out, not_202_out, not_203_out);
  and and_31 (and_31_out, not_204_out, not_205_out, not_206_out, not_207_out, not_208_out, not_209_out, F5, not_210_out, not_211_out, F2, not_212_out, F0);
  and and_32 (and_32_out, not_213_out, not_214_out, not_215_out, not_216_out, not_217_out, not_218_out, F5, not_219_out, not_220_out, F2, F1, F0);
  and and_33 (and_33_out, not_221_out, not_222_out, not_223_out, not_224_out, not_225_out, not_226_out, F5, not_227_out, F3, not_228_out, F1, not_229_out);
  and and_34 (and_34_out, not_230_out, not_231_out, not_232_out, not_233_out, not_234_out, not_235_out, F5, not_236_out, F3, not_237_out, F1, F0);
  and and_35 (and_35_out, not_238_out, not_239_out, OP3, not_240_out, OP1, not_241_out);
  and and_36 (and_36_out, not_242_out, not_243_out, OP3, OP2, not_244_out, OP0);
  or or_1 (S1, and_13_out, and_14_out, and_15_out, and_16_out, and_17_out, and_18_out, and_19_out);
  or or_2 (S2, and_20_out, and_21_out, and_22_out, and_23_out, and_24_out, and_25_out, and_26_out, and_27_out, and_28_out, and_29_out, and_30_out);
  or or_3 (S3, and_31_out, and_32_out, and_33_out, and_34_out, and_35_out, and_36_out);
  or or_4 (S0, and_1_out, and_2_out, and_3_out, and_4_out, and_5_out, and_6_out, and_7_out, and_8_out, and_9_out, and_10_out, and_11_out, and_12_out);
endmodule

// 控制信号生成
module \控制信号自动生成  (
  input  OP0,
  input  OP1,
  input  OP2,
  input  OP3,
  input  OP4,
  input  OP5,
  input  F0,
  input  F1,
  input  F2,
  input  F3,
  input  F4,
  input  F5,
  output MemToReg,
  output MemWrite,
  output ALU_SRC,
  output RegWrite,
  output SysCALL,
  output SignedExt,
  output RegDst,
  output BEQ,
  output BNE,
  output JR,
  output JUMP,
  output JAL,
  output SLLV,
  output LUI,
  output SB,
  output BGTZ
);

  wire and_2_out, and_3_out, and_4_out, and_5_out, and_6_out, and_7_out, and_8_out, and_9_out, and_10_out,
       and_11_out, and_12_out, and_13_out, and_14_out, and_15_out, and_16_out, and_17_out, and_18_out,
       and_19_out, and_20_out, and_21_out, and_22_out, and_23_out, and_24_out, and_25_out, and_26_out,
       and_27_out, and_28_out, and_29_out, and_30_out, and_31_out, and_33_out, and_34_out, and_35_out,
       and_36_out, and_37_out, and_38_out, and_39_out, and_40_out, and_41_out, and_42_out, and_43_out,
       and_44_out, and_45_out, and_46_out, and_47_out, and_48_out, and_49_out, and_50_out, and_51_out,
       and_52_out, and_53_out, and_54_out, and_55_out, and_59_out, and_60_out, not_1_out, not_2_out,
       not_3_out, not_4_out, not_5_out, not_6_out, not_7_out, not_8_out, not_9_out, not_10_out, not_11_out,
       not_12_out, not_13_out, not_14_out, not_15_out, not_16_out, not_17_out, not_18_out, not_19_out,
       not_20_out, not_21_out, not_22_out, not_23_out, not_24_out, not_25_out, not_26_out, not_27_out,
       not_28_out, not_29_out, not_30_out, not_31_out, not_32_out, not_33_out, not_34_out, not_35_out,
       not_36_out, not_37_out, not_38_out, not_39_out, not_40_out, not_41_out, not_42_out, not_43_out,
       not_44_out, not_45_out, not_46_out, not_47_out, not_48_out, not_49_out, not_50_out, not_51_out,
       not_52_out, not_53_out, not_54_out, not_55_out, not_56_out, not_57_out, not_58_out, not_59_out,
       not_60_out, not_61_out, not_62_out, not_63_out, not_64_out, not_65_out, not_66_out, not_67_out,
       not_68_out, not_69_out, not_70_out, not_71_out, not_72_out, not_73_out, not_74_out, not_75_out,
       not_76_out, not_77_out, not_78_out, not_79_out, not_80_out, not_81_out, not_82_out, not_83_out,
       not_84_out, not_85_out, not_86_out, not_87_out, not_88_out, not_89_out, not_90_out, not_91_out,
       not_92_out, not_93_out, not_94_out, not_95_out, not_96_out, not_97_out, not_98_out, not_99_out,
       not_100_out, not_101_out, not_102_out, not_103_out, not_104_out, not_105_out, not_106_out,
       not_107_out, not_108_out, not_109_out, not_110_out, not_111_out, not_112_out, not_113_out,
       not_114_out, not_115_out, not_116_out, not_117_out, not_118_out, not_119_out, not_120_out,
       not_121_out, not_122_out, not_123_out, not_124_out, not_125_out, not_126_out, not_127_out,
       not_128_out, not_129_out, not_130_out, not_131_out, not_132_out, not_133_out, not_134_out,
       not_135_out, not_136_out, not_137_out, not_138_out, not_139_out, not_140_out, not_141_out,
       not_142_out, not_143_out, not_144_out, not_145_out, not_146_out, not_147_out, not_148_out,
       not_149_out, not_150_out, not_151_out, not_152_out, not_153_out, not_154_out, not_155_out,
       not_156_out, not_157_out, not_158_out, not_159_out, not_160_out, not_161_out, not_162_out,
       not_163_out, not_164_out, not_165_out, not_166_out, not_167_out, not_168_out, not_169_out,
       not_170_out, not_171_out, not_172_out, not_173_out, not_174_out, not_175_out, not_176_out,
       not_177_out, not_178_out, not_179_out, not_180_out, not_181_out, not_182_out, not_183_out,
       not_184_out, not_185_out, not_186_out, not_187_out, not_188_out, not_189_out, not_190_out,
       not_191_out, not_192_out, not_193_out, not_194_out, not_195_out, not_196_out, not_197_out,
       not_198_out, not_199_out, not_200_out, not_201_out, not_202_out, not_203_out, not_204_out,
       not_205_out, not_206_out, not_207_out, not_208_out, not_209_out, not_210_out, not_211_out,
       not_212_out, not_213_out, not_214_out, not_215_out, not_216_out, not_217_out, not_218_out,
       not_219_out, not_220_out, not_221_out, not_222_out, not_223_out, not_224_out, not_225_out,
       not_226_out, not_227_out, not_228_out, not_229_out, not_230_out, not_231_out, not_232_out,
       not_233_out, not_234_out, not_235_out, not_236_out, not_237_out, not_238_out, not_239_out,
       not_240_out, not_241_out, not_242_out, not_243_out, not_244_out, not_245_out, not_246_out,
       not_247_out, not_248_out, not_249_out, not_250_out, not_251_out, not_252_out, not_253_out,
       not_254_out, not_255_out, not_256_out, not_257_out, not_258_out, not_259_out, not_260_out,
       not_261_out, not_262_out, not_263_out, not_264_out, not_265_out, not_266_out, not_267_out,
       not_268_out, not_269_out, not_270_out, not_271_out, not_272_out, not_273_out, not_274_out,
       not_275_out, not_276_out, not_277_out, not_278_out, not_279_out, not_280_out, not_281_out,
       not_282_out, not_283_out, not_284_out, not_285_out, not_286_out, not_287_out, not_288_out,
       not_289_out, not_290_out, not_291_out, not_292_out, not_293_out, not_294_out, not_295_out,
       not_296_out, not_297_out, not_298_out, not_299_out, not_300_out, not_301_out, not_302_out,
       not_303_out, not_304_out, not_305_out, not_306_out, not_307_out, not_308_out, not_309_out,
       not_310_out, not_311_out, not_312_out, not_313_out, not_314_out, not_315_out, not_316_out,
       not_317_out, not_318_out, not_319_out, not_320_out, not_321_out, not_322_out, not_323_out,
       not_324_out, not_325_out, not_326_out, not_327_out, not_328_out, not_329_out, not_330_out,
       not_331_out, not_332_out, not_333_out, not_334_out, not_335_out, not_336_out, not_337_out,
       not_338_out, not_339_out, not_340_out, not_341_out, not_342_out, not_343_out, not_344_out,
       not_345_out, not_346_out, not_347_out, not_348_out, not_349_out, not_350_out, not_351_out,
       not_352_out, not_353_out, not_354_out, not_355_out, not_356_out, not_357_out, not_358_out,
       not_359_out, not_360_out, not_361_out, not_362_out, not_363_out, not_364_out, not_365_out,
       not_366_out, not_367_out, not_368_out, not_369_out, not_370_out, not_371_out, not_372_out,
       not_373_out, not_374_out, not_375_out, not_376_out, not_377_out, not_378_out, not_379_out,
       not_380_out, not_381_out, not_382_out, not_383_out, not_384_out, not_385_out, not_386_out,
       not_387_out, not_388_out, not_389_out, not_390_out, not_391_out, not_392_out, not_393_out,
       not_394_out, not_395_out, not_396_out, not_397_out, not_398_out, not_399_out, not_400_out,
       not_401_out, not_402_out, not_403_out, not_404_out, not_405_out, not_406_out, not_407_out,
       not_408_out, not_409_out, not_410_out, not_411_out, not_412_out, not_413_out, not_414_out,
       not_415_out, not_416_out, not_417_out, not_418_out, not_419_out, not_420_out;

  not not_1 (not_1_out, OP4);
  not not_2 (not_2_out, OP3);
  not not_3 (not_3_out, OP2);
  not not_4 (not_4_out, OP4);
  not not_5 (not_5_out, OP2);
  not not_6 (not_6_out, OP4);
  not not_7 (not_7_out, OP2);
  not not_8 (not_8_out, OP1);
  not not_9 (not_9_out, OP0);
  not not_10 (not_10_out, OP5);
  not not_11 (not_11_out, OP4);
  not not_12 (not_12_out, OP2);
  not not_13 (not_13_out, OP1);
  not not_14 (not_14_out, OP0);
  not not_15 (not_15_out, OP5);
  not not_16 (not_16_out, OP4);
  not not_17 (not_17_out, OP1);
  not not_18 (not_18_out, OP0);
  not not_19 (not_19_out, OP5);
  not not_20 (not_20_out, OP4);
  not not_21 (not_21_out, OP2);
  not not_22 (not_22_out, OP1);
  not not_23 (not_23_out, OP5);
  not not_24 (not_24_out, OP4);
  not not_25 (not_25_out, OP2);
  not not_26 (not_26_out, OP0);
  not not_27 (not_27_out, OP5);
  not not_28 (not_28_out, OP4);
  not not_29 (not_29_out, OP1);
  not not_30 (not_30_out, OP4);
  not not_31 (not_31_out, OP3);
  not not_32 (not_32_out, OP2);
  not not_33 (not_33_out, OP4);
  not not_34 (not_34_out, OP2);
  not not_35 (not_35_out, OP4);
  not not_36 (not_36_out, OP2);
  not not_37 (not_37_out, OP1);
  not not_38 (not_38_out, OP0);
  not not_39 (not_39_out, OP5);
  not not_40 (not_40_out, OP4);
  not not_41 (not_41_out, OP3);
  not not_42 (not_42_out, OP2);
  not not_43 (not_43_out, OP1);
  not not_44 (not_44_out, OP0);
  not not_45 (not_45_out, F5);
  not not_46 (not_46_out, F4);
  not not_47 (not_47_out, F3);
  not not_48 (not_48_out, F2);
  not not_49 (not_49_out, F1);
  not not_50 (not_50_out, F0);
  not not_51 (not_51_out, OP5);
  not not_52 (not_52_out, OP4);
  not not_53 (not_53_out, OP3);
  not not_54 (not_54_out, OP2);
  not not_55 (not_55_out, OP1);
  not not_56 (not_56_out, OP0);
  not not_57 (not_57_out, F5);
  not not_58 (not_58_out, F4);
  not not_59 (not_59_out, F3);
  not not_60 (not_60_out, F2);
  not not_61 (not_61_out, OP5);
  not not_62 (not_62_out, OP4);
  not not_63 (not_63_out, OP3);
  not not_64 (not_64_out, OP2);
  not not_65 (not_65_out, OP1);
  not not_66 (not_66_out, OP0);
  not not_67 (not_67_out, F5);
  not not_68 (not_68_out, F4);
  not not_69 (not_69_out, F3);
  not not_70 (not_70_out, F2);
  not not_71 (not_71_out, F0);
  not not_72 (not_72_out, OP5);
  not not_73 (not_73_out, OP4);
  not not_74 (not_74_out, OP3);
  not not_75 (not_75_out, OP2);
  not not_76 (not_76_out, OP1);
  not not_77 (not_77_out, OP0);
  not not_78 (not_78_out, F4);
  not not_79 (not_79_out, F3);
  not not_80 (not_80_out, F2);
  not not_81 (not_81_out, F1);
  not not_82 (not_82_out, F0);
  not not_83 (not_83_out, OP5);
  not not_84 (not_84_out, OP4);
  not not_85 (not_85_out, OP3);
  not not_86 (not_86_out, OP2);
  not not_87 (not_87_out, OP1);
  not not_88 (not_88_out, OP0);
  not not_89 (not_89_out, F4);
  not not_90 (not_90_out, F3);
  not not_91 (not_91_out, F2);
  not not_92 (not_92_out, F1);
  not not_93 (not_93_out, OP5);
  not not_94 (not_94_out, OP4);
  not not_95 (not_95_out, OP3);
  not not_96 (not_96_out, OP2);
  not not_97 (not_97_out, OP1);
  not not_98 (not_98_out, OP0);
  not not_99 (not_99_out, F4);
  not not_100 (not_100_out, F3);
  not not_101 (not_101_out, F2);
  not not_102 (not_102_out, F0);
  not not_103 (not_103_out, OP5);
  not not_104 (not_104_out, OP4);
  not not_105 (not_105_out, OP3);
  not not_106 (not_106_out, OP2);
  not not_107 (not_107_out, OP1);
  not not_108 (not_108_out, OP0);
  not not_109 (not_109_out, F4);
  not not_110 (not_110_out, F3);
  not not_111 (not_111_out, F1);
  not not_112 (not_112_out, F0);
  not not_113 (not_113_out, OP5);
  not not_114 (not_114_out, OP4);
  not not_115 (not_115_out, OP3);
  not not_116 (not_116_out, OP2);
  not not_117 (not_117_out, OP1);
  not not_118 (not_118_out, OP0);
  not not_119 (not_119_out, F4);
  not not_120 (not_120_out, F3);
  not not_121 (not_121_out, F1);
  not not_122 (not_122_out, OP5);
  not not_123 (not_123_out, OP4);
  not not_124 (not_124_out, OP3);
  not not_125 (not_125_out, OP2);
  not not_126 (not_126_out, OP1);
  not not_127 (not_127_out, OP0);
  not not_128 (not_128_out, F4);
  not not_129 (not_129_out, F3);
  not not_130 (not_130_out, OP5);
  not not_131 (not_131_out, OP4);
  not not_132 (not_132_out, OP3);
  not not_133 (not_133_out, OP2);
  not not_134 (not_134_out, OP1);
  not not_135 (not_135_out, OP0);
  not not_136 (not_136_out, F4);
  not not_137 (not_137_out, F2);
  not not_138 (not_138_out, F0);
  not not_139 (not_139_out, OP5);
  not not_140 (not_140_out, OP4);
  not not_141 (not_141_out, OP3);
  not not_142 (not_142_out, OP2);
  not not_143 (not_143_out, OP1);
  not not_144 (not_144_out, OP0);
  not not_145 (not_145_out, F4);
  not not_146 (not_146_out, F2);
  not not_147 (not_147_out, OP5);
  not not_148 (not_148_out, OP4);
  not not_149 (not_149_out, OP3);
  not not_150 (not_150_out, OP2);
  not not_151 (not_151_out, OP5);
  not not_152 (not_152_out, OP4);
  not not_153 (not_153_out, OP2);
  not not_154 (not_154_out, OP1);
  not not_155 (not_155_out, OP0);
  not not_156 (not_156_out, OP5);
  not not_157 (not_157_out, OP4);
  not not_158 (not_158_out, OP1);
  not not_159 (not_159_out, OP0);
  not not_160 (not_160_out, OP5);
  not not_161 (not_161_out, OP4);
  not not_162 (not_162_out, OP2);
  not not_163 (not_163_out, OP1);
  not not_164 (not_164_out, OP5);
  not not_165 (not_165_out, OP4);
  not not_166 (not_166_out, OP2);
  not not_167 (not_167_out, OP0);
  not not_168 (not_168_out, OP5);
  not not_169 (not_169_out, OP4);
  not not_170 (not_170_out, OP1);
  not not_171 (not_171_out, OP4);
  not not_172 (not_172_out, OP3);
  not not_173 (not_173_out, OP2);
  not not_174 (not_174_out, OP5);
  not not_175 (not_175_out, OP4);
  not not_176 (not_176_out, OP3);
  not not_177 (not_177_out, OP2);
  not not_178 (not_178_out, OP1);
  not not_179 (not_179_out, OP0);
  not not_180 (not_180_out, F5);
  not not_181 (not_181_out, F4);
  not not_182 (not_182_out, F3);
  not not_183 (not_183_out, F1);
  not not_184 (not_184_out, F0);
  not not_185 (not_185_out, OP5);
  not not_186 (not_186_out, OP4);
  not not_187 (not_187_out, OP5);
  not not_188 (not_188_out, OP4);
  not not_189 (not_189_out, OP3);
  not not_190 (not_190_out, OP2);
  not not_191 (not_191_out, OP1);
  not not_192 (not_192_out, OP0);
  not not_193 (not_193_out, F5);
  not not_194 (not_194_out, F4);
  not not_195 (not_195_out, F1);
  not not_196 (not_196_out, F0);
  not not_197 (not_197_out, OP5);
  not not_198 (not_198_out, OP4);
  not not_199 (not_199_out, OP3);
  not not_200 (not_200_out, OP1);
  not not_201 (not_201_out, OP0);
  not not_202 (not_202_out, OP5);
  not not_203 (not_203_out, OP4);
  not not_204 (not_204_out, OP3);
  not not_205 (not_205_out, OP1);
  not not_206 (not_206_out, OP5);
  not not_207 (not_207_out, OP4);
  not not_208 (not_208_out, OP2);
  not not_209 (not_209_out, OP1);
  not not_210 (not_210_out, OP0);
  not not_211 (not_211_out, OP5);
  not not_212 (not_212_out, OP4);
  not not_213 (not_213_out, OP2);
  not not_214 (not_214_out, OP1);
  not not_215 (not_215_out, OP5);
  not not_216 (not_216_out, OP4);
  not not_217 (not_217_out, OP2);
  not not_218 (not_218_out, OP0);
  not not_219 (not_219_out, OP4);
  not not_220 (not_220_out, OP3);
  not not_221 (not_221_out, OP2);
  not not_222 (not_222_out, OP4);
  not not_223 (not_223_out, OP2);
  not not_224 (not_224_out, OP5);
  not not_225 (not_225_out, OP4);
  not not_226 (not_226_out, OP4);
  not not_227 (not_227_out, OP2);
  not not_228 (not_228_out, OP1);
  not not_229 (not_229_out, OP0);
  not not_230 (not_230_out, OP5);
  not not_231 (not_231_out, OP4);
  not not_232 (not_232_out, OP3);
  not not_233 (not_233_out, OP5);
  not not_234 (not_234_out, OP4);
  not not_235 (not_235_out, OP3);
  not not_236 (not_236_out, OP2);
  not not_237 (not_237_out, OP1);
  not not_238 (not_238_out, OP0);
  not not_239 (not_239_out, F5);
  not not_240 (not_240_out, F4);
  not not_241 (not_241_out, F3);
  not not_242 (not_242_out, F2);
  not not_243 (not_243_out, F1);
  not not_244 (not_244_out, F0);
  not not_245 (not_245_out, OP5);
  not not_246 (not_246_out, OP4);
  not not_247 (not_247_out, OP3);
  not not_248 (not_248_out, OP2);
  not not_249 (not_249_out, OP1);
  not not_250 (not_250_out, OP0);
  not not_251 (not_251_out, F5);
  not not_252 (not_252_out, F4);
  not not_253 (not_253_out, F3);
  not not_254 (not_254_out, F2);
  not not_255 (not_255_out, OP5);
  not not_256 (not_256_out, OP4);
  not not_257 (not_257_out, OP3);
  not not_258 (not_258_out, OP2);
  not not_259 (not_259_out, OP1);
  not not_260 (not_260_out, OP0);
  not not_261 (not_261_out, F5);
  not not_262 (not_262_out, F4);
  not not_263 (not_263_out, F3);
  not not_264 (not_264_out, F2);
  not not_265 (not_265_out, F0);
  not not_266 (not_266_out, OP5);
  not not_267 (not_267_out, OP4);
  not not_268 (not_268_out, OP3);
  not not_269 (not_269_out, OP2);
  not not_270 (not_270_out, OP1);
  not not_271 (not_271_out, OP0);
  not not_272 (not_272_out, F4);
  not not_273 (not_273_out, F3);
  not not_274 (not_274_out, F2);
  not not_275 (not_275_out, F1);
  not not_276 (not_276_out, F0);
  not not_277 (not_277_out, OP5);
  not not_278 (not_278_out, OP4);
  not not_279 (not_279_out, OP3);
  not not_280 (not_280_out, OP2);
  not not_281 (not_281_out, OP1);
  not not_282 (not_282_out, OP0);
  not not_283 (not_283_out, F4);
  not not_284 (not_284_out, F3);
  not not_285 (not_285_out, F2);
  not not_286 (not_286_out, F1);
  not not_287 (not_287_out, OP5);
  not not_288 (not_288_out, OP4);
  not not_289 (not_289_out, OP3);
  not not_290 (not_290_out, OP2);
  not not_291 (not_291_out, OP1);
  not not_292 (not_292_out, OP0);
  not not_293 (not_293_out, F4);
  not not_294 (not_294_out, F3);
  not not_295 (not_295_out, F2);
  not not_296 (not_296_out, F0);
  not not_297 (not_297_out, OP5);
  not not_298 (not_298_out, OP4);
  not not_299 (not_299_out, OP3);
  not not_300 (not_300_out, OP2);
  not not_301 (not_301_out, OP1);
  not not_302 (not_302_out, OP0);
  not not_303 (not_303_out, F4);
  not not_304 (not_304_out, F3);
  not not_305 (not_305_out, F1);
  not not_306 (not_306_out, F0);
  not not_307 (not_307_out, OP5);
  not not_308 (not_308_out, OP4);
  not not_309 (not_309_out, OP3);
  not not_310 (not_310_out, OP2);
  not not_311 (not_311_out, OP1);
  not not_312 (not_312_out, OP0);
  not not_313 (not_313_out, F4);
  not not_314 (not_314_out, F3);
  not not_315 (not_315_out, F1);
  not not_316 (not_316_out, OP5);
  not not_317 (not_317_out, OP4);
  not not_318 (not_318_out, OP3);
  not not_319 (not_319_out, OP2);
  not not_320 (not_320_out, OP1);
  not not_321 (not_321_out, OP0);
  not not_322 (not_322_out, F4);
  not not_323 (not_323_out, F3);
  not not_324 (not_324_out, OP5);
  not not_325 (not_325_out, OP4);
  not not_326 (not_326_out, OP3);
  not not_327 (not_327_out, OP2);
  not not_328 (not_328_out, OP1);
  not not_329 (not_329_out, OP0);
  not not_330 (not_330_out, F4);
  not not_331 (not_331_out, F2);
  not not_332 (not_332_out, F0);
  not not_333 (not_333_out, OP5);
  not not_334 (not_334_out, OP4);
  not not_335 (not_335_out, OP3);
  not not_336 (not_336_out, OP2);
  not not_337 (not_337_out, OP1);
  not not_338 (not_338_out, OP0);
  not not_339 (not_339_out, F4);
  not not_340 (not_340_out, F2);
  not not_341 (not_341_out, OP5);
  not not_342 (not_342_out, OP4);
  not not_343 (not_343_out, OP3);
  not not_344 (not_344_out, OP2);
  not not_345 (not_345_out, OP1);
  not not_346 (not_346_out, OP0);
  not not_347 (not_347_out, F5);
  not not_348 (not_348_out, F4);
  not not_349 (not_349_out, F2);
  not not_350 (not_350_out, F1);
  not not_351 (not_351_out, F0);
  not not_352 (not_352_out, OP5);
  not not_353 (not_353_out, OP4);
  not not_354 (not_354_out, OP3);
  not not_355 (not_355_out, OP2);
  not not_356 (not_356_out, OP1);
  not not_357 (not_357_out, OP0);
  not not_358 (not_358_out, F5);
  not not_359 (not_359_out, F4);
  not not_360 (not_360_out, F3);
  not not_361 (not_361_out, F1);
  not not_362 (not_362_out, F0);
  not not_363 (not_363_out, OP5);
  not not_364 (not_364_out, OP4);
  not not_365 (not_365_out, OP3);
  not not_366 (not_366_out, OP1);
  not not_367 (not_367_out, OP0);
  not not_368 (not_368_out, OP5);
  not not_369 (not_369_out, OP4);
  not not_370 (not_370_out, OP3);
  not not_371 (not_371_out, OP1);
  not not_372 (not_372_out, OP0);
  not not_373 (not_373_out, OP1);
  not not_374 (not_374_out, OP2);
  not not_375 (not_375_out, OP3);
  not not_376 (not_376_out, OP4);
  not not_377 (not_377_out, OP5);
  not not_378 (not_378_out, F0);
  not not_379 (not_379_out, F1);
  not not_380 (not_380_out, F2);
  not not_381 (not_381_out, F4);
  not not_382 (not_382_out, F5);
  not not_383 (not_383_out, OP0);
  not not_384 (not_384_out, OP2);
  not not_385 (not_385_out, OP3);
  not not_386 (not_386_out, OP4);
  not not_387 (not_387_out, OP5);
  not not_388 (not_388_out, F0);
  not not_389 (not_389_out, F1);
  not not_390 (not_390_out, F2);
  not not_391 (not_391_out, F4);
  not not_392 (not_392_out, F5);
  not not_393 (not_393_out, OP2);
  not not_394 (not_394_out, OP3);
  not not_395 (not_395_out, OP4);
  not not_396 (not_396_out, OP5);
  not not_397 (not_397_out, OP2);
  not not_398 (not_398_out, OP3);
  not not_399 (not_399_out, OP4);
  not not_400 (not_400_out, OP5);
  not not_401 (not_401_out, OP5);
  not not_402 (not_402_out, OP4);
  not not_403 (not_403_out, OP3);
  not not_404 (not_404_out, OP2);
  not not_405 (not_405_out, OP1);
  not not_406 (not_406_out, OP0);
  not not_407 (not_407_out, F5);
  not not_408 (not_408_out, F4);
  not not_409 (not_409_out, F3);
  not not_410 (not_410_out, F1);
  not not_411 (not_411_out, F0);
  not not_412 (not_412_out, OP5);
  not not_413 (not_413_out, OP4);
  not not_414 (not_414_out, OP4);
  not not_415 (not_415_out, OP2);
  not not_416 (not_416_out, OP1);
  not not_417 (not_417_out, OP0);
  not not_418 (not_418_out, OP5);
  not not_419 (not_419_out, OP4);
  not not_420 (not_420_out, OP3);
  and and_1 (MemToReg, OP5, not_1_out, not_2_out, not_3_out, OP1, OP0);
  and and_2 (and_2_out, OP5, not_4_out, OP3, not_5_out, OP1, OP0);
  and and_3 (and_3_out, OP5, not_6_out, OP3, not_7_out, not_8_out, not_9_out);
  and and_4 (and_4_out, not_10_out, not_11_out, OP3, not_12_out, not_13_out, not_14_out);
  and and_5 (and_5_out, not_15_out, not_16_out, OP3, OP2, not_17_out, not_18_out);
  and and_6 (and_6_out, not_19_out, not_20_out, OP3, not_21_out, not_22_out, OP0);
  and and_7 (and_7_out, not_23_out, not_24_out, OP3, not_25_out, OP1, not_26_out);
  and and_8 (and_8_out, not_27_out, not_28_out, OP3, OP2, not_29_out, OP0);
  and and_9 (and_9_out, OP5, not_30_out, not_31_out, not_32_out, OP1, OP0);
  and and_10 (and_10_out, OP5, not_33_out, OP3, not_34_out, OP1, OP0);
  and and_11 (and_11_out, OP5, not_35_out, OP3, not_36_out, not_37_out, not_38_out);
  and and_12 (and_12_out, not_39_out, not_40_out, not_41_out, not_42_out, not_43_out, not_44_out, not_45_out, not_46_out, not_47_out, not_48_out, not_49_out, not_50_out);
  and and_13 (and_13_out, not_51_out, not_52_out, not_53_out, not_54_out, not_55_out, not_56_out, not_57_out, not_58_out, not_59_out, not_60_out, F1, F0);
  and and_14 (and_14_out, not_61_out, not_62_out, not_63_out, not_64_out, not_65_out, not_66_out, not_67_out, not_68_out, not_69_out, not_70_out, F1, not_71_out);
  and and_15 (and_15_out, not_72_out, not_73_out, not_74_out, not_75_out, not_76_out, not_77_out, F5, not_78_out, not_79_out, not_80_out, not_81_out, not_82_out);
  and and_16 (and_16_out, not_83_out, not_84_out, not_85_out, not_86_out, not_87_out, not_88_out, F5, not_89_out, not_90_out, not_91_out, not_92_out, F0);
  and and_17 (and_17_out, not_93_out, not_94_out, not_95_out, not_96_out, not_97_out, not_98_out, F5, not_99_out, not_100_out, not_101_out, F1, not_102_out);
  and and_18 (and_18_out, not_103_out, not_104_out, not_105_out, not_106_out, not_107_out, not_108_out, F5, not_109_out, not_110_out, F2, not_111_out, not_112_out);
  and and_19 (and_19_out, not_113_out, not_114_out, not_115_out, not_116_out, not_117_out, not_118_out, F5, not_119_out, not_120_out, F2, not_121_out, F0);
  and and_20 (and_20_out, not_122_out, not_123_out, not_124_out, not_125_out, not_126_out, not_127_out, F5, not_128_out, not_129_out, F2, F1, F0);
  and and_21 (and_21_out, not_130_out, not_131_out, not_132_out, not_133_out, not_134_out, not_135_out, F5, not_136_out, F3, not_137_out, F1, not_138_out);
  and and_22 (and_22_out, not_139_out, not_140_out, not_141_out, not_142_out, not_143_out, not_144_out, F5, not_145_out, F3, not_146_out, F1, F0);
  and and_23 (and_23_out, not_147_out, not_148_out, not_149_out, not_150_out, OP1, OP0);
  and and_24 (and_24_out, not_151_out, not_152_out, OP3, not_153_out, not_154_out, not_155_out);
  and and_25 (and_25_out, not_156_out, not_157_out, OP3, OP2, not_158_out, not_159_out);
  and and_26 (and_26_out, not_160_out, not_161_out, OP3, not_162_out, not_163_out, OP0);
  and and_27 (and_27_out, not_164_out, not_165_out, OP3, not_166_out, OP1, not_167_out);
  and and_28 (and_28_out, not_168_out, not_169_out, OP3, OP2, not_170_out, OP0);
  and and_29 (and_29_out, OP5, not_171_out, not_172_out, not_173_out, OP1, OP0);
  and and_30 (and_30_out, not_174_out, not_175_out, not_176_out, not_177_out, not_178_out, not_179_out, not_180_out, not_181_out, not_182_out, F2, not_183_out, not_184_out);
  and and_31 (and_31_out, not_185_out, not_186_out, OP3, OP2, OP1, OP0);
  and and_32 (SysCALL, not_187_out, not_188_out, not_189_out, not_190_out, not_191_out, not_192_out, not_193_out, not_194_out, F3, F2, not_195_out, not_196_out);
  and and_33 (and_33_out, not_197_out, not_198_out, not_199_out, OP2, not_200_out, not_201_out);
  and and_34 (and_34_out, not_202_out, not_203_out, not_204_out, OP2, not_205_out, OP0);
  and and_35 (and_35_out, not_206_out, not_207_out, OP3, not_208_out, not_209_out, not_210_out);
  and and_36 (and_36_out, not_211_out, not_212_out, OP3, not_213_out, not_214_out, OP0);
  and and_37 (and_37_out, not_215_out, not_216_out, OP3, not_217_out, OP1, not_218_out);
  and and_38 (and_38_out, OP5, not_219_out, not_220_out, not_221_out, OP1, OP0);
  and and_39 (and_39_out, OP5, not_222_out, OP3, not_223_out, OP1, OP0);
  and and_40 (and_40_out, not_224_out, not_225_out, OP3, OP2, OP1, OP0);
  and and_41 (and_41_out, OP5, not_226_out, OP3, not_227_out, not_228_out, not_229_out);
  and and_42 (and_42_out, not_230_out, not_231_out, not_232_out, OP2, OP1, OP0);
  and and_43 (and_43_out, not_233_out, not_234_out, not_235_out, not_236_out, not_237_out, not_238_out, not_239_out, not_240_out, not_241_out, not_242_out, not_243_out, not_244_out);
  and and_44 (and_44_out, not_245_out, not_246_out, not_247_out, not_248_out, not_249_out, not_250_out, not_251_out, not_252_out, not_253_out, not_254_out, F1, F0);
  and and_45 (and_45_out, not_255_out, not_256_out, not_257_out, not_258_out, not_259_out, not_260_out, not_261_out, not_262_out, not_263_out, not_264_out, F1, not_265_out);
  and and_46 (and_46_out, not_266_out, not_267_out, not_268_out, not_269_out, not_270_out, not_271_out, F5, not_272_out, not_273_out, not_274_out, not_275_out, not_276_out);
  and and_47 (and_47_out, not_277_out, not_278_out, not_279_out, not_280_out, not_281_out, not_282_out, F5, not_283_out, not_284_out, not_285_out, not_286_out, F0);
  and and_48 (and_48_out, not_287_out, not_288_out, not_289_out, not_290_out, not_291_out, not_292_out, F5, not_293_out, not_294_out, not_295_out, F1, not_296_out);
  and and_49 (and_49_out, not_297_out, not_298_out, not_299_out, not_300_out, not_301_out, not_302_out, F5, not_303_out, not_304_out, F2, not_305_out, not_306_out);
  and and_50 (and_50_out, not_307_out, not_308_out, not_309_out, not_310_out, not_311_out, not_312_out, F5, not_313_out, not_314_out, F2, not_315_out, F0);
  and and_51 (and_51_out, not_316_out, not_317_out, not_318_out, not_319_out, not_320_out, not_321_out, F5, not_322_out, not_323_out, F2, F1, F0);
  and and_52 (and_52_out, not_324_out, not_325_out, not_326_out, not_327_out, not_328_out, not_329_out, F5, not_330_out, F3, not_331_out, F1, not_332_out);
  and and_53 (and_53_out, not_333_out, not_334_out, not_335_out, not_336_out, not_337_out, not_338_out, F5, not_339_out, F3, not_340_out, F1, F0);
  and and_54 (and_54_out, not_341_out, not_342_out, not_343_out, not_344_out, not_345_out, not_346_out, not_347_out, not_348_out, F3, not_349_out, not_350_out, not_351_out);
  and and_55 (and_55_out, not_352_out, not_353_out, not_354_out, not_355_out, not_356_out, not_357_out, not_358_out, not_359_out, not_360_out, F2, not_361_out, not_362_out);
  and and_56 (BEQ, not_363_out, not_364_out, not_365_out, OP2, not_366_out, not_367_out);
  and and_57 (BNE, not_368_out, not_369_out, not_370_out, OP2, not_371_out, OP0);
  and and_58 (JR, not_372_out, not_373_out, not_374_out, not_375_out, not_376_out, not_377_out, not_378_out, not_379_out, not_380_out, F3, not_381_out, not_382_out);
  and and_59 (and_59_out, not_383_out, not_384_out, not_385_out, not_386_out, not_387_out, not_388_out, not_389_out, not_390_out, F3, not_391_out, not_392_out);
  and and_60 (and_60_out, OP1, not_393_out, not_394_out, not_395_out, not_396_out);
  and and_61 (JAL, OP0, OP1, not_397_out, not_398_out, not_399_out, not_400_out);
  and and_62 (SLLV, not_401_out, not_402_out, not_403_out, not_404_out, not_405_out, not_406_out, not_407_out, not_408_out, not_409_out, F2, not_410_out, not_411_out);
  and and_63 (LUI, not_412_out, not_413_out, OP3, OP2, OP1, OP0);
  and and_64 (SB, OP5, not_414_out, OP3, not_415_out, not_416_out, not_417_out);
  and and_65 (BGTZ, not_418_out, not_419_out, not_420_out, OP2, OP1, OP0);
  or or_1 (MemWrite, and_2_out, and_3_out);
  or or_2 (ALU_SRC, and_4_out, and_5_out, and_6_out, and_7_out, and_8_out, and_9_out, and_10_out, and_11_out);
  or or_3 (SignedExt, and_33_out, and_34_out, and_35_out, and_36_out, and_37_out, and_38_out, and_39_out, and_40_out, and_41_out, and_42_out);
  or or_4 (JUMP, and_59_out, and_60_out);
  or or_5 (RegWrite, and_12_out, and_13_out, and_14_out, and_15_out, and_16_out, and_17_out, and_18_out, and_19_out, and_20_out, and_21_out, and_22_out, and_23_out, and_24_out, and_25_out, and_26_out, and_27_out, and_28_out, and_29_out, and_30_out, and_31_out);
  or or_6 (RegDst, and_43_out, and_44_out, and_45_out, and_46_out, and_47_out, and_48_out, and_49_out, and_50_out, and_51_out, and_52_out, and_53_out, and_54_out, and_55_out);
endmodule

// ALU
module MIPS_ALU (
  input  [4:0] shamt,
  input  [31:0] X,
  input  [31:0] Y,
  input  [3:0] AluOP,
  output Equal,
  output [31:0] Result,
  output [31:0] Result_2
);

  wire [0:0] comparator_1_lt, comparator_2_lt;
  wire [31:0] adder_1_out, AND_out, divider_1_out, divider_1_rem, multiplier_1_cout, multiplier_1_out,
       NOR_out, OR_out, shifter_1_out, shifter_2_out, shifter_3_out, subtractor_1_out, XOR_out;

  assign AND_out = X & Y;  // AND_Gate AND, 32 bits wide
  assign OR_out = X | Y;  // OR_Gate OR, 32 bits wide
  Shifter #(.width(32), .shift("ll")) shifter_1 (.in(Y), .\dist (shamt), .out(shifter_1_out));
  Shifter #(.width(32), .shift("ar")) shifter_2 (.in(Y), .\dist (shamt), .out(shifter_2_out));
  Shifter #(.width(32), .shift("lr")) shifter_3 (.in(Y), .\dist (shamt), .out(shifter_3_out));
  Multiplier #(.width(32)) multiplier_1 (.a(X), .b(Y), .out(multiplier_1_out), .cout(multiplier_1_cout));  // open: cin
  Divider #(.width(32)) divider_1 (.a(X), .b(Y), .out(divider_1_out), .rem(divider_1_rem));  // open: upper
  Adder #(.width(32)) adder_1 (.a(X), .b(Y), .out(adder_1_out));  // open: cin, cout
  Subtractor #(.width(32)) subtractor_1 (.a(X), .b(Y), .out(subtractor_1_out));  // open: bin, bout
  assign XOR_out = X ^ Y;  // XOR_Gate XOR, 32 bits wide
  assign NOR_out = ~(X | Y);  // NOR_Gate NOR, 32 bits wide
  Comparator #(.width(32), .mode("twosComplement")) comparator_1 (
    .a(X), .b(Y), .eq(Equal), .lt(comparator_1_lt[0]));  // open: gt
  Comparator #(.width(32), .mode("unsigned")) comparator_2 (.a(X), .b(Y), .lt(comparator_2_lt[0]));  // open: gt, eq
  Multiplexer #(.select(4), .width(32), .disabled("Z"), .enable("false")) multiplexer_1 (
    .in0(shifter_1_out), .in1(shifter_2_out), .in2(shifter_3_out), .in3(multiplier_1_out),
    .in4(divider_1_out), .in5(adder_1_out), .in6(subtractor_1_out), .in7(AND_out), .in8(OR_out),
    .in9(XOR_out), .in10(NOR_out), .in11({{31{1'b0}}, comparator_1_lt[0]}),
    .in12({{31{1'b0}}, comparator_2_lt[0]}), .in13({32{1'b0}}), .in14({32{1'b0}}), .in15({32{1'b0}}),
    .out(Result), .sel(AluOP));
  Multiplexer #(.select(4), .width(32), .disabled("Z"), .enable("false")) multiplexer_2 (
    .in0({32{1'b0}}), .in1({32{1'b0}}), .in2({32{1'b0}}), .in3(multiplier_1_cout), .in4(divider_1_rem),
    .in5({32{1'b0}}), .in6({32{1'b0}}), .in7({32{1'b0}}), .in8({32{1'b0}}), .in9({32{1'b0}}),
    .in10({32{1'b0}}), .in11({32{1'b0}}), .in12({32{1'b0}}), .in13({32{1'b0}}), .in14({32{1'b0}}),
    .in15({32{1'b0}}), .out(Result_2), .sel(AluOP));

  // Other names for the same wires on the sheet: Result2[31:0] = Result_2; S[3:0] = AluOP

  // Notes on the sheet:
  //   不要改变此引脚区域内容，也不要改变ALU封装形式
  //   输入引脚
  //   输出引脚
endmodule

module MIPS_Regifile (
  input  [31:0] Din,
  input  Clk,
  input  WE,
  input  [4:0] R1_num,
  input  [4:0] W_num,
  input  [4:0] R2_num,
  output [31:0] R1,
  output [31:0] R2
);

  // RegisterFile registerfile_1: pin names not known; wires that end beside it: Din, Clk, WE, W_num, R1_num, R2_num, R1, R2
endmodule

module \理想流水线  (
  output RegWrite,
  output MemWrite,
  output [31:0] IF_PC,
  output [31:0] ID_PC,
  output [31:0] EX_PC,
  output [31:0] M_PC,
  output [31:0] WB_PC,
  output [31:0] RDin,
  output [31:0] MDin,
  output [31:0] LedData
);

  wire and_1_out, and_2_out, CLK, clock_2_out, comparator_1_eq, comparator_1_lt, comparator_2_eq, d_ff_1_q,
       En, ex_mem_1_memtoreg_out, ex_mem_1_reddst_out, ex_mem_1_regwrite_out, ex_mem_1_syscall_out, Go,
       id_ex_1_alusrcb_out, id_ex_1_memtoreg_out, id_ex_1_memwrite_out, id_ex_1_reddst_out,
       id_ex_1_regwrite_out, id_ex_1_syscall_out, IR1, IR2, IR3, mem_wb_1_memtoreg_out, mem_wb_1_reddst_out,
       mem_wb_1_syscall_out, nand_1_out, pull_resistor_1_node, register_2_q, RST, SignedExt, W1, W2, W3,
       \单周期硬布线控制器_1_alu_src , \单周期硬布线控制器_1_memtoreg , \单周期硬布线控制器_1_memwrite , \单周期硬布线控制器_1_regdst ,
       \单周期硬布线控制器_1_regwrite , \单周期硬布线控制器_1_syscall ;
  wire [3:0] id_ex_1_aluop_out, \单周期硬布线控制器_1_alu_op ;
  wire [4:0] id_ex_1_shamt_out, multiplexer_1_out, multiplexer_2_out, multiplexer_6_out;
  wire [12:0] CNT_num;
  wire [15:0] \LoadUse次数 , \总周期数 , \插入气泡数 , \无条件分支数 , \条件分支成功数 ;
  wire [31:0] adder_1_out, bit_extender_1_out, bit_extender_2_out, EX_IR, ex_mem_1_a_out,
       ex_mem_1_aluresult_out, id_ex_1_a_out, id_ex_1_b_out, id_ex_1_imm_out, ID_IR, IF_IR, MEM_IR,
       mem_wb_1_a_out, mem_wb_1_aluresult_out, mem_wb_1_b_out, mem_wb_1_memdata_out, mips_alu_1_result,
       mips_regifile_1_r1, mips_regifile_1_r2, multiplexer_3_out, multiplexer_4_out, ram_1_data, WB_IR;

  Button \u_总复位  (.out(RST));
  Button _1 (.out(IR1));
  Button _2 (.out(IR2));
  Button _3 (.out(IR3));
  // Probe on \总周期数 
  // Probe on \总周期数 
  Button \u_继续运行  (.out(Go));
  LED #(.active("true")) led_1 (.in(W1));
  LED #(.active("true")) led_2 (.in(W2));
  LED #(.active("true")) led_3 (.in(W3));
  Hex_Digit_Display hex_digit_display_1 (.value(LedData[31:28]));  // open: dp
  // Probe on IF_PC[19:0]
  // Mips_Probe mips_probe_1: pin names not known; wires that end beside it: IF_IR
  Hex_Digit_Display hex_digit_display_2 (.value(LedData[27:24]));  // open: dp
  Hex_Digit_Display hex_digit_display_3 (.value(LedData[23:20]));  // open: dp
  // Probe on ID_PC[19:0]
  // Mips_Probe mips_probe_2: pin names not known; wires that end beside it: ID_IR
  Hex_Digit_Display hex_digit_display_4 (.value(LedData[15:12]));  // open: dp
  Hex_Digit_Display hex_digit_display_5 (.value(LedData[19:16]));  // open: dp
  Register #(.width(32), .trigger("rising"), .Select("low")) PC (
    .D(adder_1_out), .en(En), .Q(IF_PC), .clk(CLK));  // open: clr
  Hex_Digit_Display hex_digit_display_6 (.value(LedData[11:8]));  // open: dp
  Hex_Digit_Display hex_digit_display_7 (.value(LedData[7:4]));  // open: dp
  Clock #(.highDuration(1), .lowDuration(1)) clock_1 (.out(CLK));
  // Probe on EX_PC[19:0]
  // Mips_Probe mips_probe_3: pin names not known; wires that end beside it: EX_IR
  Adder #(.width(32)) adder_1 (.a(32'h4), .b(IF_PC), .out(adder_1_out));  // open: cin, cout
  Hex_Digit_Display hex_digit_display_8 (.value(LedData[3:0]));  // open: dp
  // Probe on \总周期数 
  // Probe on M_PC[19:0]
  // Mips_Probe mips_probe_4: pin names not known; wires that end beside it: MEM_IR
  ROM #(.addrWidth(10), .dataWidth(32), .Select("low")) rom_1 (.addr(IF_PC[11:2]), .data(IF_IR));
  // Probe on \总周期数 
  // Probe on \无条件分支数 
  // Probe on \条件分支成功数 
  // Probe on \插入气泡数 
  // Probe on \LoadUse次数 
  // Probe on IF_PC[11:0]
  // Probe on WB_PC[19:0]
  // Mips_Probe mips_probe_5: pin names not known; wires that end beside it: WB_IR
  IF_ID if_id_1 (
    .IR_in(IF_IR), .PC_in(IF_PC), .IR_out(ID_IR), .PC_out(ID_PC), .CLR(RST), .CLK(CLK));  // open: RedDst_in, AluSrcB_in, Shamt_in, Syscall_in, RegWrite_in, JMP_in, AluOp_in, JAL_in, JR_in, MemWrite_in, PredictJMP_in, SLLV_in, Beq_in, LUI_in, Bne_in, A_in, SB_in, MemToReg_in, BGTZ_in, B_in, Imm_in, RedDst_out, AluSrcB_out, Syscall_out, Shamt_out, RegWrite_out, JMP_out, AluOp_out, JAL_out, JR_out, MemWrite_out, PredictJMP_out, SLLV_out, Beq_out, A_out, LUI_out, Bne_out, SB_out, MemToReg_out, B_out, BGTZ_out, Imm_out, Stall
  // Probe on EX_PC[11:0]
  // Probe on ID_PC[11:0]
  // Probe on M_PC[11:0]
  D_Flip_Flop #(.trigger("high"), .Pre_Clr_Positions("LEGACY"), .NegatePresetClear("false"), .enable("true"), .NewFFLayout("false")) d_ff_1 (.Q(d_ff_1_q));  // open: clk, D, Qn, preset, en, reset
  // Probe on 13'hc
  Multiplexer #(.select(1), .width(5), .disabled("Z"), .enable("false")) multiplexer_1 (
    .in0(ID_IR[25:21]), .in1(5'b00100), .out(multiplexer_1_out), .sel(\单周期硬布线控制器_1_syscall ));
  // Probe on WB_PC[11:0]
  Comparator #(.width(13), .mode("twosComplement")) comparator_1 (
    .a(CNT_num), .b(13'hc), .eq(comparator_1_eq), .lt(comparator_1_lt));  // open: gt
  Clock #(.highDuration(1), .lowDuration(1)) clock_2 (.out(clock_2_out));
  \单周期硬布线控制器  \u_单周期硬布线控制器_1  (
    .Func(ID_IR[5:0]), .OP(ID_IR[31:26]), .ALU_OP(\单周期硬布线控制器_1_alu_op ), .MemToReg(\单周期硬布线控制器_1_memtoreg ),
    .MemWrite(\单周期硬布线控制器_1_memwrite ), .ALU_SRC(\单周期硬布线控制器_1_alu_src ), .RegWrite(\单周期硬布线控制器_1_regwrite ),
    .SysCALL(\单周期硬布线控制器_1_syscall ), .SignedExt(SignedExt), .RegDst(\单周期硬布线控制器_1_regdst ));  // open: JR, JMP, Beq, JAL, Bne, SLLV, LUI, SB, BGTZ, in_3, MFC0, MTC0
  Multiplexer #(.select(1), .width(5), .disabled("Z"), .enable("false")) multiplexer_2 (
    .in0(ID_IR[20:16]), .in1(5'b00010), .out(multiplexer_2_out), .sel(\单周期硬布线控制器_1_syscall ));
  assign bit_extender_1_out = {{16{1'b0}}, ID_IR[15:0]};  // Bit_Extender bit_extender_1
  assign bit_extender_2_out = {{16{ID_IR[15]}}, ID_IR[15:0]};  // Bit_Extender bit_extender_2
  nand nand_1 (nand_1_out, d_ff_1_q, comparator_1_eq);
  Counter #(.width(13), .max('h1fff), .ongoal("stay"), .trigger("rising"), .behavior("old")) counter_1 (
    .count(comparator_1_lt), .Q(CNT_num), .clk(clock_2_out));  // open: load, D, carry, clr, preset
  Multiplexer #(.select(1), .width(32), .disabled("Z"), .enable("false")) multiplexer_3 (
    .in0(bit_extender_1_out), .in1(bit_extender_2_out), .out(multiplexer_3_out), .sel(SignedExt));
  Controlled_Buffer #(.width(1), .negatecontrol("false")) controlled_buffer_1 (
    .in(clock_2_out), .en(nand_1_out));  // open: out
  Pull_Resistor #(.pull(1)) pull_resistor_1 (.node(pull_resistor_1_node));
  MIPS_Regifile mips_regifile_1 (
    .Din(RDin), .Clk(CLK), .R1(mips_regifile_1_r1), .R2(mips_regifile_1_r2), .WE(RegWrite),
    .W_num(multiplexer_6_out), .R1_num(multiplexer_1_out), .R2_num(multiplexer_2_out));
  Counter #(.width(16), .max('hffff), .ongoal("wrap"), .trigger("rising"), .behavior("new")) counter_2 (
    .Q(\总周期数 ), .clk(CLK), .down(En));  // open: load, D, count, carry, clr, preset
  ID_EX id_ex_1 (
    .RedDst_in(\单周期硬布线控制器_1_regdst ), .AluSrcB_in(\单周期硬布线控制器_1_alu_src ), .Shamt_in(ID_IR[10:6]),
    .Syscall_in(\单周期硬布线控制器_1_syscall ), .RegWrite_in(\单周期硬布线控制器_1_regwrite ),
    .AluOp_in(\单周期硬布线控制器_1_alu_op ), .MemWrite_in(\单周期硬布线控制器_1_memwrite ), .IR_in(ID_IR), .PC_in(ID_PC),
    .A_in(mips_regifile_1_r1), .MemToReg_in(\单周期硬布线控制器_1_memtoreg ), .B_in(mips_regifile_1_r2),
    .Imm_in(multiplexer_3_out), .RedDst_out(id_ex_1_reddst_out), .AluSrcB_out(id_ex_1_alusrcb_out),
    .Syscall_out(id_ex_1_syscall_out), .RegWrite_out(id_ex_1_regwrite_out), .Shamt_out(id_ex_1_shamt_out),
    .AluOp_out(id_ex_1_aluop_out), .MemWrite_out(id_ex_1_memwrite_out), .IR_out(EX_IR), .PC_out(EX_PC),
    .A_out(id_ex_1_a_out), .MemToReg_out(id_ex_1_memtoreg_out), .B_out(id_ex_1_b_out),
    .Imm_out(id_ex_1_imm_out), .CLR(RST), .CLK(CLK));  // open: JMP_in, JAL_in, JR_in, SLLV_in, Beq_in, LUI_in, Bne_in, SB_in, BGTZ_in, JMP_out, JAL_out, JR_out, PredictJMP_out, SLLV_out, Beq_out, LUI_out, Bne_out, SB_out, BGTZ_out, Stall, ERET_in, ERET_OUT, PredictJMP_in
  Multiplexer #(.select(1), .width(32), .disabled("Z"), .enable("false")) multiplexer_4 (
    .in0(id_ex_1_b_out), .in1(id_ex_1_imm_out), .out(multiplexer_4_out), .sel(id_ex_1_alusrcb_out));
  MIPS_ALU mips_alu_1 (
    .X(id_ex_1_a_out), .Y(multiplexer_4_out), .AluOP(id_ex_1_aluop_out), .Result(mips_alu_1_result),
    .shamt(id_ex_1_shamt_out));  // open: Equal, Result_2
  EX_MEM ex_mem_1 (
    .RedDst_in(id_ex_1_reddst_out), .Syscall_in(id_ex_1_syscall_out), .RegWrite_in(id_ex_1_regwrite_out),
    .AluResult_in(mips_alu_1_result), .MemWrite_in(id_ex_1_memwrite_out), .IR_in(EX_IR), .PC_in(EX_PC),
    .A_in(id_ex_1_a_out), .MemToReg_in(id_ex_1_memtoreg_out), .B_in(id_ex_1_b_out),
    .RedDst_out(ex_mem_1_reddst_out), .Syscall_out(ex_mem_1_syscall_out),
    .RegWrite_out(ex_mem_1_regwrite_out), .AluResult_out(ex_mem_1_aluresult_out), .MemWrite_out(MemWrite),
    .IR_out(MEM_IR), .PC_out(M_PC), .A_out(ex_mem_1_a_out), .MemToReg_out(ex_mem_1_memtoreg_out),
    .B_out(MDin), .CLR(RST), .CLK(CLK));  // open: AluSrcB_in, Shamt_in, JMP_in, JAL_in, JR_in, SignedExt_in, SLLV_in, Beq_in, LUI_in, Bne_in, SB_in, BGTZ_in, Imm_in, AluSrcB_out, Shamt_out, JMP_out, JAL_out, JR_out, SignedExt_out, SLLV_out, Beq_out, LUI_out, Bne_out, SB_out, BGTZ_out, Imm_out, Stall, ERET_in, ERET_OUT
  RAM #(.addrWidth(10), .dataWidth(32), .bus("separate"), .Select("high")) ram_1 (
    .addr(ex_mem_1_aluresult_out[11:2]), .din(MDin), .data(ram_1_data), .str(MemWrite), .clk(CLK));  // open: sel, ld, clr
  MEM_WB mem_wb_1 (
    .RedDst_in(ex_mem_1_reddst_out), .MemData_in(ram_1_data), .Syscall_in(ex_mem_1_syscall_out),
    .RegWrite_in(ex_mem_1_regwrite_out), .AluResult_in(ex_mem_1_aluresult_out), .IR_in(MEM_IR), .PC_in(M_PC),
    .A_in(ex_mem_1_a_out), .MemToReg_in(ex_mem_1_memtoreg_out), .B_in(MDin),
    .RedDst_out(mem_wb_1_reddst_out), .Syscall_out(mem_wb_1_syscall_out), .RegWrite_out(RegWrite),
    .MemData_out(mem_wb_1_memdata_out), .AluResult_out(mem_wb_1_aluresult_out), .IR_out(WB_IR),
    .PC_out(WB_PC), .A_out(mem_wb_1_a_out), .MemToReg_out(mem_wb_1_memtoreg_out), .B_out(mem_wb_1_b_out),
    .CLR(RST), .CLK(CLK));  // open: AluSrcB_in, JMP_in, JAL_in, JR_in, MemWrite_in, SignedExt_in, SLLV_in, Beq_in, LUI_in, Bne_in, SB_in, BGTZ_in, Imm_in, AluSrcB_out, JMP_out, JAL_out, JR_out, MemWrite_out, SignedExt_out, SLLV_out, Beq_out, Bne_out, SB_out, BGTZ_out, Imm_out, Stall, LUI_out, ERET_in, ERET_OUT
  Multiplexer #(.select(1), .width(32), .disabled("Z"), .enable("false")) multiplexer_5 (
    .in0(mem_wb_1_aluresult_out), .in1(mem_wb_1_memdata_out), .out(RDin), .sel(mem_wb_1_memtoreg_out));
  Multiplexer #(.select(1), .width(5), .disabled("Z"), .enable("false")) multiplexer_6 (
    .in0(WB_IR[20:16]), .in1(WB_IR[15:11]), .out(multiplexer_6_out), .sel(mem_wb_1_reddst_out));
  Comparator #(.width(32), .mode("twosComplement")) comparator_2 (
    .a(32'h22), .b(mem_wb_1_b_out), .eq(comparator_2_eq));  // open: gt, lt
  and and_1 (and_1_out, comparator_2_eq, mem_wb_1_syscall_out);
  and and_2 (and_2_out, mem_wb_1_syscall_out, ~comparator_2_eq);  // AND_Gate
  Register #(.width(32), .trigger("rising"), .Select("low")) register_1 (
    .D(mem_wb_1_a_out), .en(and_1_out), .Q(LedData), .clk(CLK));  // open: clr
  not not_1 (En, register_2_q);
  Register #(.width(1), .trigger("rising"), .Select("low")) register_2 (
    .D(mem_wb_1_syscall_out), .en(and_2_out), .Q(register_2_q), .clk(CLK), .clr(Go));

  // Other names for the same wires on the sheet: MEM_PC[31:0] = M_PC

  // Notes on the sheet:
  //   中断源
  //   时空图监测，可删除
  //   中断等待指示
  //   数码管输出
  //   contents of rom_1 (hex, n*v repeats v):
  //   20110001 8000c05 20110001 20120002 20130003 8000c09 20110001 20120002 20130003 8000c0d 20110001
  //   20120002 20130003 8000c11 20110001 20120002 20130003 c000cb8 20100001 20110001 118fc0 112020
  //   20020022 c 118882 12200001 8000c15 112020 20020022 c 20110001 118880 112020 20020022 c 12200001
  //   8000c1f 20110001 118fc0 112020 20020022 c 1188c3 112020 20020022 c 118903 112020 20020022 c 118903
  //   112020 20020022 c 118903 112020 20020022 c 118903 112020 20020022 c 118903 112020 20020022 c 118903
  //   112020 20020022 c 118903 112020 20020022 c 20100001 109fc0 139fc3 8021 2012000c 24160003 26100001
  //   3210000f 20080008 20090001 139900 2709825 132020 20020022 c 1094022 1500fff9 22100001 2018000f
  //   2188024 108700 20080008 20090001 139902 2709825 132021 20020022 c 1094022 1500fff9 108702 2c9b022
  //   12c00001 8000c50 4020 1084027 84400 3508ffff 82021 20020022 c 2010ffff 20110000 ae300000 22100001
  //   22310004 ae300000 22100001 22310004 ae300000 22100001 22310004 ae300000 22100001 22310004 ae300000
  //   22100001 22310004 ae300000 22100001 22310004 ae300000 22100001 22310004 ae300000 22100001 22310004
  //   ae300000 22100001 22310004 ae300000 22100001 22310004 ae300000 22100001 22310004 ae300000 22100001
  //   22310004 ae300000 22100001 22310004 ae300000 22100001 22310004 ae300000 22100001 22310004 ae300000
  //   22100001 22310004 22100001 8020 2011003c 8e130000 8e340000 274402a 11000002 ae330000 ae140000
  //   2231fffc 1611fff8 102020 20020022 c 22100004 2011003c 1611fff2 20020032 c 20100000 22100001 102020
  //   20020022 c 22100002 102020 20020022 c 22100003 102020 20020022 c 22100004 102020 20020022 c 22100005
  //   102020 20020022 c 22100006 102020 20020022 c 22100007 102020 20020022 c 22100008 102020 20020022
  //   20020022 c 3e00008
  //   控制位
  //   流水调试日志用
  //   暂停节拍，不能为0
  //   Func
  //   rs
  //   rt
  //   rd
  //   戳工具置1进入计数暂停模式，ctrl+k时钟自动运行到对应节拍暂停
  //   ctrl+k关闭时钟连续运行，将控制位置零，进入单步调试模式调试
  //   用这个时钟源需要去掉电路中的其他时钟源
  //   可计数暂停的时钟源
  //   为方便自动评测，需要输出流水线各段保存的PC值，注意是PC不是PC+4，另外ID段寄存器写入信息，Mem段内存写入信息也要输出
endmodule

module \气泡流水线  (
  output RegWrite,
  output MemWrite,
  output [31:0] IF_PC,
  output [31:0] ID_PC,
  output [31:0] EX_PC,
  output [31:0] M_PC,
  output [31:0] WB_PC,
  output [31:0] RDin,
  output [31:0] MDin,
  output [31:0] LedData
);

  wire and_1_out, and_2_out, and_3_out, and_4_out, and_5_out, and_6_out, and_7_out, and_8_out, Branch, Clear,
       CLK, clock_1_out, clock_2_out, comparator_1_eq, comparator_1_lt, comparator_2_gt, comparator_3_eq,
       Correlated, d_ff_1_q, En, EX_Beq, EX_BGTZ, EX_Bne, EX_JAL, EX_JMP, EX_JR, ex_mem_1_memtoreg_out,
       ex_mem_1_syscall_out, EX_RegDst, EX_RegWrite, Go, id_ex_1_alusrcb_out, id_ex_1_memtoreg_out,
       id_ex_1_memwrite_out, id_ex_1_sb_out, id_ex_1_syscall_out, IR1, IR2, IR3, MEM_JAL, MEM_RegDst,
       MEM_RegWrite, MEM_SB, mem_wb_1_jal_out, mem_wb_1_memtoreg_out, mem_wb_1_reddst_out,
       mem_wb_1_syscall_out, mips_alu_1_equal, nand_1_out, not_1_out, or_1_out, or_3_out, register_2_q, RST,
       SignedExt, W1, W2, W3, \单周期硬布线控制器_1_alu_src , \单周期硬布线控制器_1_beq , \单周期硬布线控制器_1_bgtz ,
       \单周期硬布线控制器_1_bne , \单周期硬布线控制器_1_jal , \单周期硬布线控制器_1_jmp , \单周期硬布线控制器_1_jr , \单周期硬布线控制器_1_lui ,
       \单周期硬布线控制器_1_memtoreg , \单周期硬布线控制器_1_memwrite , \单周期硬布线控制器_1_regdst , \单周期硬布线控制器_1_regwrite ,
       \单周期硬布线控制器_1_sb , \单周期硬布线控制器_1_sllv , \单周期硬布线控制器_1_syscall ;
  wire [3:0] id_ex_1_aluop_out, \单周期硬布线控制器_1_alu_op ;
  wire [4:0] EX_Shamt, multiplexer_1_out, multiplexer_2_out, multiplexer_3_out, multiplexer_4_out,
       multiplexer_13_out, multiplexer_15_out, R1_num, R2_num, undriven;
  wire [5:0] Func;
  wire [12:0] CNT_num;
  wire [15:0] \LoadUse次数 , \总周期数 , \插入气泡数 , \无条件分支数 , \条件分支成功数 ;
  wire [15:8] ram_1_data_2;
  wire [31:0] adder_2_out, adder_3_out, adder_4_out, bit_extender_1_out, bit_extender_2_out,
       controlled_buffer_2_out, EX_A, EX_B, EX_Imm, EX_IR, ex_mem_1_a_out, ex_mem_1_aluresult_out, IF_IR,
       MEM_IR, mem_wb_1_a_out, mem_wb_1_aluresult_out, mem_wb_1_b_out, mem_wb_1_memdata_out,
       mips_alu_1_result, mips_regifile_1_r1, mips_regifile_1_r2, multiplexer_7_out, multiplexer_8_out,
       multiplexer_10_out, multiplexer_11_out, multiplexer_12_out, PC_4, ram_1_data, shifter_1_out, WB_IR;
  wire [31:6] ID_IR;

  Button \u_总复位  (.out(RST));
  Button _1 (.out(IR1));
  Button _2 (.out(IR2));
  Button _3 (.out(IR3));
  // Probe on \总周期数 
  // Probe on \总周期数 
  Button \u_继续运行  (.out(Go));
  LED #(.active("true")) led_1 (.in(W1));
  LED #(.active("true")) led_2 (.in(W2));
  LED #(.active("true")) led_3 (.in(W3));
  Hex_Digit_Display hex_digit_display_1 (.value(LedData[31:28]));  // open: dp
  // Probe on IF_PC[19:0]
  // Mips_Probe mips_probe_1: pin names not known; wires that end beside it: IF_IR
  and and_1 (and_1_out, ~Correlated, En);  // AND_Gate
  Hex_Digit_Display hex_digit_display_2 (.value(LedData[27:24]));  // open: dp
  Hex_Digit_Display hex_digit_display_3 (.value(LedData[23:20]));  // open: dp
  // Probe on ID_PC[19:0]
  // Mips_Probe mips_probe_2: pin names not known; wires that end beside it: {ID_IR, Func}
  Register #(.width(32), .trigger("rising"), .Select("low")) PC (
    .D(controlled_buffer_2_out), .en(and_1_out), .Q(IF_PC), .clk(CLK));  // open: clr
  Hex_Digit_Display hex_digit_display_4 (.value(LedData[19:16]));  // open: dp
  Hex_Digit_Display hex_digit_display_5 (.value(LedData[15:12]));  // open: dp
  Adder #(.width(32)) adder_1 (.a(32'h4), .b(IF_PC), .out(PC_4));  // open: cin, cout
  Hex_Digit_Display hex_digit_display_6 (.value(LedData[11:8]));  // open: dp
  Hex_Digit_Display hex_digit_display_7 (.value(LedData[7:4]));  // open: dp
  Clock #(.highDuration(1), .lowDuration(1)) clock_1 (.out(clock_1_out));
  // Probe on EX_PC[19:0]
  // Mips_Probe mips_probe_3: pin names not known; wires that end beside it: clock_1_out, EX_IR, CLK
  Hex_Digit_Display hex_digit_display_8 (.value(LedData[3:0]));  // open: dp
  ROM #(.addrWidth(10), .dataWidth(32), .Select("low")) rom_1 (.addr(IF_PC[11:2]), .data(IF_IR));
  // Probe on \总周期数 
  // Probe on M_PC[19:0]
  // Mips_Probe mips_probe_4: pin names not known; wires that end beside it: MEM_IR
  Multiplexer #(.select(1), .width(5), .disabled("Z"), .enable("false")) multiplexer_1 (
    .in0(MEM_IR[20:16]), .in1(MEM_IR[15:11]), .out(multiplexer_1_out), .sel(MEM_RegDst));
  Multiplexer #(.select(1), .width(5), .disabled("Z"), .enable("false")) multiplexer_2 (
    .in0(EX_IR[20:16]), .in1(EX_IR[15:11]), .out(multiplexer_2_out), .sel(EX_RegDst));
  // Probe on \总周期数 
  // Probe on \无条件分支数 
  // Probe on \条件分支成功数 
  // Probe on \插入气泡数 
  // Probe on \LoadUse次数 
  IF_ID if_id_1 (
    .IR_in(IF_IR), .PC_in(IF_PC), .IR_out({ID_IR, Func}), .PC_out(ID_PC), .CLR(or_1_out), .Stall(Correlated),
    .CLK(CLK));  // open: RedDst_in, AluSrcB_in, Shamt_in, Syscall_in, RegWrite_in, JMP_in, AluOp_in, JAL_in, JR_in, MemWrite_in, PredictJMP_in, SLLV_in, Beq_in, LUI_in, Bne_in, A_in, SB_in, MemToReg_in, BGTZ_in, B_in, Imm_in, RedDst_out, AluSrcB_out, Syscall_out, Shamt_out, RegWrite_out, JMP_out, AluOp_out, JAL_out, JR_out, MemWrite_out, PredictJMP_out, SLLV_out, Beq_out, A_out, LUI_out, Bne_out, SB_out, MemToReg_out, B_out, BGTZ_out, Imm_out
  or or_1 (or_1_out, Clear, RST);
  Multiplexer #(.select(1), .width(5), .disabled("Z"), .enable("false")) multiplexer_3 (
    .in0(multiplexer_2_out), .in1({5{1'b1}}), .out(multiplexer_3_out), .sel(EX_JAL));
  // Probe on IF_PC[11:0]
  // Probe on WB_PC[19:0]
  // Mips_Probe mips_probe_5: pin names not known; wires that end beside it: WB_IR
  Multiplexer #(.select(1), .width(5), .disabled("Z"), .enable("false")) multiplexer_4 (
    .in0(multiplexer_1_out), .in1({5{1'b1}}), .out(multiplexer_4_out), .sel(MEM_JAL));
  // Probe on EX_PC[11:0]
  // Probe on ID_PC[11:0]
  \单周期硬布线控制器  \u_单周期硬布线控制器_1  (
    .Func(Func), .OP(ID_IR[31:26]), .ALU_OP(\单周期硬布线控制器_1_alu_op ), .MemToReg(\单周期硬布线控制器_1_memtoreg ),
    .MemWrite(\单周期硬布线控制器_1_memwrite ), .ALU_SRC(\单周期硬布线控制器_1_alu_src ), .RegWrite(\单周期硬布线控制器_1_regwrite ),
    .SysCALL(\单周期硬布线控制器_1_syscall ), .SignedExt(SignedExt), .RegDst(\单周期硬布线控制器_1_regdst ),
    .JR(\单周期硬布线控制器_1_jr ), .JMP(\单周期硬布线控制器_1_jmp ), .Beq(\单周期硬布线控制器_1_beq ), .JAL(\单周期硬布线控制器_1_jal ),
    .Bne(\单周期硬布线控制器_1_bne ), .SLLV(\单周期硬布线控制器_1_sllv ), .LUI(\单周期硬布线控制器_1_lui ), .SB(\单周期硬布线控制器_1_sb ),
    .BGTZ(\单周期硬布线控制器_1_bgtz ));  // open: in_3, MFC0, MTC0
  // Probe on M_PC[11:0]
  D_Flip_Flop #(.trigger("high"), .Pre_Clr_Positions("LEGACY"), .NegatePresetClear("false"), .enable("true"), .NewFFLayout("false")) d_ff_1 (.Q(d_ff_1_q));  // open: clk, D, Qn, preset, en, reset
  // Probe on 13'h1b
  Multiplexer #(.select(1), .width(5), .disabled("Z"), .enable("false")) multiplexer_5 (
    .in0(ID_IR[25:21]), .in1(5'b00100), .out(R1_num), .sel(\单周期硬布线控制器_1_syscall ));
  Multiplexer #(.select(1), .width(5), .disabled("Z"), .enable("false")) multiplexer_6 (
    .in0(ID_IR[20:16]), .in1(5'b00010), .out(R2_num), .sel(\单周期硬布线控制器_1_syscall ));
  // Probe on WB_PC[11:0]
  Comparator #(.width(13), .mode("twosComplement")) comparator_1 (
    .a(CNT_num), .b(13'h1b), .eq(comparator_1_eq), .lt(comparator_1_lt));  // open: gt
  Clock #(.highDuration(1), .lowDuration(1)) clock_2 (.out(clock_2_out));
  assign bit_extender_1_out = {{16{1'b0}}, {ID_IR[15:6], Func}};  // Bit_Extender bit_extender_1
  assign bit_extender_2_out = {{16{ID_IR[15]}}, {ID_IR[15:6], Func}};  // Bit_Extender bit_extender_2
  \数据相关检测  \u_数据相关检测_1  (
    .R1_num(R1_num), .MEM_WriteReg_num(multiplexer_4_out), .R2_num(R2_num),
    .EX_WriteReg_num(multiplexer_3_out), .OP(ID_IR[31:26]), .FUNC(Func), .MEM_WriteReg(MEM_RegWrite),
    .EX_WriteReg(EX_RegWrite), .Correlated(Correlated));
  nand nand_1 (nand_1_out, d_ff_1_q, comparator_1_eq);
  Counter #(.width(13), .max('h1fff), .ongoal("stay"), .trigger("rising"), .behavior("old")) counter_1 (
    .count(comparator_1_lt), .Q(CNT_num), .clk(clock_2_out));  // open: load, D, carry, clr, preset
  MIPS_Regifile mips_regifile_1 (
    .Din(RDin), .Clk(CLK), .R1(mips_regifile_1_r1), .R2(mips_regifile_1_r2), .WE(RegWrite),
    .W_num(multiplexer_15_out), .R1_num(R1_num), .R2_num(R2_num));
  assign CLK = nand_1_out ? clock_2_out : 1'bz;  // Controlled_Buffer controlled_buffer_1
  Multiplexer #(.select(1), .width(32), .disabled("Z"), .enable("false")) multiplexer_7 (
    .in0(bit_extender_1_out), .in1(bit_extender_2_out), .out(multiplexer_7_out), .sel(SignedExt));
  Pull_Resistor #(.pull(1)) pull_resistor_1 (.node(CLK));
  Shifter #(.width(32), .shift("ll")) shifter_1 (.in(EX_Imm), .\dist (5'b00010), .out(shifter_1_out));
  Adder #(.width(32)) adder_2 (.a(EX_PC), .b(32'h4), .out(adder_2_out));  // open: cin, cout
  not not_1 (not_1_out, Clear);
  or or_2 (Clear, EX_JMP, Branch);
  Counter #(.width(16), .max('hffff), .ongoal("wrap"), .trigger("rising"), .behavior("new")) counter_2 (
    .Q(\总周期数 ), .clk(and_2_out));  // open: load, D, count, carry, clr, preset, down
  and and_2 (and_2_out, En, CLK);
  ID_EX id_ex_1 (
    .RedDst_in(\单周期硬布线控制器_1_regdst ), .AluSrcB_in(\单周期硬布线控制器_1_alu_src ), .Shamt_in(ID_IR[10:6]),
    .Syscall_in(\单周期硬布线控制器_1_syscall ), .RegWrite_in(\单周期硬布线控制器_1_regwrite ), .JMP_in(\单周期硬布线控制器_1_jmp ),
    .JAL_in(\单周期硬布线控制器_1_jal ), .AluOp_in(\单周期硬布线控制器_1_alu_op ), .JR_in(\单周期硬布线控制器_1_jr ),
    .MemWrite_in(\单周期硬布线控制器_1_memwrite ), .IR_in({ID_IR, Func}), .SLLV_in(\单周期硬布线控制器_1_sllv ), .PC_in(ID_PC),
    .Beq_in(\单周期硬布线控制器_1_beq ), .LUI_in(\单周期硬布线控制器_1_lui ), .Bne_in(\单周期硬布线控制器_1_bne ),
    .SB_in(\单周期硬布线控制器_1_sb ), .A_in(mips_regifile_1_r1), .MemToReg_in(\单周期硬布线控制器_1_memtoreg ),
    .BGTZ_in(\单周期硬布线控制器_1_bgtz ), .B_in(mips_regifile_1_r2), .Imm_in(multiplexer_7_out),
    .RedDst_out(EX_RegDst), .AluSrcB_out(id_ex_1_alusrcb_out), .Syscall_out(id_ex_1_syscall_out),
    .RegWrite_out(EX_RegWrite), .Shamt_out(EX_Shamt), .JMP_out(EX_JMP), .JAL_out(EX_JAL),
    .AluOp_out(id_ex_1_aluop_out), .JR_out(EX_JR), .MemWrite_out(id_ex_1_memwrite_out), .IR_out(EX_IR),
    .PC_out(EX_PC), .Beq_out(EX_Beq), .A_out(EX_A), .Bne_out(EX_Bne), .SB_out(id_ex_1_sb_out),
    .MemToReg_out(id_ex_1_memtoreg_out), .BGTZ_out(EX_BGTZ), .B_out(EX_B), .Imm_out(EX_Imm), .CLR(or_3_out),
    .Stall(1'b0), .CLK(CLK));  // open: PredictJMP_out, SLLV_out, LUI_out, ERET_in, ERET_OUT, PredictJMP_in
  or or_3 (or_3_out, Clear, Correlated, RST);
  assign controlled_buffer_2_out = EX_JR ? EX_A : 32'bz;  // Controlled_Buffer controlled_buffer_2
  Adder #(.width(32)) adder_3 (.a(shifter_1_out), .b(adder_2_out), .out(adder_3_out));  // open: cin, cout
  and and_3 (and_3_out, EX_JMP, ~EX_JR);  // AND_Gate
  assign controlled_buffer_2_out = and_3_out ? {EX_PC[31:28], EX_IR[25:0], 2'b00} : 32'bz;  // Controlled_Buffer controlled_buffer_3
  assign controlled_buffer_2_out = not_1_out ? PC_4 : 32'bz;  // Controlled_Buffer controlled_buffer_4
  Multiplexer #(.select(1), .width(32), .disabled("Z"), .enable("false")) multiplexer_8 (
    .in0(EX_B), .in1(EX_Imm), .out(multiplexer_8_out), .sel(id_ex_1_alusrcb_out));
  assign controlled_buffer_2_out = Branch ? adder_3_out : 32'bz;  // Controlled_Buffer controlled_buffer_5
  Multiplexer #(.select(1), .width(5), .disabled("Z"), .enable("false")) multiplexer_9 (.in0(undriven));  // open: in1, out, sel
  Comparator #(.width(32), .mode("twosComplement")) comparator_2 (
    .a(EX_A), .b({32{1'b0}}), .gt(comparator_2_gt));  // open: eq, lt
  MIPS_ALU mips_alu_1 (
    .X(EX_A), .Y(multiplexer_8_out), .AluOP(id_ex_1_aluop_out), .Equal(mips_alu_1_equal),
    .Result(mips_alu_1_result), .shamt(EX_Shamt));  // open: Result_2
  and and_4 (and_4_out, EX_Beq, mips_alu_1_equal);
  and and_5 (and_5_out, EX_Bne, ~mips_alu_1_equal);  // AND_Gate
  and and_6 (and_6_out, comparator_2_gt, EX_BGTZ);
  or or_4 (Branch, and_4_out, and_5_out, and_6_out);
  Multiplexer #(.select(1), .width(32), .disabled("Z"), .enable("false")) multiplexer_10 (
    .in0(MDin), .in1(multiplexer_11_out), .out(multiplexer_10_out), .sel(MEM_SB));
  EX_MEM ex_mem_1 (
    .RedDst_in(EX_RegDst), .Syscall_in(id_ex_1_syscall_out), .RegWrite_in(EX_RegWrite), .JAL_in(EX_JAL),
    .AluResult_in(mips_alu_1_result), .MemWrite_in(id_ex_1_memwrite_out), .IR_in(EX_IR), .PC_in(EX_PC),
    .SB_in(id_ex_1_sb_out), .A_in(EX_A), .MemToReg_in(id_ex_1_memtoreg_out), .B_in(EX_B),
    .RedDst_out(MEM_RegDst), .Syscall_out(ex_mem_1_syscall_out), .RegWrite_out(MEM_RegWrite),
    .JAL_out(MEM_JAL), .AluResult_out(ex_mem_1_aluresult_out), .MemWrite_out(MemWrite), .IR_out(MEM_IR),
    .PC_out(M_PC), .A_out(ex_mem_1_a_out), .SB_out(MEM_SB), .MemToReg_out(ex_mem_1_memtoreg_out),
    .B_out(MDin), .CLR(RST), .Stall(1'b0), .CLK(CLK));  // open: AluSrcB_in, Shamt_in, JMP_in, JR_in, SignedExt_in, SLLV_in, Beq_in, LUI_in, Bne_in, BGTZ_in, Imm_in, AluSrcB_out, Shamt_out, JMP_out, JR_out, SignedExt_out, SLLV_out, Beq_out, LUI_out, Bne_out, BGTZ_out, Imm_out, ERET_in, ERET_OUT
  Multiplexer #(.select(2), .width(32), .disabled("Z"), .enable("false")) multiplexer_11 (
    .in0({ram_1_data[31:16], ram_1_data_2, MDin[7:0]}),
    .in1({ram_1_data[31:16], MDin[7:0], ram_1_data[7:0]}),
    .in2({ram_1_data[31:24], MDin[7:0], ram_1_data_2, ram_1_data[7:0]}),
    .in3({MDin[7:0], ram_1_data[23:16], ram_1_data_2, ram_1_data[7:0]}), .out(multiplexer_11_out),
    .sel(ex_mem_1_aluresult_out[1:0]));
  RAM #(.addrWidth(10), .dataWidth(32), .bus("separate"), .Select("high")) ram_1 (
    .addr(ex_mem_1_aluresult_out[11:2]), .din(multiplexer_10_out),
    .data({ram_1_data[31:16], ram_1_data_2, ram_1_data[7:0]}), .str(MemWrite), .clk(CLK), .ld(1'b1));  // open: sel, clr
  MEM_WB mem_wb_1 (
    .RedDst_in(MEM_RegDst), .MemData_in({ram_1_data[31:16], ram_1_data_2, ram_1_data[7:0]}),
    .Syscall_in(ex_mem_1_syscall_out), .RegWrite_in(MEM_RegWrite), .JAL_in(MEM_JAL),
    .AluResult_in(ex_mem_1_aluresult_out), .IR_in(MEM_IR), .PC_in(M_PC), .A_in(ex_mem_1_a_out),
    .MemToReg_in(ex_mem_1_memtoreg_out), .B_in(MDin), .RedDst_out(mem_wb_1_reddst_out),
    .Syscall_out(mem_wb_1_syscall_out), .RegWrite_out(RegWrite), .MemData_out(mem_wb_1_memdata_out),
    .JAL_out(mem_wb_1_jal_out), .AluResult_out(mem_wb_1_aluresult_out), .IR_out(WB_IR), .PC_out(WB_PC),
    .A_out(mem_wb_1_a_out), .MemToReg_out(mem_wb_1_memtoreg_out), .B_out(mem_wb_1_b_out), .CLR(RST),
    .Stall(1'b0), .CLK(CLK));  // open: AluSrcB_in, JMP_in, JR_in, MemWrite_in, SignedExt_in, SLLV_in, Beq_in, LUI_in, Bne_in, SB_in, BGTZ_in, Imm_in, AluSrcB_out, JMP_out, JR_out, MemWrite_out, SignedExt_out, SLLV_out, Beq_out, Bne_out, SB_out, BGTZ_out, Imm_out, LUI_out, ERET_in, ERET_OUT
  Multiplexer #(.select(1), .width(32), .disabled("Z"), .enable("false")) multiplexer_12 (
    .in0(mem_wb_1_aluresult_out), .in1(mem_wb_1_memdata_out), .out(multiplexer_12_out),
    .sel(mem_wb_1_memtoreg_out));
  Adder #(.width(32)) adder_4 (.a(WB_PC), .b(32'h4), .out(adder_4_out));  // open: cin, cout
  Multiplexer #(.select(1), .width(5), .disabled("Z"), .enable("false")) multiplexer_13 (
    .in0(WB_IR[20:16]), .in1(WB_IR[15:11]), .out(multiplexer_13_out), .sel(mem_wb_1_reddst_out));
  Multiplexer #(.select(1), .width(32), .disabled("Z"), .enable("false")) multiplexer_14 (
    .in0(multiplexer_12_out), .in1(adder_4_out), .out(RDin), .sel(mem_wb_1_jal_out));
  Multiplexer #(.select(1), .width(5), .disabled("Z"), .enable("false")) multiplexer_15 (
    .in0(multiplexer_13_out), .in1({5{1'b1}}), .out(multiplexer_15_out), .sel(mem_wb_1_jal_out));
  Comparator #(.width(32), .mode("twosComplement")) comparator_3 (
    .a(32'h22), .b(mem_wb_1_b_out), .eq(comparator_3_eq));  // open: gt, lt
  and and_7 (and_7_out, comparator_3_eq, mem_wb_1_syscall_out);
  and and_8 (and_8_out, mem_wb_1_syscall_out, ~comparator_3_eq);  // AND_Gate
  Register #(.width(32), .trigger("rising"), .Select("low")) register_1 (
    .D(mem_wb_1_a_out), .en(and_7_out), .Q(LedData), .clk(CLK));  // open: clr
  Register #(.width(1), .trigger("rising"), .Select("low")) register_2 (
    .D(mem_wb_1_syscall_out), .en(and_8_out), .Q(register_2_q), .clk(CLK), .clr(Go));
  not not_2 (En, register_2_q);

  // Other names for the same wires on the sheet: ID_IR[5:0] = Func; OP[5:0] = ID_IR[31:26]; MEM_PC[31:0] = M_PC

  // Notes on the sheet:
  //   中断源
  //   时空图监测，可删除
  //   中断等待指示
  //   数码管输出
  //   contents of rom_1 (hex, n*v repeats v):
  //   20110001 8000c05 20110001 20120002 20130003 8000c09 20110001 20120002 20130003 8000c0d 20110001
  //   20120002 20130003 8000c11 20110001 20120002 20130003 c000cb8 20100001 20110001 118fc0 112020
  //   20020022 c 118882 12200001 8000c15 112020 20020022 c 20110001 118880 112020 20020022 c 12200001
  //   8000c1f 20110001 118fc0 112020 20020022 c 1188c3 112020 20020022 c 118903 112020 20020022 c 118903
  //   112020 20020022 c 118903 112020 20020022 c 118903 112020 20020022 c 118903 112020 20020022 c 118903
  //   112020 20020022 c 118903 112020 20020022 c 20100001 109fc0 139fc3 8021 2012000c 24160003 26100001
  //   3210000f 20080008 20090001 139900 2709825 132020 20020022 c 1094022 1500fff9 22100001 2018000f
  //   2188024 108700 20080008 20090001 139902 2709825 132021 20020022 c 1094022 1500fff9 108702 2c9b022
  //   12c00001 8000c50 4020 1084027 84400 3508ffff 82021 20020022 c 2010ffff 20110000 ae300000 22100001
  //   22310004 ae300000 22100001 22310004 ae300000 22100001 22310004 ae300000 22100001 22310004 ae300000
  //   22100001 22310004 ae300000 22100001 22310004 ae300000 22100001 22310004 ae300000 22100001 22310004
  //   ae300000 22100001 22310004 ae300000 22100001 22310004 ae300000 22100001 22310004 ae300000 22100001
  //   22310004 ae300000 22100001 22310004 ae300000 22100001 22310004 ae300000 22100001 22310004 ae300000
  //   22100001 22310004 22100001 8020 2011003c 8e130000 8e340000 274402a 11000002 ae330000 ae140000
  //   2231fffc 1611fff8 102020 20020022 c 22100004 2011003c 1611fff2 20020032 c 20100000 22100001 102020
  //   20020022 c 22100002 102020 20020022 c 22100003 102020 20020022 c 22100004 102020 20020022 c 22100005
  //   102020 20020022 c 22100006 102020 20020022 c 22100007 102020 20020022 c 22100008 102020 20020022
  //   20020022 c 3e00008
  //   rt
  //   rd
  //   rt
  //   rd
  //   rt
  //   rd
  //   控制位
  //   rs
  //   流水调试日志用
  //   暂停节拍，不能为0
  //   戳工具置1进入计数暂停模式，ctrl+k时钟自动运行到对应节拍暂停
  //   ctrl+k关闭时钟连续运行，将控制位置零，进入单步调试模式调试
  //   可计数暂停的时钟源
  //   为方便自动评测，需要输出流水线各段保存的PC值，注意是PC不是PC+4，另外ID段寄存器写入信息，Mem段内存写入信息也要输出
endmodule
module \重定向流水线  (
  output RegWrite,
  output MemWrite,
  output [31:0] IF_PC,
  output [31:0] ID_PC,
  output [31:0] EX_PC,
  output [31:0] M_PC,
  output [31:0] WB_PC,
  output [31:0] RDin,
  output [31:0] MDin,
  output [31:0] LedData
);

  wire and_1_out, and_2_out, and_3_out, and_4_out, and_5_out, and_6_out, and_7_out, and_8_out, Branch, Clear,
       CLK, clock_1_out, clock_2_out, comparator_1_eq, comparator_2_eq, comparator_3_eq, comparator_3_lt,
       comparator_4_gt, comparator_5_eq, d_ff_1_q, En, EX_Beq, EX_BGTZ, EX_Bne, EX_JAL, EX_JMP, EX_JR,
       EX_LUI, ex_mem_1_memtoreg_out, ex_mem_1_syscall_out, EX_RegDst, EX_RegWrite, EX_SLLV, Go,
       id_ex_1_alusrcb_out, id_ex_1_memtoreg_out, id_ex_1_memwrite_out, id_ex_1_sb_out, id_ex_1_syscall_out,
       IR1, IR2, IR3, LoadUse, MEM_JAL, MEM_RegDst, MEM_RegWrite, MEM_SB, mem_wb_1_jal_out,
       mem_wb_1_memtoreg_out, mem_wb_1_reddst_out, mem_wb_1_syscall_out, mips_alu_1_equal, nand_1_out,
       not_1_out, or_1_out, or_2_out, or_4_out, register_4_q, RST, SignedExt, W1, W2, W3,
       \单周期硬布线控制器_1_alu_src , \单周期硬布线控制器_1_beq , \单周期硬布线控制器_1_bgtz , \单周期硬布线控制器_1_bne , \单周期硬布线控制器_1_jal ,
       \单周期硬布线控制器_1_jmp , \单周期硬布线控制器_1_jr , \单周期硬布线控制器_1_lui , \单周期硬布线控制器_1_memtoreg ,
       \单周期硬布线控制器_1_memwrite , \单周期硬布线控制器_1_regdst , \单周期硬布线控制器_1_regwrite , \单周期硬布线控制器_1_sb ,
       \单周期硬布线控制器_1_sllv , \单周期硬布线控制器_1_syscall ;
  wire [1:0] R1_trans, R2_trans, \重定向数据相关检测_1_r1 , \重定向数据相关检测_1_r2 ;
  wire [3:0] id_ex_1_aluop_out, \单周期硬布线控制器_1_alu_op ;
  wire [4:0] EX_Shamt, multiplexer_1_out, multiplexer_2_out, multiplexer_3_out, multiplexer_4_out,
       multiplexer_11_out, multiplexer_16_out, multiplexer_18_out, R1_num, R2_num;
  wire [5:0] Func;
  wire [12:0] CNT_num;
  wire [15:0] \LoadUse次数 , \总周期数 , \插入气泡数 , \无条件分支数 , \条件分支成功数 ;
  wire [15:8] ram_1_data_2;
  wire [31:0] adder_2_out, adder_3_out, adder_4_out, bit_extender_1_out, bit_extender_2_out, EX_A, EX_AluA,
       EX_B, EX_B_mux, EX_Imm, EX_IR, ex_mem_1_a_out, IF_IR, INS, MEM_AluResult, MEM_IR, mem_wb_1_a_out,
       mem_wb_1_aluresult_out, mem_wb_1_b_out, mem_wb_1_memdata_out, mips_alu_1_result, mips_regifile_1_r1,
       mips_regifile_1_r2, multiplexer_7_out, multiplexer_10_out, multiplexer_12_out, multiplexer_13_out,
       multiplexer_14_out, multiplexer_15_out, PC_4, ram_1_data, shifter_1_out, WB_IR;
  wire [31:6] ID_IR;

  Button \u_总复位  (.out(RST));
  Button _1 (.out(IR1));
  Button _2 (.out(IR2));
  Button _3 (.out(IR3));
  // Probe on \总周期数 
  // Probe on \总周期数 
  Button \u_继续运行  (.out(Go));
  LED #(.active("true")) led_1 (.in(W1));
  LED #(.active("true")) led_2 (.in(W2));
  LED #(.active("true")) led_3 (.in(W3));
  Hex_Digit_Display hex_digit_display_1 (.value(LedData[31:28]));  // open: dp
  // Probe on IF_PC[19:0]
  // Mips_Probe mips_probe_1: pin names not known; wires that end beside it: IF_IR
  and and_1 (and_1_out, ~LoadUse, En);  // AND_Gate
  Hex_Digit_Display hex_digit_display_2 (.value(LedData[23:20]));  // open: dp
  Hex_Digit_Display hex_digit_display_3 (.value(LedData[27:24]));  // open: dp
  // Probe on ID_PC[19:0]
  // Mips_Probe mips_probe_2: pin names not known; wires that end beside it: {ID_IR, Func}
  Register #(.width(32), .trigger("rising"), .Select("low")) PC (
    .D(INS), .en(and_1_out), .Q(IF_PC), .clk(CLK));  // open: clr
  Hex_Digit_Display hex_digit_display_4 (.value(LedData[15:12]));  // open: dp
  Hex_Digit_Display hex_digit_display_5 (.value(LedData[19:16]));  // open: dp
  Adder #(.width(32)) adder_1 (.a(32'h4), .b(IF_PC), .out(PC_4));  // open: cin, cout
  Hex_Digit_Display hex_digit_display_6 (.value(LedData[11:8]));  // open: dp
  Hex_Digit_Display hex_digit_display_7 (.value(LedData[7:4]));  // open: dp
  Clock #(.highDuration(1), .lowDuration(1)) clock_1 (.out(clock_1_out));
  // Probe on EX_PC[19:0]
  // Mips_Probe mips_probe_3: pin names not known; wires that end beside it: clock_1_out, EX_IR, CLK
  Counter #(.width(16), .max('hffff), .ongoal("wrap"), .trigger("rising"), .behavior("new")) counter_1 (
    .Q(\总周期数 ), .clk(and_2_out));  // open: load, D, count, carry, clr, preset, down
  and and_2 (and_2_out, En, CLK);
  Hex_Digit_Display hex_digit_display_8 (.value(LedData[3:0]));  // open: dp
  ROM #(.addrWidth(10), .dataWidth(32), .Select("low")) rom_1 (.addr(IF_PC[11:2]), .data(IF_IR));
  // Probe on \总周期数 
  // Probe on M_PC[19:0]
  // Mips_Probe mips_probe_4: pin names not known; wires that end beside it: MEM_IR
  Multiplexer #(.select(1), .width(5), .disabled("Z"), .enable("false")) multiplexer_1 (
    .in0(MEM_IR[20:16]), .in1(MEM_IR[15:11]), .out(multiplexer_1_out), .sel(MEM_RegDst));
  Multiplexer #(.select(1), .width(5), .disabled("Z"), .enable("false")) multiplexer_2 (
    .in0(EX_IR[20:16]), .in1(EX_IR[15:11]), .out(multiplexer_2_out), .sel(EX_RegDst));
  // Probe on \总周期数 
  // Probe on \无条件分支数 
  // Probe on \条件分支成功数 
  // Probe on \插入气泡数 
  // Probe on \LoadUse次数 
  IF_ID if_id_1 (
    .IR_in(IF_IR), .PC_in(IF_PC), .IR_out({ID_IR, Func}), .PC_out(ID_PC), .CLR(or_1_out), .Stall(LoadUse),
    .CLK(CLK));  // open: RedDst_in, AluSrcB_in, Shamt_in, Syscall_in, RegWrite_in, JMP_in, AluOp_in, JAL_in, JR_in, MemWrite_in, PredictJMP_in, SLLV_in, Beq_in, LUI_in, Bne_in, A_in, SB_in, MemToReg_in, BGTZ_in, B_in, Imm_in, RedDst_out, AluSrcB_out, Syscall_out, Shamt_out, RegWrite_out, JMP_out, AluOp_out, JAL_out, JR_out, MemWrite_out, PredictJMP_out, SLLV_out, Beq_out, A_out, LUI_out, Bne_out, SB_out, MemToReg_out, B_out, BGTZ_out, Imm_out
  or or_1 (or_1_out, Clear, RST);
  Multiplexer #(.select(1), .width(5), .disabled("Z"), .enable("false")) multiplexer_3 (
    .in0(multiplexer_2_out), .in1({5{1'b1}}), .out(multiplexer_3_out), .sel(EX_JAL));
  // Probe on IF_PC[11:0]
  // Probe on WB_PC[19:0]
  // Mips_Probe mips_probe_5: pin names not known; wires that end beside it: WB_IR
  Multiplexer #(.select(1), .width(5), .disabled("Z"), .enable("false")) multiplexer_4 (
    .in0(multiplexer_1_out), .in1({5{1'b1}}), .out(multiplexer_4_out), .sel(MEM_JAL));
  // Probe on ID_PC[11:0]
  // Probe on EX_PC[11:0]
  \单周期硬布线控制器  \u_单周期硬布线控制器_1  (
    .Func(Func), .OP(ID_IR[31:26]), .ALU_OP(\单周期硬布线控制器_1_alu_op ), .MemToReg(\单周期硬布线控制器_1_memtoreg ),
    .MemWrite(\单周期硬布线控制器_1_memwrite ), .ALU_SRC(\单周期硬布线控制器_1_alu_src ), .RegWrite(\单周期硬布线控制器_1_regwrite ),
    .SysCALL(\单周期硬布线控制器_1_syscall ), .SignedExt(SignedExt), .RegDst(\单周期硬布线控制器_1_regdst ),
    .JR(\单周期硬布线控制器_1_jr ), .JMP(\单周期硬布线控制器_1_jmp ), .Beq(\单周期硬布线控制器_1_beq ), .JAL(\单周期硬布线控制器_1_jal ),
    .Bne(\单周期硬布线控制器_1_bne ), .SLLV(\单周期硬布线控制器_1_sllv ), .LUI(\单周期硬布线控制器_1_lui ), .SB(\单周期硬布线控制器_1_sb ),
    .BGTZ(\单周期硬布线控制器_1_bgtz ));  // open: in_3, MFC0, MTC0
  Comparator #(.width(6), .mode("twosComplement")) comparator_1 (
    .a(EX_IR[31:26]), .b(6'b100011), .eq(comparator_1_eq));  // open: gt, lt
  or or_2 (or_2_out, comparator_1_eq, comparator_2_eq);
  Comparator #(.width(6), .mode("twosComplement")) comparator_2 (
    .a(EX_IR[31:26]), .b(6'b100101), .eq(comparator_2_eq));  // open: gt, lt
  // Probe on M_PC[11:0]
  D_Flip_Flop #(.trigger("high"), .Pre_Clr_Positions("LEGACY"), .NegatePresetClear("false"), .enable("true"), .NewFFLayout("false")) d_ff_1 (.Q(d_ff_1_q));  // open: clk, D, Qn, preset, en, reset
  // Probe on 13'h10
  Multiplexer #(.select(1), .width(5), .disabled("Z"), .enable("false")) multiplexer_5 (
    .in0(ID_IR[25:21]), .in1(5'b00100), .out(R1_num), .sel(\单周期硬布线控制器_1_syscall ));
  Multiplexer #(.select(1), .width(5), .disabled("Z"), .enable("false")) multiplexer_6 (
    .in0(ID_IR[20:16]), .in1(5'b00010), .out(R2_num), .sel(\单周期硬布线控制器_1_syscall ));
  // Probe on WB_PC[11:0]
  Comparator #(.width(13), .mode("twosComplement")) comparator_3 (
    .a(CNT_num), .b(13'h10), .eq(comparator_3_eq), .lt(comparator_3_lt));  // open: gt
  Clock #(.highDuration(1), .lowDuration(1)) clock_2 (.out(clock_2_out));
  assign bit_extender_1_out = {{16{1'b0}}, {ID_IR[15:6], Func}};  // Bit_Extender bit_extender_1
  assign bit_extender_2_out = {{16{ID_IR[15]}}, {ID_IR[15:6], Func}};  // Bit_Extender bit_extender_2
  \重定向数据相关检测  \u_重定向数据相关检测_1  (
    .R1_num(R1_num), .MEM_WriteReg_num(multiplexer_4_out), .R2_num(R2_num),
    .EX_WriteReg_num(multiplexer_3_out), .isLW(or_2_out), .OP(ID_IR[31:26]), .FUNC(Func),
    .R1(\重定向数据相关检测_1_r1 ), .LoadUse(LoadUse), .R2(\重定向数据相关检测_1_r2 ), .MEM_RegWrite(MEM_RegWrite),
    .EX_RegWrite(EX_RegWrite));
  nand nand_1 (nand_1_out, d_ff_1_q, comparator_3_eq);
  Counter #(.width(13), .max('h1fff), .ongoal("stay"), .trigger("rising"), .behavior("old")) counter_2 (
    .count(comparator_3_lt), .Q(CNT_num), .clk(clock_2_out));  // open: load, D, carry, clr, preset
  MIPS_Regifile mips_regifile_1 (
    .Din(RDin), .Clk(CLK), .R1(mips_regifile_1_r1), .R2(mips_regifile_1_r2), .WE(RegWrite),
    .W_num(multiplexer_18_out), .R1_num(R1_num), .R2_num(R2_num));
  assign CLK = nand_1_out ? clock_2_out : 1'bz;  // Controlled_Buffer controlled_buffer_1
  Multiplexer #(.select(1), .width(32), .disabled("Z"), .enable("false")) multiplexer_7 (
    .in0(bit_extender_1_out), .in1(bit_extender_2_out), .out(multiplexer_7_out), .sel(SignedExt));
  Register #(.width(2), .trigger("rising"), .Select("low")) register_1 (
    .D(\重定向数据相关检测_1_r1 ), .Q(R1_trans), .clk(CLK));  // open: en, clr
  Register #(.width(2), .trigger("rising"), .Select("low")) register_2 (
    .D(\重定向数据相关检测_1_r2 ), .Q(R2_trans), .clk(CLK));  // open: en, clr
  Pull_Resistor #(.pull(1)) pull_resistor_1 (.node(CLK));
  // Probe on mips_regifile_1_r1
  // Probe on mips_regifile_1_r2
  Multiplexer #(.select(2), .width(32), .disabled("Z"), .enable("false")) multiplexer_8 (
    .in0(EX_B), .in1(MEM_AluResult), .in2(RDin), .in3(MEM_AluResult), .out(EX_B_mux), .sel(R2_trans));
  Shifter #(.width(32), .shift("ll")) shifter_1 (.in(EX_Imm), .\dist (5'b00010), .out(shifter_1_out));
  Adder #(.width(32)) adder_2 (.a(EX_PC), .b(32'h4), .out(adder_2_out));  // open: cin, cout
  or or_3 (Clear, EX_JMP, Branch);
  not not_1 (not_1_out, Clear);
  Multiplexer #(.select(2), .width(32), .disabled("Z"), .enable("false")) multiplexer_9 (
    .in0(EX_A), .in1(MEM_AluResult), .in2(RDin), .in3(MEM_AluResult), .out(EX_AluA), .sel(R1_trans));
  ID_EX id_ex_1 (
    .RedDst_in(\单周期硬布线控制器_1_regdst ), .AluSrcB_in(\单周期硬布线控制器_1_alu_src ), .Shamt_in(ID_IR[10:6]),
    .Syscall_in(\单周期硬布线控制器_1_syscall ), .RegWrite_in(\单周期硬布线控制器_1_regwrite ), .JMP_in(\单周期硬布线控制器_1_jmp ),
    .JAL_in(\单周期硬布线控制器_1_jal ), .AluOp_in(\单周期硬布线控制器_1_alu_op ), .JR_in(\单周期硬布线控制器_1_jr ),
    .MemWrite_in(\单周期硬布线控制器_1_memwrite ), .IR_in({ID_IR, Func}), .SLLV_in(\单周期硬布线控制器_1_sllv ), .PC_in(ID_PC),
    .Beq_in(\单周期硬布线控制器_1_beq ), .LUI_in(\单周期硬布线控制器_1_lui ), .Bne_in(\单周期硬布线控制器_1_bne ),
    .SB_in(\单周期硬布线控制器_1_sb ), .A_in(mips_regifile_1_r1), .MemToReg_in(\单周期硬布线控制器_1_memtoreg ),
    .BGTZ_in(\单周期硬布线控制器_1_bgtz ), .B_in(mips_regifile_1_r2), .Imm_in(multiplexer_7_out),
    .RedDst_out(EX_RegDst), .AluSrcB_out(id_ex_1_alusrcb_out), .Syscall_out(id_ex_1_syscall_out),
    .RegWrite_out(EX_RegWrite), .Shamt_out(EX_Shamt), .JMP_out(EX_JMP), .JAL_out(EX_JAL),
    .AluOp_out(id_ex_1_aluop_out), .JR_out(EX_JR), .MemWrite_out(id_ex_1_memwrite_out), .IR_out(EX_IR),
    .SLLV_out(EX_SLLV), .PC_out(EX_PC), .Beq_out(EX_Beq), .LUI_out(EX_LUI), .A_out(EX_A), .Bne_out(EX_Bne),
    .SB_out(id_ex_1_sb_out), .MemToReg_out(id_ex_1_memtoreg_out), .BGTZ_out(EX_BGTZ), .B_out(EX_B),
    .Imm_out(EX_Imm), .CLR(or_4_out), .CLK(CLK));  // open: PredictJMP_out, Stall, ERET_in, ERET_OUT, PredictJMP_in
  or or_4 (or_4_out, Clear, LoadUse, RST);
  assign INS = EX_JR ? EX_AluA : 32'bz;  // Controlled_Buffer controlled_buffer_2
  Adder #(.width(32)) adder_3 (.a(shifter_1_out), .b(adder_2_out), .out(adder_3_out));  // open: cin, cout
  and and_3 (and_3_out, EX_JMP, ~EX_JR);  // AND_Gate
  assign INS = and_3_out ? {EX_PC[31:28], EX_IR[25:0], 2'b00} : 32'bz;  // Controlled_Buffer controlled_buffer_3
  assign INS = not_1_out ? PC_4 : 32'bz;  // Controlled_Buffer controlled_buffer_4
  // Probe on EX_AluA
  // Probe on EX_B_mux
  Multiplexer #(.select(1), .width(32), .disabled("Z"), .enable("false")) multiplexer_10 (
    .in0(EX_B_mux), .in1(EX_Imm), .out(multiplexer_10_out), .sel(id_ex_1_alusrcb_out));
  assign INS = Branch ? adder_3_out : 32'bz;  // Controlled_Buffer controlled_buffer_5
  Multiplexer #(.select(1), .width(5), .disabled("Z"), .enable("false")) multiplexer_11 (
    .in0(EX_Shamt), .in1(EX_AluA[4:0]), .out(multiplexer_11_out), .sel(EX_SLLV));
  Comparator #(.width(32), .mode("twosComplement")) comparator_4 (
    .a(EX_AluA), .b({32{1'b0}}), .gt(comparator_4_gt));  // open: eq, lt
  MIPS_ALU mips_alu_1 (
    .X(EX_AluA), .Y(multiplexer_10_out), .AluOP(id_ex_1_aluop_out), .Equal(mips_alu_1_equal),
    .Result(mips_alu_1_result), .shamt(multiplexer_11_out));  // open: Result_2
  // Probe on mips_alu_1_result
  Multiplexer #(.select(1), .width(32), .disabled("Z"), .enable("false")) multiplexer_12 (
    .in0(mips_alu_1_result), .in1({EX_Imm[15:0], {16{1'b0}}}), .out(multiplexer_12_out), .sel(EX_LUI));
  and and_4 (and_4_out, EX_Beq, mips_alu_1_equal);
  and and_5 (and_5_out, EX_Bne, ~mips_alu_1_equal);  // AND_Gate
  and and_6 (and_6_out, comparator_4_gt, EX_BGTZ);
  or or_5 (Branch, and_4_out, and_5_out, and_6_out);
  Multiplexer #(.select(1), .width(32), .disabled("Z"), .enable("false")) multiplexer_13 (
    .in0(MDin), .in1(multiplexer_14_out), .out(multiplexer_13_out), .sel(MEM_SB));
  EX_MEM ex_mem_1 (
    .RedDst_in(EX_RegDst), .Syscall_in(id_ex_1_syscall_out), .RegWrite_in(EX_RegWrite), .JAL_in(EX_JAL),
    .AluResult_in(multiplexer_12_out), .MemWrite_in(id_ex_1_memwrite_out), .IR_in(EX_IR), .PC_in(EX_PC),
    .SB_in(id_ex_1_sb_out), .A_in(EX_AluA), .MemToReg_in(id_ex_1_memtoreg_out), .B_in(EX_B_mux),
    .RedDst_out(MEM_RegDst), .Syscall_out(ex_mem_1_syscall_out), .RegWrite_out(MEM_RegWrite),
    .JAL_out(MEM_JAL), .AluResult_out(MEM_AluResult), .MemWrite_out(MemWrite), .IR_out(MEM_IR),
    .PC_out(M_PC), .A_out(ex_mem_1_a_out), .SB_out(MEM_SB), .MemToReg_out(ex_mem_1_memtoreg_out),
    .B_out(MDin), .CLR(RST), .CLK(CLK));  // open: AluSrcB_in, Shamt_in, JMP_in, JR_in, SignedExt_in, SLLV_in, Beq_in, LUI_in, Bne_in, BGTZ_in, Imm_in, AluSrcB_out, Shamt_out, JMP_out, JR_out, SignedExt_out, SLLV_out, Beq_out, LUI_out, Bne_out, BGTZ_out, Imm_out, Stall, ERET_in, ERET_OUT
  Multiplexer #(.select(2), .width(32), .disabled("Z"), .enable("false")) multiplexer_14 (
    .in0({ram_1_data[31:16], ram_1_data_2, MDin[7:0]}),
    .in1({ram_1_data[31:16], MDin[7:0], ram_1_data[7:0]}),
    .in2({ram_1_data[31:24], MDin[7:0], ram_1_data_2, ram_1_data[7:0]}),
    .in3({MDin[7:0], ram_1_data[23:16], ram_1_data_2, ram_1_data[7:0]}), .out(multiplexer_14_out),
    .sel(MEM_AluResult[1:0]));
  RAM #(.addrWidth(10), .dataWidth(32), .bus("separate"), .Select("high")) ram_1 (
    .addr(MEM_AluResult[11:2]), .din(multiplexer_13_out),
    .data({ram_1_data[31:16], ram_1_data_2, ram_1_data[7:0]}), .str(MemWrite), .clk(CLK), .ld(1'b1));  // open: sel, clr
  MEM_WB mem_wb_1 (
    .RedDst_in(MEM_RegDst), .MemData_in({ram_1_data[31:16], ram_1_data_2, ram_1_data[7:0]}),
    .Syscall_in(ex_mem_1_syscall_out), .RegWrite_in(MEM_RegWrite), .JAL_in(MEM_JAL),
    .AluResult_in(MEM_AluResult), .IR_in(MEM_IR), .PC_in(M_PC), .A_in(ex_mem_1_a_out),
    .MemToReg_in(ex_mem_1_memtoreg_out), .B_in(MDin), .RedDst_out(mem_wb_1_reddst_out),
    .Syscall_out(mem_wb_1_syscall_out), .RegWrite_out(RegWrite), .MemData_out(mem_wb_1_memdata_out),
    .JAL_out(mem_wb_1_jal_out), .AluResult_out(mem_wb_1_aluresult_out), .IR_out(WB_IR), .PC_out(WB_PC),
    .A_out(mem_wb_1_a_out), .MemToReg_out(mem_wb_1_memtoreg_out), .B_out(mem_wb_1_b_out), .CLR(RST), .CLK(CLK));  // open: AluSrcB_in, JMP_in, JR_in, MemWrite_in, SignedExt_in, SLLV_in, Beq_in, LUI_in, Bne_in, SB_in, BGTZ_in, Imm_in, AluSrcB_out, JMP_out, JR_out, MemWrite_out, SignedExt_out, SLLV_out, Beq_out, Bne_out, SB_out, BGTZ_out, Imm_out, Stall, LUI_out, ERET_in, ERET_OUT
  Multiplexer #(.select(1), .width(32), .disabled("Z"), .enable("false")) multiplexer_15 (
    .in0(mem_wb_1_aluresult_out), .in1(mem_wb_1_memdata_out), .out(multiplexer_15_out),
    .sel(mem_wb_1_memtoreg_out));
  Adder #(.width(32)) adder_4 (.a(WB_PC), .b(32'h4), .out(adder_4_out));  // open: cin, cout
  Multiplexer #(.select(1), .width(5), .disabled("Z"), .enable("false")) multiplexer_16 (
    .in0(WB_IR[20:16]), .in1(WB_IR[15:11]), .out(multiplexer_16_out), .sel(mem_wb_1_reddst_out));
  Multiplexer #(.select(1), .width(32), .disabled("Z"), .enable("false")) multiplexer_17 (
    .in0(multiplexer_15_out), .in1(adder_4_out), .out(RDin), .sel(mem_wb_1_jal_out));
  Multiplexer #(.select(1), .width(5), .disabled("Z"), .enable("false")) multiplexer_18 (
    .in0(multiplexer_16_out), .in1({5{1'b1}}), .out(multiplexer_18_out), .sel(mem_wb_1_jal_out));
  Comparator #(.width(32), .mode("twosComplement")) comparator_5 (
    .a(32'h22), .b(mem_wb_1_b_out), .eq(comparator_5_eq));  // open: gt, lt
  and and_7 (and_7_out, comparator_5_eq, mem_wb_1_syscall_out);
  and and_8 (and_8_out, mem_wb_1_syscall_out, ~comparator_5_eq);  // AND_Gate
  Register #(.width(32), .trigger("rising"), .Select("low")) register_3 (
    .D(mem_wb_1_a_out), .en(and_7_out), .Q(LedData), .clk(CLK));  // open: clr
  Register #(.width(1), .trigger("rising"), .Select("low")) register_4 (
    .D(mem_wb_1_syscall_out), .en(and_8_out), .Q(register_4_q), .clk(CLK), .clr(Go));
  not not_2 (En, register_4_q);

  // Other names for the same wires on the sheet: ID_IR[5:0] = Func; OP[5:0] = ID_IR[31:26]; MEM_PC[31:0] = M_PC

  // Notes on the sheet:
  //   中断源
  //   时空图监测，可删除
  //   中断等待指示
  //   数码管输出
  //   contents of rom_1 (hex, n*v repeats v):
  //   20110001 8000c05 20110001 20120002 20130003 8000c09 20110001 20120002 20130003 8000c0d 20110001
  //   20120002 20130003 8000c11 20110001 20120002 20130003 c000cb8 20100001 20110001 118fc0 112020
  //   20020022 c 118882 12200001 8000c15 112020 20020022 c 20110001 118880 112020 20020022 c 12200001
  //   8000c1f 20110001 118fc0 112020 20020022 c 1188c3 112020 20020022 c 118903 112020 20020022 c 118903
  //   112020 20020022 c 118903 112020 20020022 c 118903 112020 20020022 c 118903 112020 20020022 c 118903
  //   112020 20020022 c 118903 112020 20020022 c 20100001 109fc0 139fc3 8021 2012000c 24160003 26100001
  //   3210000f 20080008 20090001 139900 2709825 132020 20020022 c 1094022 1500fff9 22100001 2018000f
  //   2188024 108700 20080008 20090001 139902 2709825 132021 20020022 c 1094022 1500fff9 108702 2c9b022
  //   12c00001 8000c50 4020 1084027 84400 3508ffff 82021 20020022 c 2010ffff 20110000 ae300000 22100001
  //   22310004 ae300000 22100001 22310004 ae300000 22100001 22310004 ae300000 22100001 22310004 ae300000
  //   22100001 22310004 ae300000 22100001 22310004 ae300000 22100001 22310004 ae300000 22100001 22310004
  //   ae300000 22100001 22310004 ae300000 22100001 22310004 ae300000 22100001 22310004 ae300000 22100001
  //   22310004 ae300000 22100001 22310004 ae300000 22100001 22310004 ae300000 22100001 22310004 ae300000
  //   22100001 22310004 22100001 8020 2011003c 8e130000 8e340000 274402a 11000002 ae330000 ae140000
  //   2231fffc 1611fff8 102020 20020022 c 22100004 2011003c 1611fff2 20020032 c 20100000 22100001 102020
  //   20020022 c 22100002 102020 20020022 c 22100003 102020 20020022 c 22100004 102020 20020022 c 22100005
  //   102020 20020022 c 22100006 102020 20020022 c 22100007 102020 20020022 c 22100008 102020 20020022
  //   20020022 c 3e00008
  //   rt
  //   rd
  //   rt
  //   rd
  //   rt
  //   rd
  //   控制位
  //   rs
  //   流水调试日志用
  //   暂停节拍，不能为0
  //   戳工具置1进入计数暂停模式，ctrl+k时钟自动运行到对应节拍暂停
  //   ctrl+k关闭时钟连续运行，将控制位置零，进入单步调试模式调试
  //   可计数暂停的时钟源
  //   为方便自动评测，需要输出流水线各段保存的PC值，注意是PC不是PC+4，另外ID段寄存器写入信息，Mem段内存写入信息也要输出
endmodule

module \中断按键参考电路  (
  input  \同步清零信号 ,
  output \与中断屏蔽位与 
);

  wire \_1号中断_out , and_1_out, clock_1_out, d_ff_1_q, or_1_out, or_2_out;

  Clock #(.highDuration(1), .lowDuration(1)) clock_1 (.out(clock_1_out));
  Button \_1号中断  (.out(\_1号中断_out ));
  or or_1 (or_1_out, \与中断屏蔽位与 , d_ff_1_q);
  LED #(.active("true")) \_1号中断等待指示灯  (.in(or_1_out));
  D_Flip_Flop #(.trigger("rising"), .Pre_Clr_Positions("LEGACY"), .NegatePresetClear("false"), .enable("true"), .NewFFLayout("false")) d_ff_1 (
    .clk(\_1号中断_out ), .D(1'b1), .Q(d_ff_1_q), .reset(\与中断屏蔽位与 ));  // open: Qn, preset, en
  or or_2 (or_2_out, d_ff_1_q, \与中断屏蔽位与 );
  and and_1 (and_1_out, or_2_out, ~\同步清零信号 );  // AND_Gate
  D_Flip_Flop #(.trigger("rising"), .Pre_Clr_Positions("LEGACY"), .NegatePresetClear("false"), .enable("true"), .NewFFLayout("false")) IR1 (
    .clk(clock_1_out), .D(and_1_out), .Q(\与中断屏蔽位与 ));  // open: Qn, preset, en, reset
  \单周期硬布线控制器  \u_单周期硬布线控制器_1  ();  // open: Func, OP, ALU_OP, MemToReg, MemWrite, ALU_SRC, RegWrite, SysCALL, SignedExt, RegDst, JR, JMP, Beq, JAL, Bne, SLLV, LUI, SB, BGTZ, in_3, MFC0, MTC0

  // Notes on the sheet:
  //   中断信号采样参考电路
  //   Reset 
endmodule

module \单周期MIPS_单级中断  (
  input  IR1,
  input  IR2,
  input  IR3,
  output RegWrite,
  output MemWrite,
  output [31:0] PC,
  output [31:0] IR,
  output [31:0] RDin,
  output [31:0] MDin,
  output [31:0] LedData
);

  wire and_1_out, and_2_out, and_3_out, and_4_out, and_5_out, and_6_out, and_7_out, and_8_out, CLK,
       clock_2_out, comparator_1_eq, comparator_2_eq, comparator_3_eq, comparator_4_eq, comparator_5_eq,
       comparator_5_lt, d_ff_1_q, decoder_1_out1, decoder_1_out2, decoder_1_out3, En, ERET, Go, IE_ctrl,
       IR1_2_q, IR1_3_q, IR1_q, IR1_t, ir1_t_t, IR2_t, ir2_t_t, IR3_t, ir3_t_t, IRA, IRB, IRC, JAL, JR, Led,
       mips_alu_1_equal, nand_1_out, or_1_out, or_5_out, or_9_out, or_10_out, or_11_out, or_12_out,
       priority_encoder_1_gs, register_2_q, register_3_q, Rst1, Rst2, Rst3, SignedExt, SYSCALL, W1, W2, W3,
       \单周期硬布线控制器_1_alu_src , \单周期硬布线控制器_1_beq , \单周期硬布线控制器_1_bne , \单周期硬布线控制器_1_jmp ,
       \单周期硬布线控制器_1_memtoreg , \单周期硬布线控制器_1_regdst ;
  wire [1:0] priority_encoder_1_out, register_4_q;
  wire [3:0] \单周期硬布线控制器_1_alu_op ;
  wire [4:0] multiplexer_6_out, multiplexer_7_out, multiplexer_8_out, multiplexer_9_out;
  wire [12:0] CNT_num;
  wire [15:0] \总周期数 ;
  wire [31:0] A, adder_1_out, adder_2_out, bit_extender_1_out, bit_extender_2_out, bit_extender_3_out, EPC,
       mips_alu_1_result, multiplexer_1_out, multiplexer_3_out, multiplexer_4_out, multiplexer_5_out,
       multiplexer_10_out, multiplexer_12_out, multiplexer_13_out, PC___4, ram_1_data, shifter_1_out,
       shifter_2_out, \中断入口地址 ;

  Clock #(.highDuration(1), .lowDuration(1)) clock_1 ();  // open: out
  Button _1 (.out(IRA));
  Button _2 (.out(IRB));
  Button _3 (.out(IRC));
  Button \u_继续运行  (.out(Go));
  LED #(.active("true")) led_1 (.in(W1));
  LED #(.active("true")) led_2 (.in(W2));
  LED #(.active("true")) led_3 (.in(W3));
  Multiplexer #(.select(1), .width(32), .disabled("Z"), .enable("false")) multiplexer_1 (
    .in0(adder_1_out), .in1(adder_2_out), .out(multiplexer_1_out), .sel(or_5_out));
  Hex_Digit_Display hex_digit_display_1 (.value(LedData[31:28]));  // open: dp
  Comparator #(.width(16), .mode("twosComplement")) comparator_1 (
    .a(16'h23b), .b(\总周期数 ), .eq(comparator_1_eq));  // open: gt, lt
  Comparator #(.width(16), .mode("twosComplement")) comparator_2 (
    .a(\总周期数 ), .b(16'h1), .eq(comparator_2_eq));  // open: gt, lt
  Comparator #(.width(16), .mode("twosComplement")) comparator_3 (
    .a(\总周期数 ), .b(16'h4), .eq(comparator_3_eq));  // open: gt, lt
  Comparator #(.width(16), .mode("twosComplement")) comparator_4 (
    .a(\总周期数 ), .b(16'h7), .eq(comparator_4_eq));  // open: gt, lt
  D_Flip_Flop #(.trigger("high"), .Pre_Clr_Positions("LEGACY"), .NegatePresetClear("false"), .enable("true"), .NewFFLayout("false")) d_ff_1 (.Q(d_ff_1_q));  // open: clk, D, Qn, preset, en, reset
  // Probe on 13'h368
  Multiplexer #(.select(1), .width(32), .disabled("Z"), .enable("false")) multiplexer_2 (
    .in0(multiplexer_1_out), .in1(multiplexer_5_out), .out(PC___4), .sel(\单周期硬布线控制器_1_jmp ));
  Multiplexer #(.select(1), .width(32), .disabled("Z"), .enable("false")) multiplexer_3 (
    .in0(PC___4), .in1(\中断入口地址 ), .out(multiplexer_3_out), .sel(IE_ctrl));
  Hex_Digit_Display hex_digit_display_2 (.value(LedData[23:20]));  // open: dp
  Hex_Digit_Display hex_digit_display_3 (.value(LedData[27:24]));  // open: dp
  or or_1 (or_1_out, comparator_1_eq, comparator_2_eq);
  assign IRA = or_1_out ? ~CLK : 1'bz;  // Controlled_Inverter controlled_inverter_1
  assign IRB = comparator_3_eq ? ~CLK : 1'bz;  // Controlled_Inverter controlled_inverter_2
  assign IRC = comparator_4_eq ? ~CLK : 1'bz;  // Controlled_Inverter controlled_inverter_3
  Comparator #(.width(13), .mode("twosComplement")) comparator_5 (
    .a(CNT_num), .b(13'h368), .eq(comparator_5_eq), .lt(comparator_5_lt));  // open: gt
  Clock #(.highDuration(1), .lowDuration(1)) clock_2 (.out(clock_2_out));
  Multiplexer #(.select(1), .width(32), .disabled("Z"), .enable("false")) multiplexer_4 (
    .in0(multiplexer_3_out), .in1(EPC), .out(multiplexer_4_out), .sel(ERET));
  Hex_Digit_Display hex_digit_display_4 (.value(LedData[19:16]));  // open: dp
  Hex_Digit_Display hex_digit_display_5 (.value(LedData[15:12]));  // open: dp
  Pull_Resistor #(.pull(0)) pull_resistor_1 (.node(IRA));
  Pull_Resistor #(.pull(0)) pull_resistor_2 (.node(IRB));
  Pull_Resistor #(.pull(0)) pull_resistor_3 (.node(IRC));
  Counter #(.width(13), .max('h1fff), .ongoal("stay"), .trigger("rising"), .behavior("old")) counter_1 (
    .count(comparator_5_lt), .Q(CNT_num), .clk(clock_2_out));  // open: load, D, carry, clr, preset
  Register #(.width(32), .trigger("rising"), .Select("low")) u_PC (
    .D(multiplexer_4_out), .en(En), .Q(PC), .clk(CLK));  // open: clr
  Hex_Digit_Display hex_digit_display_6 (.value(LedData[11:8]));  // open: dp
  Hex_Digit_Display hex_digit_display_7 (.value(LedData[7:4]));  // open: dp
  // Probe on \总周期数 
  nand nand_1 (nand_1_out, d_ff_1_q, comparator_5_eq);
  Multiplexer #(.select(1), .width(32), .disabled("Z"), .enable("false")) multiplexer_5 (
    .in0(shifter_1_out), .in1(A), .out(multiplexer_5_out), .sel(JR));
  Hex_Digit_Display hex_digit_display_8 (.value(LedData[3:0]));  // open: dp
  assign CLK = nand_1_out ? clock_2_out : 1'bz;  // Controlled_Buffer controlled_buffer_1
  Pull_Resistor #(.pull(1)) pull_resistor_4 (.node(CLK));
  Adder #(.width(32)) adder_1 (.a(PC), .b(32'h4), .out(adder_1_out));  // open: cin, cout
  ROM #(.addrWidth(10), .dataWidth(32), .Select("high")) rom_1 (.addr(PC[11:2]), .data(IR));
  or or_2 (IR1_t, IR1, IRA);
  // Mips_Probe mips_probe_1: pin names not known; wires that end beside it: IR
  or or_3 (IR2_t, IR2, IRB);
  Multiplexer #(.select(1), .width(5), .disabled("Z"), .enable("false")) multiplexer_6 (
    .in0(IR[20:16]), .in1(IR[15:11]), .out(multiplexer_6_out), .sel(\单周期硬布线控制器_1_regdst ));
  Multiplexer #(.select(1), .width(5), .disabled("Z"), .enable("false")) multiplexer_7 (
    .in0(IR[25:21]), .in1(5'b00100), .out(multiplexer_7_out), .sel(SYSCALL));
  Multiplexer #(.select(1), .width(5), .disabled("Z"), .enable("false")) multiplexer_8 (
    .in0(IR[20:16]), .in1(5'b00010), .out(multiplexer_8_out), .sel(SYSCALL));
  Multiplexer #(.select(1), .width(5), .disabled("Z"), .enable("false")) multiplexer_9 (
    .in0(multiplexer_6_out), .in1({5{1'b1}}), .out(multiplexer_9_out), .sel(JAL));
  assign bit_extender_1_out = {{16{1'b0}}, IR[15:0]};  // Bit_Extender bit_extender_1
  assign bit_extender_2_out = {{16{IR[15]}}, IR[15:0]};  // Bit_Extender bit_extender_2
  assign bit_extender_3_out = {{6{IR[25]}}, IR[25:0]};  // Bit_Extender bit_extender_3
  or or_4 (IR3_t, IR3, IRC);
  \单周期硬布线控制器  \u_单周期硬布线控制器_1  (
    .Func(IR[5:0]), .OP(IR[31:26]), .ALU_OP(\单周期硬布线控制器_1_alu_op ), .MemToReg(\单周期硬布线控制器_1_memtoreg ),
    .MemWrite(MemWrite), .ALU_SRC(\单周期硬布线控制器_1_alu_src ), .RegWrite(RegWrite), .SysCALL(SYSCALL),
    .SignedExt(SignedExt), .RegDst(\单周期硬布线控制器_1_regdst ), .JR(JR), .JMP(\单周期硬布线控制器_1_jmp ),
    .Beq(\单周期硬布线控制器_1_beq ), .JAL(JAL), .Bne(\单周期硬布线控制器_1_bne ));  // open: SLLV, LUI, SB, BGTZ, in_3, MFC0, MTC0
  Multiplexer #(.select(1), .width(32), .disabled("Z"), .enable("false")) multiplexer_10 (
    .in0(bit_extender_1_out), .in1(bit_extender_2_out), .out(multiplexer_10_out), .sel(SignedExt));
  Multiplexer #(.select(1), .width(32), .disabled("Z"), .enable("false")) multiplexer_11 (
    .in0(multiplexer_13_out), .in1(adder_1_out), .out(RDin), .sel(JAL));
  Shifter #(.width(32), .shift("ll")) shifter_1 (.in(bit_extender_3_out), .\dist (5'b00010), .out(shifter_1_out));
  and and_1 (and_1_out, Led, SYSCALL);
  Register #(.width(32), .trigger("rising"), .Select("low")) register_1 (
    .D(A), .en(and_1_out), .Q(LedData), .clk(CLK));  // open: clr
  and and_2 (and_2_out, \单周期硬布线控制器_1_beq , mips_alu_1_equal);
  MIPS_Regifile mips_regifile_1 (
    .Din(RDin), .Clk(CLK), .R1(A), .R2(MDin), .WE(RegWrite), .W_num(multiplexer_9_out),
    .R1_num(multiplexer_7_out), .R2_num(multiplexer_8_out));
  and and_3 (and_3_out, \单周期硬布线控制器_1_bne , ~mips_alu_1_equal);  // AND_Gate
  Multiplexer #(.select(1), .width(32), .disabled("Z"), .enable("false")) multiplexer_12 (
    .in0(MDin), .in1(multiplexer_10_out), .out(multiplexer_12_out), .sel(\单周期硬布线控制器_1_alu_src ));
  and and_4 (and_4_out, CLK, En);
  or or_5 (or_5_out, and_2_out, and_3_out);
  Comparator #(.width(32), .mode("twosComplement")) comparator_6 (.a(32'h22), .b(MDin), .eq(Led));  // open: gt, lt
  Shifter #(.width(32), .shift("ll")) shifter_2 (.in(multiplexer_10_out), .\dist (5'b00010), .out(shifter_2_out));
  Counter #(.width(16), .max('hffff), .ongoal("wrap"), .trigger("rising"), .behavior("new")) counter_2 (
    .Q(\总周期数 ), .clk(and_4_out));  // open: load, D, count, carry, clr, preset, down
  MIPS_ALU mips_alu_1 (
    .X(A), .Y(multiplexer_12_out), .AluOP(\单周期硬布线控制器_1_alu_op ), .Equal(mips_alu_1_equal),
    .Result(mips_alu_1_result), .shamt(IR[10:6]));  // open: Result_2
  Adder #(.width(32)) adder_2 (.a(shifter_2_out), .b(adder_1_out), .out(adder_2_out));  // open: cin, cout
  and and_5 (and_5_out, SYSCALL, ~Led);  // AND_Gate
  Register #(.width(1), .trigger("rising"), .Select("low")) register_2 (
    .D(SYSCALL), .en(and_5_out), .Q(register_2_q), .clk(CLK), .clr(Go));
  Multiplexer #(.select(1), .width(32), .disabled("Z"), .enable("false")) multiplexer_13 (
    .in0(mips_alu_1_result), .in1(ram_1_data), .out(multiplexer_13_out), .sel(\单周期硬布线控制器_1_memtoreg ));
  RAM #(.addrWidth(10), .dataWidth(32), .bus("separate"), .Select("high")) ram_1 (
    .addr(mips_alu_1_result[11:2]), .din(MDin), .data(ram_1_data), .str(MemWrite), .sel(En), .clk(CLK),
    .ld(1'b1));  // open: clr
  not not_1 (En, register_2_q);
  D_Flip_Flop #(.trigger("rising"), .Pre_Clr_Positions("LEGACY"), .NegatePresetClear("false"), .enable("true"), .NewFFLayout("false")) u_IR1 (
    .clk(IRA), .D(1'b1), .Q(IR1_q), .reset(ir1_t_t));  // open: Qn, preset, en
  or or_6 (W1, ir1_t_t, IR1_q);
  or or_7 (W2, ir2_t_t, IR1_3_q);
  D_Flip_Flop #(.trigger("rising"), .Pre_Clr_Positions("LEGACY"), .NegatePresetClear("false"), .enable("true"), .NewFFLayout("false")) IR1_2 (
    .clk(IRC), .D(1'b1), .Q(IR1_2_q), .reset(ir3_t_t));  // open: Qn, preset, en
  or or_8 (W3, ir3_t_t, IR1_2_q);
  Comparator #(.width(32), .mode("twosComplement")) comparator_7 (.a(IR), .b(32'h42000018), .eq(ERET));  // open: gt, lt
  or or_9 (or_9_out, IR1_q, ir1_t_t);
  D_Flip_Flop #(.trigger("rising"), .Pre_Clr_Positions("LEGACY"), .NegatePresetClear("false"), .enable("true"), .NewFFLayout("false")) IR1_3 (
    .clk(IRB), .D(1'b1), .Q(IR1_3_q), .reset(ir2_t_t));  // open: Qn, preset, en
  or or_10 (or_10_out, IR1_2_q, ir3_t_t);
  and and_6 (and_6_out, or_9_out, ~Rst1);  // AND_Gate
  or or_11 (or_11_out, IR1_3_q, ir2_t_t);
  and and_7 (and_7_out, or_11_out, ~Rst2);  // AND_Gate
  and and_8 (and_8_out, or_10_out, ~Rst3);  // AND_Gate
  D_Flip_Flop #(.trigger("rising"), .Pre_Clr_Positions("LEGACY"), .NegatePresetClear("false"), .enable("true"), .NewFFLayout("false")) IR1_4 (
    .clk(CLK), .D(and_6_out), .Q(ir1_t_t));  // open: Qn, preset, en, reset
  D_Flip_Flop #(.trigger("rising"), .Pre_Clr_Positions("LEGACY"), .NegatePresetClear("false"), .enable("true"), .NewFFLayout("false")) IR1_5 (
    .clk(CLK), .D(and_7_out), .Q(ir2_t_t));  // open: Qn, preset, en, reset
  D_Flip_Flop #(.trigger("rising"), .Pre_Clr_Positions("LEGACY"), .NegatePresetClear("false"), .enable("true"), .NewFFLayout("false")) IR1_6 (
    .clk(CLK), .D(and_8_out), .Q(ir3_t_t));  // open: Qn, preset, en, reset
  or or_12 (or_12_out, ERET, IE_ctrl);
  Priority_Encoder #(.select(2), .disabled("Z")) priority_encoder_1 (
    .in0(1'b0), .in1(ir1_t_t), .in2(ir2_t_t), .in3(ir3_t_t), .out(priority_encoder_1_out),
    .gs(priority_encoder_1_gs));  // open: en_out, en_in
  Multiplexer #(.select(2), .width(32), .disabled("Z"), .enable("false")) multiplexer_14 (
    .in1(32'h30ac), .in2(32'h3150), .in3(32'h31f4), .out(\中断入口地址 ), .sel(priority_encoder_1_out));  // open: in0
  Register #(.width(1), .trigger("rising"), .Select("low")) register_3 (
    .D(IE_ctrl), .en(or_12_out), .Q(register_3_q), .clk(CLK));  // open: clr
  and and_9 (IE_ctrl, priority_encoder_1_gs, ~register_3_q);  // AND_Gate
  Register #(.width(2), .trigger("rising"), .Select("low")) register_4 (
    .D(priority_encoder_1_out), .en(IE_ctrl), .Q(register_4_q), .clk(CLK));  // open: clr
  Decoder #(.select(2), .tristate("false"), .disabled("Z"), .enable("false")) decoder_1 (
    .out1(decoder_1_out1), .out2(decoder_1_out2), .out3(decoder_1_out3), .sel(register_4_q));  // open: out0
  Register #(.width(32), .trigger("rising"), .Select("low")) register_5 (
    .D(PC___4), .en(IE_ctrl), .Q(EPC), .clk(CLK));  // open: clr
  and and_10 (Rst1, decoder_1_out1, ERET);
  and and_11 (Rst2, decoder_1_out2, ERET);
  and and_12 (Rst3, decoder_1_out3, ERET);

  // Notes on the sheet:
  //   中断源
  //   中断等待指示
  //   总复位信号应将除ROM以外所有存储组件全部清零
  //   单级中断测试信号模拟器
  //   控制位
  //   暂停节拍，不能为0
  //   戳工具置1进入计数暂停模式，ctrl+k时钟自动运行到对应节拍暂停
  //   ctrl+k关闭时钟连续运行，将控制位置零，进入单步调试模式调试
  //   用这个时钟源需要去掉电路中的其他时钟源
  //   数码管输出
  //   数码管输出应该用寄存器锁存，否则显示数据只能一闪而过
  //   可计数暂停的时钟源
  //   指令存储器
  //   contents of rom_1 (hex, n*v repeats v):
  //   201d07d0 20100001 109fc0 139fc3 8021 2012000c 24160008 26100001 3210000f 20080008 20090001 139900
  //   2709825 132020 20020022 c 1094022 1500fff9 22100001 2018000f 2188024 108700 20080008 20090001 139902
  //   2709825 132021 20020022 c 1094022 1500fff9 108702 2c9b022 12c00001 8000c07 4020 1084027 84400
  //   3508ffff 82021 20020022 c 8000c01 afa20000 23bd0004 afa40000 23bd0004 afb00000 23bd0004 afb30000
  //   23bd0004 afb40000 23bd0004 afb50000 23bd0004 afb60000 23bd0004 20160001 20140003 20150001 168020
  //   108100 2149825 132020 20020022 c 1600fffa 295a022 1680fff7 23bdfffc 8fb60000 23bdfffc 8fb50000
  //   23bdfffc 8fb40000 23bdfffc 8fb30000 23bdfffc 8fb00000 23bdfffc 8fa40000 23bdfffc 8fa20000 42000018
  //   afa20000 23bd0004 afa40000 23bd0004 afb00000 23bd0004 afb30000 23bd0004 afb40000 23bd0004 afb50000
  //   23bd0004 afb60000 23bd0004 20160002 20140003 20150001 168020 108100 2149825 132020 20020022 c
  //   1600fffa 295a022 1680fff7 23bdfffc 8fb60000 23bdfffc 8fb50000 23bdfffc 8fb40000 23bdfffc 8fb30000
  //   23bdfffc 8fb00000 23bdfffc 8fa40000 23bdfffc 8fa20000 42000018 afa20000 23bd0004 afa40000 23bd0004
  //   afb00000 23bd0004 afb30000 23bd0004 afb40000 23bd0004 afb50000 23bd0004 afb60000 23bd0004 20160003
  //   20140003 20150001 168020 108100 2149825 132020 20020022 c 1600fffa 295a022 1680fff7 23bdfffc
  //   8fb60000 23bdfffc 8fb50000 23bdfffc 8fb40000 23bdfffc 8fb30000 23bdfffc 8fb00000 23bdfffc 8fa40000
  //   23bdfffc 8fa20000 42000018
  //   OP
  //   Func
  //   rs
  //   指令字
  //   rt
  //   rd
  //   JMP
  //   JR
  //   OP
  //   Func
  //   Beq
  //   Bne
  //   MemToReg
  //   MemWrite
  //   AluOP
  //   AluSrcB
  //   RegWrite
  //   JAL
  //   RegDst
  //   Syscall
  //   为方便自动评测，需要输出PC，IR，寄存器堆写如数据RDin
  //   RAM写使能MemWrite、RAM写入数据MDin等信号
endmodule

module \单周期MIPS_多级中断  (
  input  IR1,
  input  IR2,
  input  IR3,
  output RegWrite,
  output MemWrite,
  output [31:0] PC,
  output [31:0] IR,
  output [31:0] RDin,
  output [31:0] MDin,
  output [31:0] LedData
);

  wire and_1_out, and_2_out, and_3_out, and_4_out, and_5_out, and_6_out, and_7_out, and_8_out, CLK,
       clock_2_out, comparator_1_eq, comparator_2_eq, comparator_3_eq, comparator_4_eq, comparator_5_eq,
       comparator_6_eq, comparator_6_lt, comparator_9_gt, d_ff_1_q, decoder_1_out1, decoder_1_out2,
       decoder_1_out3, En, ERET, Go, IE_ctrl, IR1_2_q, IR1_3_q, IR1_q, IR1_t, ir1_t_t, IR2_t, ir2_t_t, IR3_t,
       ir3_t_t, IRA, IRB, IRC, JAL, JR, Led, MFC0, mips_alu_1_equal, MTC0, nand_1_out, or_1_out, or_2_out,
       or_6_out, or_7_out, or_11_out, or_12_out, or_13_out, or_14_out, or_15_out, or_16_out,
       priority_encoder_1_gs, register_2_q, register_3_q, Rst1, Rst2, Rst3, SignedExt, SYSCALL, W1, W2, W3,
       \单周期硬布线控制器_1_alu_src , \单周期硬布线控制器_1_beq , \单周期硬布线控制器_1_bne , \单周期硬布线控制器_1_jmp ,
       \单周期硬布线控制器_1_memtoreg , \单周期硬布线控制器_1_regdst ;
  wire [1:0] multiplexer_15_out, multiplexer_17_out, multiplexer_19_out, register_6_q, register_8_q, \当前中断号 ,
       \最优中断号 ;
  wire [3:0] \单周期硬布线控制器_1_alu_op ;
  wire [4:0] multiplexer_6_out, multiplexer_7_out, multiplexer_8_out, multiplexer_9_out;
  wire [12:0] CNT_num;
  wire [15:0] \总周期数 ;
  wire [31:0] A, adder_1_out, adder_2_out, bit_extender_1_out, bit_extender_2_out, bit_extender_3_out, EPC,
       mips_alu_1_result, multiplexer_1_out, multiplexer_3_out, multiplexer_4_out, multiplexer_5_out,
       multiplexer_10_out, multiplexer_12_out, multiplexer_13_out, multiplexer_16_out, multiplexer_18_out,
       multiplexer_20_out, PC_4, ram_1_data, register_7_q, register_9_q, shifter_1_out, shifter_2_out,
       \中断入口地址 ;

  Clock #(.highDuration(1), .lowDuration(1)) clock_1 ();  // open: out
  Button _1 (.out(IRA));
  Button _2 (.out(IRB));
  Button _3 (.out(IRC));
  Button \u_继续运行  (.out(Go));
  LED #(.active("true")) led_1 (.in(W1));
  LED #(.active("true")) led_2 (.in(W2));
  LED #(.active("true")) led_3 (.in(W3));
  Multiplexer #(.select(1), .width(32), .disabled("Z"), .enable("false")) multiplexer_1 (
    .in0(adder_1_out), .in1(adder_2_out), .out(multiplexer_1_out), .sel(or_6_out));
  Hex_Digit_Display hex_digit_display_1 (.value(LedData[31:28]));  // open: dp
  Comparator #(.width(16), .mode("twosComplement")) comparator_1 (
    .a(16'h258), .b(\总周期数 ), .eq(comparator_1_eq));  // open: gt, lt
  Comparator #(.width(16), .mode("twosComplement")) comparator_2 (
    .a(\总周期数 ), .b(16'h1), .eq(comparator_2_eq));  // open: gt, lt
  Comparator #(.width(16), .mode("twosComplement")) comparator_3 (
    .a(\总周期数 ), .b(16'h4), .eq(comparator_3_eq));  // open: gt, lt
  Comparator #(.width(16), .mode("twosComplement")) comparator_4 (
    .a(\总周期数 ), .b(16'h7), .eq(comparator_4_eq));  // open: gt, lt
  Comparator #(.width(16), .mode("twosComplement")) comparator_5 (
    .a(\总周期数 ), .b(16'h241), .eq(comparator_5_eq));  // open: gt, lt
  D_Flip_Flop #(.trigger("high"), .Pre_Clr_Positions("LEGACY"), .NegatePresetClear("false"), .enable("true"), .NewFFLayout("false")) d_ff_1 (.Q(d_ff_1_q));  // open: clk, D, Qn, preset, en, reset
  // Probe on 13'h13
  Multiplexer #(.select(1), .width(32), .disabled("Z"), .enable("false")) multiplexer_2 (
    .in0(multiplexer_1_out), .in1(multiplexer_5_out), .out(PC_4), .sel(\单周期硬布线控制器_1_jmp ));
  Multiplexer #(.select(1), .width(32), .disabled("Z"), .enable("false")) multiplexer_3 (
    .in0(PC_4), .in1(\中断入口地址 ), .out(multiplexer_3_out), .sel(IE_ctrl));
  Hex_Digit_Display hex_digit_display_2 (.value(LedData[23:20]));  // open: dp
  Hex_Digit_Display hex_digit_display_3 (.value(LedData[27:24]));  // open: dp
  or or_1 (or_1_out, comparator_1_eq, comparator_2_eq);
  assign IRA = or_1_out ? ~CLK : 1'bz;  // Controlled_Inverter controlled_inverter_1
  assign IRB = comparator_3_eq ? ~CLK : 1'bz;  // Controlled_Inverter controlled_inverter_2
  or or_2 (or_2_out, comparator_4_eq, comparator_5_eq);
  assign IRC = or_2_out ? ~CLK : 1'bz;  // Controlled_Inverter controlled_inverter_3
  Comparator #(.width(13), .mode("twosComplement")) comparator_6 (
    .a(CNT_num), .b(13'h13), .eq(comparator_6_eq), .lt(comparator_6_lt));  // open: gt
  Clock #(.highDuration(1), .lowDuration(1)) clock_2 (.out(clock_2_out));
  Multiplexer #(.select(1), .width(32), .disabled("Z"), .enable("false")) multiplexer_4 (
    .in0(multiplexer_3_out), .in1(EPC), .out(multiplexer_4_out), .sel(ERET));
  Hex_Digit_Display hex_digit_display_4 (.value(LedData[19:16]));  // open: dp
  Hex_Digit_Display hex_digit_display_5 (.value(LedData[15:12]));  // open: dp
  Pull_Resistor #(.pull(0)) pull_resistor_1 (.node(IRA));
  Pull_Resistor #(.pull(0)) pull_resistor_2 (.node(IRB));
  Pull_Resistor #(.pull(0)) pull_resistor_3 (.node(IRC));
  Counter #(.width(13), .max('h1fff), .ongoal("stay"), .trigger("rising"), .behavior("old")) counter_1 (
    .count(comparator_6_lt), .Q(CNT_num), .clk(clock_2_out));  // open: load, D, carry, clr, preset
  Register #(.width(32), .trigger("rising"), .Select("low")) u_PC (
    .D(multiplexer_4_out), .en(En), .Q(PC), .clk(CLK));  // open: clr
  Hex_Digit_Display hex_digit_display_6 (.value(LedData[11:8]));  // open: dp
  Hex_Digit_Display hex_digit_display_7 (.value(LedData[7:4]));  // open: dp
  // Probe on \总周期数 
  nand nand_1 (nand_1_out, d_ff_1_q, comparator_6_eq);
  Multiplexer #(.select(1), .width(32), .disabled("Z"), .enable("false")) multiplexer_5 (
    .in0(shifter_1_out), .in1(A), .out(multiplexer_5_out), .sel(JR));
  Hex_Digit_Display hex_digit_display_8 (.value(LedData[3:0]));  // open: dp
  assign CLK = nand_1_out ? clock_2_out : 1'bz;  // Controlled_Buffer controlled_buffer_1
  Pull_Resistor #(.pull(1)) pull_resistor_4 (.node(CLK));
  Adder #(.width(32)) adder_1 (.a(PC), .b(32'h4), .out(adder_1_out));  // open: cin, cout
  ROM #(.addrWidth(10), .dataWidth(32), .Select("high")) rom_1 (.addr(PC[11:2]), .data(IR));
  or or_3 (IR1_t, IR1, IRA);
  // Mips_Probe mips_probe_1: pin names not known; wires that end beside it: IR
  or or_4 (IR2_t, IR2, IRB);
  Multiplexer #(.select(1), .width(5), .disabled("Z"), .enable("false")) multiplexer_6 (
    .in0(IR[20:16]), .in1(IR[15:11]), .out(multiplexer_6_out), .sel(\单周期硬布线控制器_1_regdst ));
  Multiplexer #(.select(1), .width(5), .disabled("Z"), .enable("false")) multiplexer_7 (
    .in0(IR[25:21]), .in1(5'b00100), .out(multiplexer_7_out), .sel(SYSCALL));
  Multiplexer #(.select(1), .width(5), .disabled("Z"), .enable("false")) multiplexer_8 (
    .in0(IR[20:16]), .in1(5'b00010), .out(multiplexer_8_out), .sel(SYSCALL));
  Multiplexer #(.select(1), .width(5), .disabled("Z"), .enable("false")) multiplexer_9 (
    .in0(multiplexer_6_out), .in1({5{1'b1}}), .out(multiplexer_9_out), .sel(JAL));
  assign bit_extender_1_out = {{16{1'b0}}, IR[15:0]};  // Bit_Extender bit_extender_1
  assign bit_extender_2_out = {{16{IR[15]}}, IR[15:0]};  // Bit_Extender bit_extender_2
  assign bit_extender_3_out = {{6{IR[25]}}, IR[25:0]};  // Bit_Extender bit_extender_3
  or or_5 (IR3_t, IR3, IRC);
  \单周期硬布线控制器  \u_单周期硬布线控制器_1  (
    .Func(IR[5:0]), .OP(IR[31:26]), .ALU_OP(\单周期硬布线控制器_1_alu_op ), .MemToReg(\单周期硬布线控制器_1_memtoreg ),
    .MemWrite(MemWrite), .ALU_SRC(\单周期硬布线控制器_1_alu_src ), .RegWrite(RegWrite), .SysCALL(SYSCALL),
    .SignedExt(SignedExt), .RegDst(\单周期硬布线控制器_1_regdst ), .JR(JR), .JMP(\单周期硬布线控制器_1_jmp ),
    .Beq(\单周期硬布线控制器_1_beq ), .JAL(JAL), .Bne(\单周期硬布线控制器_1_bne ), .in_3(IR[25:21]), .MFC0(MFC0), .MTC0(MTC0));  // open: SLLV, LUI, SB, BGTZ
  Multiplexer #(.select(1), .width(32), .disabled("Z"), .enable("false")) multiplexer_10 (
    .in0(bit_extender_1_out), .in1(bit_extender_2_out), .out(multiplexer_10_out), .sel(SignedExt));
  Multiplexer #(.select(1), .width(32), .disabled("Z"), .enable("false")) multiplexer_11 (
    .in0(multiplexer_13_out), .in1(adder_1_out), .out(RDin), .sel(JAL));
  Shifter #(.width(32), .shift("ll")) shifter_1 (.in(bit_extender_3_out), .\dist (5'b00010), .out(shifter_1_out));
  and and_1 (and_1_out, Led, SYSCALL);
  Register #(.width(32), .trigger("rising"), .Select("low")) register_1 (
    .D(A), .en(and_1_out), .Q(LedData), .clk(CLK));  // open: clr
  and and_2 (and_2_out, \单周期硬布线控制器_1_beq , mips_alu_1_equal);
  MIPS_Regifile mips_regifile_1 (
    .Din(RDin), .Clk(CLK), .R1(A), .R2(MDin), .WE(RegWrite), .W_num(multiplexer_9_out),
    .R1_num(multiplexer_7_out), .R2_num(multiplexer_8_out));
  and and_3 (and_3_out, \单周期硬布线控制器_1_bne , ~mips_alu_1_equal);  // AND_Gate
  Multiplexer #(.select(1), .width(32), .disabled("Z"), .enable("false")) multiplexer_12 (
    .in0(MDin), .in1(multiplexer_10_out), .out(multiplexer_12_out), .sel(\单周期硬布线控制器_1_alu_src ));
  and and_4 (and_4_out, CLK, En);
  or or_6 (or_6_out, and_2_out, and_3_out);
  Comparator #(.width(32), .mode("twosComplement")) comparator_7 (.a(32'h22), .b(MDin), .eq(Led));  // open: gt, lt
  Shifter #(.width(32), .shift("ll")) shifter_2 (.in(multiplexer_10_out), .\dist (5'b00010), .out(shifter_2_out));
  Counter #(.width(16), .max('hffff), .ongoal("wrap"), .trigger("rising"), .behavior("new")) counter_2 (
    .Q(\总周期数 ), .clk(and_4_out));  // open: load, D, count, carry, clr, preset, down
  MIPS_ALU mips_alu_1 (
    .X(A), .Y(multiplexer_12_out), .AluOP(\单周期硬布线控制器_1_alu_op ), .Equal(mips_alu_1_equal),
    .Result(mips_alu_1_result), .shamt(IR[10:6]));  // open: Result_2
  Adder #(.width(32)) adder_2 (.a(shifter_2_out), .b(adder_1_out), .out(adder_2_out));  // open: cin, cout
  and and_5 (and_5_out, SYSCALL, ~Led);  // AND_Gate
  Register #(.width(1), .trigger("rising"), .Select("low")) register_2 (
    .D(SYSCALL), .en(and_5_out), .Q(register_2_q), .clk(CLK), .clr(Go));
  Multiplexer #(.select(1), .width(32), .disabled("Z"), .enable("false")) multiplexer_13 (
    .in0(mips_alu_1_result), .in1(ram_1_data), .out(multiplexer_13_out), .sel(\单周期硬布线控制器_1_memtoreg ));
  RAM #(.addrWidth(10), .dataWidth(32), .bus("separate"), .Select("high")) ram_1 (
    .addr(mips_alu_1_result[11:2]), .din(MDin), .data(ram_1_data), .str(MemWrite), .sel(En), .clk(CLK),
    .ld(1'b1));  // open: clr
  not not_1 (En, register_2_q);
  Comparator #(.width(32), .mode("twosComplement")) comparator_8 (.a(IR), .b(32'h42000018), .eq(ERET));  // open: gt, lt
  or or_7 (or_7_out, ERET, MFC0, MTC0, IE_ctrl);
  Comparator #(.width(2), .mode("unsigned")) comparator_9 (
    .a(\最优中断号 ), .b(\当前中断号 ), .gt(comparator_9_gt));  // open: eq, lt
  D_Flip_Flop #(.trigger("rising"), .Pre_Clr_Positions("LEGACY"), .NegatePresetClear("false"), .enable("true"), .NewFFLayout("false")) u_IR1 (
    .clk(IRA), .D(1'b1), .Q(IR1_q), .reset(ir1_t_t));  // open: Qn, preset, en
  or or_8 (W1, ir1_t_t, IR1_q);
  or or_9 (W2, ir2_t_t, IR1_3_q);
  D_Flip_Flop #(.trigger("rising"), .Pre_Clr_Positions("LEGACY"), .NegatePresetClear("false"), .enable("true"), .NewFFLayout("false")) IR1_2 (
    .clk(IRC), .D(1'b1), .Q(IR1_2_q), .reset(ir3_t_t));  // open: Qn, preset, en
  or or_10 (W3, ir3_t_t, IR1_2_q);
  or or_11 (or_11_out, MTC0, IE_ctrl);
  // Probe on \总周期数 
  or or_12 (or_12_out, IR1_q, ir1_t_t);
  D_Flip_Flop #(.trigger("rising"), .Pre_Clr_Positions("LEGACY"), .NegatePresetClear("false"), .enable("true"), .NewFFLayout("false")) IR1_3 (
    .clk(IRB), .D(1'b1), .Q(IR1_3_q), .reset(ir2_t_t));  // open: Qn, preset, en
  or or_13 (or_13_out, IR1_2_q, ir3_t_t);
  Register #(.width(1), .trigger("rising"), .Select("low")) register_3 (
    .D(or_11_out), .en(or_7_out), .Q(register_3_q), .clk(CLK));  // open: clr
  and and_6 (and_6_out, or_12_out, ~Rst1);  // AND_Gate
  or or_14 (or_14_out, IR1_3_q, ir2_t_t);
  and and_7 (and_7_out, or_14_out, ~Rst2);  // AND_Gate
  and and_8 (and_8_out, or_13_out, ~Rst3);  // AND_Gate
  and and_9 (IE_ctrl, ~register_3_q, comparator_9_gt);  // AND_Gate
  D_Flip_Flop #(.trigger("rising"), .Pre_Clr_Positions("LEGACY"), .NegatePresetClear("false"), .enable("true"), .NewFFLayout("false")) IR1_4 (
    .clk(CLK), .D(and_6_out), .Q(ir1_t_t));  // open: Qn, preset, en, reset
  D_Flip_Flop #(.trigger("rising"), .Pre_Clr_Positions("LEGACY"), .NegatePresetClear("false"), .enable("true"), .NewFFLayout("false")) u_IR2 (
    .clk(CLK), .D(and_7_out), .Q(ir2_t_t));  // open: Qn, preset, en, reset
  D_Flip_Flop #(.trigger("rising"), .Pre_Clr_Positions("LEGACY"), .NegatePresetClear("false"), .enable("true"), .NewFFLayout("false")) u_IR3 (
    .clk(CLK), .D(and_8_out), .Q(ir3_t_t));  // open: Qn, preset, en, reset
  Priority_Encoder #(.select(2), .disabled("Z")) priority_encoder_1 (
    .in0(1'b1), .in1(ir1_t_t), .in2(ir2_t_t), .in3(ir3_t_t), .out(\最优中断号 ), .gs(priority_encoder_1_gs));  // open: en_out, en_in
  Multiplexer #(.select(2), .width(32), .disabled("Z"), .enable("true")) multiplexer_14 (
    .in1(32'h30ac), .in2(32'h3158), .in3(32'h3204), .out(\中断入口地址 ), .sel(\最优中断号 ), .en(priority_encoder_1_gs));  // open: in0
  Multiplexer #(.select(1), .width(2), .disabled("Z"), .enable("false")) multiplexer_15 (
    .in0(\最优中断号 ), .in1(register_6_q), .out(multiplexer_15_out), .sel(ERET));
  or or_15 (or_15_out, ERET, IE_ctrl);
  or or_16 (or_16_out, ERET, IE_ctrl);
  Multiplexer #(.select(1), .width(32), .disabled("Z"), .enable("false")) multiplexer_16 (
    .in0(PC_4), .in1(register_7_q), .out(multiplexer_16_out), .sel(ERET));
  Register #(.width(2), .trigger("rising"), .Select("low")) register_4 (
    .D(multiplexer_15_out), .en(or_15_out), .Q(\当前中断号 ), .clk(CLK));  // open: clr
  Register #(.width(32), .trigger("rising"), .Select("low")) register_5 (
    .D(multiplexer_16_out), .en(or_16_out), .Q(EPC), .clk(CLK));  // open: clr
  Decoder #(.select(2), .tristate("false"), .disabled("Z"), .enable("false")) decoder_1 (
    .out1(decoder_1_out1), .out2(decoder_1_out2), .out3(decoder_1_out3), .sel(\最优中断号 ));  // open: out0
  Multiplexer #(.select(1), .width(2), .disabled("Z"), .enable("false")) multiplexer_17 (
    .in0(\当前中断号 ), .in1(register_8_q), .out(multiplexer_17_out), .sel(ERET));
  Multiplexer #(.select(1), .width(32), .disabled("Z"), .enable("false")) multiplexer_18 (
    .in0(EPC), .in1(register_9_q), .out(multiplexer_18_out), .sel(ERET));
  Register #(.width(2), .trigger("rising"), .Select("low")) register_6 (
    .D(multiplexer_17_out), .en(or_15_out), .Q(register_6_q), .clk(CLK));  // open: clr
  Register #(.width(32), .trigger("rising"), .Select("low")) register_7 (
    .D(multiplexer_18_out), .en(or_16_out), .Q(register_7_q), .clk(CLK));  // open: clr
  and and_10 (Rst1, decoder_1_out1, ERET);
  and and_11 (Rst2, decoder_1_out2, ERET);
  and and_12 (Rst3, decoder_1_out3, ERET);
  Multiplexer #(.select(1), .width(2), .disabled("Z"), .enable("false")) multiplexer_19 (
    .in0(register_6_q), .in1(2'b00), .out(multiplexer_19_out), .sel(ERET));
  Multiplexer #(.select(1), .width(32), .disabled("Z"), .enable("false")) multiplexer_20 (
    .in0(register_7_q), .in1({32{1'b0}}), .out(multiplexer_20_out), .sel(ERET));
  Register #(.width(2), .trigger("rising"), .Select("low")) register_8 (
    .D(multiplexer_19_out), .en(or_15_out), .Q(register_8_q), .clk(CLK));  // open: clr
  Register #(.width(32), .trigger("rising"), .Select("low")) register_9 (
    .D(multiplexer_20_out), .en(or_16_out), .Q(register_9_q), .clk(CLK));  // open: clr

  // Notes on the sheet:
  //   中断源
  //   中断等待指示
  //   总复位信号应将除ROM以外所有存储组件全部清零
  //   多级中断测试信号模拟器
  //   控制位
  //   暂停节拍，不能为0
  //   戳工具置1进入计数暂停模式，ctrl+k时钟自动运行到对应节拍暂停
  //   ctrl+k关闭时钟连续运行，将控制位置零，进入单步调试模式调试
  //   用这个时钟源需要去掉电路中的其他时钟源
  //   数码管输出
  //   数码管输出应该用寄存器锁存，否则显示数据只能一闪而过
  //   可计数暂停的时钟源
  //   指令存储器
  //   contents of rom_1 (hex, n*v repeats v):
  //   201d07d0 20100001 109fc0 139fc3 8021 2012000c 24160008 26100001 3210000f 20080008 20090001 139900
  //   2709825 132020 20020022 c 1094022 1500fff9 22100001 2018000f 2188024 108700 20080008 20090001 139902
  //   2709825 132021 20020022 c 1094022 1500fff9 108702 2c9b022 12c00001 8000c07 4020 1084027 84400
  //   3508ffff 82021 20020022 c 8000c01 afa20000 23bd0004 afa40000 23bd0004 afb00000 23bd0004 afb30000
  //   23bd0004 afb40000 23bd0004 afb50000 23bd0004 afb60000 23bd0004 40000000 20160001 20140003 20150001
  //   168020 108100 2149825 132020 20020022 c 1600fffa 295a022 1680fff7 40800000 23bdfffc 8fb60000
  //   23bdfffc 8fb50000 23bdfffc 8fb40000 23bdfffc 8fb30000 23bdfffc 8fb00000 23bdfffc 8fa40000 23bdfffc
  //   8fa20000 42000018 afa20000 23bd0004 afa40000 23bd0004 afb00000 23bd0004 afb30000 23bd0004 afb40000
  //   23bd0004 afb50000 23bd0004 afb60000 23bd0004 40000000 20160002 20140003 20150001 168020 108100
  //   2149825 132020 20020022 c 1600fffa 295a022 1680fff7 40800000 23bdfffc 8fb60000 23bdfffc 8fb50000
  //   23bdfffc 8fb40000 23bdfffc 8fb30000 23bdfffc 8fb00000 23bdfffc 8fa40000 23bdfffc 8fa20000 42000018
  //   afa20000 23bd0004 afa40000 23bd0004 afb00000 23bd0004 afb30000 23bd0004 afb40000 23bd0004 afb50000
  //   23bd0004 afb60000 23bd0004 40000000 20160003 20140003 20150001 168020 108100 2149825 132020 20020022
  //   c 1600fffa 295a022 1680fff7 40800000 23bdfffc 8fb60000 23bdfffc 8fb50000 23bdfffc 8fb40000 23bdfffc
  //   8fb30000 23bdfffc 8fb00000 23bdfffc 8fa40000 23bdfffc 8fa20000 42000018
  //   OP
  //   Func
  //   rs
  //   指令字
  //   rt
  //   rd
  //   JMP
  //   JR
  //   OP
  //   Func
  //   Beq
  //   Bne
  //   MemToReg
  //   MemWrite
  //   AluOP
  //   AluSrcB
  //   RegWrite
  //   JAL
  //   RegDst
  //   Syscall
  //   为方便自动评测，需要输出PC，IR，寄存器堆写如数据RDin
  //   RAM写使能MemWrite、RAM写入数据MDin等信号
endmodule

module \封装正确性测试  (
);

  wire IR1, IR2, IR3, MemW, RegW;
  wire [31:0] EX_PC, ID_PC, IF_PC, IR, LED, MDin, MDinr, MEM_PC, PC, RDin, RDinr, WB_PC;

  \单周期MIPS  \u_单周期mips_1  (
    .RegWrite(RegW), .MemWrite(MemW), .PC(PC), .IR(IR), .RDin(RDin), .MDin(MDin), .LedData(LED));  // open: IR1, IR2, IR3
  \气泡流水线  \u_气泡流水线_1  (
    .RegWrite(RegW), .MemWrite(MemW), .IF_PC(IF_PC), .ID_PC(ID_PC), .EX_PC(EX_PC), .M_PC(MEM_PC),
    .WB_PC(WB_PC), .RDin(RDinr), .MDin(MDinr), .LedData(LED));
  \单周期MIPS_单级中断  \u_单周期mips_单级中断_1  (
    .IR1(IR1), .IR2(IR2), .IR3(IR3), .RegWrite(RegW), .MemWrite(MemW), .PC(PC), .IR(IR), .RDin(RDin),
    .MDin(MDin), .LedData(LED));
  \理想流水线  \u_理想流水线_1  (
    .RegWrite(RegW), .MemWrite(MemW), .IF_PC(IF_PC), .ID_PC(ID_PC), .EX_PC(EX_PC), .M_PC(MEM_PC),
    .WB_PC(WB_PC), .RDin(RDinr), .MDin(MDinr), .LedData(LED));
  \重定向流水线  \u_重定向流水线_1  (
    .RegWrite(RegW), .MemWrite(MemW), .IF_PC(IF_PC), .ID_PC(ID_PC), .EX_PC(EX_PC), .M_PC(MEM_PC),
    .WB_PC(WB_PC), .RDin(RDinr), .MDin(MDinr), .LedData(LED));
  \单周期MIPS_多级中断  \u_单周期mips_多级中断_1  (
    .IR1(IR1), .IR2(IR2), .IR3(IR3), .RegWrite(RegW), .MemWrite(MemW), .PC(PC), .IR(IR), .RDin(RDin),
    .MDin(MDin), .LedData(LED));

  // Notes on the sheet:
  //   单周期封装测试
  //   气泡流水封装测试
  //   单周期+单级中断封装测试
  //   请检查上面封装有无位宽不匹配，引脚标签是否和连接的标签相对应，否则无法在educoder平台上正确测试
  //   理想流水封装测试
  //   重定向流水封装测试
  //   单周期+多级中断封装测试
endmodule

module IF_ID (
  input  RedDst_in,
  input  AluSrcB_in,
  input  [4:0] Shamt_in,
  input  Syscall_in,
  input  RegWrite_in,
  input  JMP_in,
  input  JAL_in,
  input  [3:0] AluOp_in,
  input  JR_in,
  input  MemWrite_in,
  input  [31:0] IR_in,
  input  PredictJMP_in,
  input  SLLV_in,
  input  [31:0] PC_in,
  input  Beq_in,
  input  LUI_in,
  input  Bne_in,
  input  SB_in,
  input  [31:0] A_in,
  input  MemToReg_in,
  input  BGTZ_in,
  input  [31:0] B_in,
  input  [31:0] Imm_in,
  input  CLR,
  input  Stall,
  input  CLK,
  output RedDst_out,
  output AluSrcB_out,
  output Syscall_out,
  output RegWrite_out,
  output [4:0] Shamt_out,
  output JMP_out,
  output JAL_out,
  output [3:0] AluOp_out,
  output JR_out,
  output MemWrite_out,
  output [31:0] IR_out,
  output PredictJMP_out,
  output SLLV_out,
  output [31:0] PC_out,
  output Beq_out,
  output LUI_out,
  output [31:0] A_out,
  output Bne_out,
  output SB_out,
  output MemToReg_out,
  output BGTZ_out,
  output [31:0] B_out,
  output [31:0] Imm_out
);

  wire multiplexer_1_out, multiplexer_2_out, multiplexer_3_out, multiplexer_4_out, multiplexer_5_out,
       multiplexer_6_out, multiplexer_7_out, multiplexer_8_out, multiplexer_9_out, multiplexer_10_out,
       multiplexer_11_out, multiplexer_12_out, multiplexer_13_out, multiplexer_14_out, multiplexer_15_out,
       multiplexer_16_out, not_1_out, not_2_out, pull_resistor_6_node, undriven, undriven_2;
  wire [3:0] multiplexer_18_out;
  wire [4:0] multiplexer_17_out;
  wire [31:0] multiplexer_19_out, multiplexer_20_out, multiplexer_21_out, multiplexer_22_out,
       multiplexer_23_out;

  Multiplexer #(.select(1), .width(1), .disabled("Z"), .enable("false")) multiplexer_1 (
    .in0(RedDst_in), .in1(1'b0), .out(multiplexer_1_out), .sel(CLR));
  Multiplexer #(.select(1), .width(1), .disabled("Z"), .enable("false")) multiplexer_2 (
    .in0(Syscall_in), .in1(1'b0), .out(multiplexer_2_out), .sel(CLR));
  Multiplexer #(.select(1), .width(1), .disabled("Z"), .enable("false")) multiplexer_3 (
    .in0(JMP_in), .in1(1'b0), .out(multiplexer_3_out), .sel(CLR));
  Multiplexer #(.select(1), .width(1), .disabled("Z"), .enable("false")) multiplexer_4 (
    .in0(JR_in), .in1(1'b0), .out(multiplexer_4_out), .sel(CLR));
  Multiplexer #(.select(1), .width(1), .disabled("Z"), .enable("false")) multiplexer_5 (
    .in0(PredictJMP_in), .in1(1'b0), .out(multiplexer_5_out), .sel(CLR));
  Multiplexer #(.select(1), .width(1), .disabled("Z"), .enable("false")) multiplexer_6 (
    .in0(Beq_in), .in1(1'b0), .out(multiplexer_6_out), .sel(CLR));
  Multiplexer #(.select(1), .width(1), .disabled("Z"), .enable("false")) multiplexer_7 (
    .in0(Bne_in), .in1(1'b0), .out(multiplexer_7_out), .sel(CLR));
  Multiplexer #(.select(1), .width(1), .disabled("Z"), .enable("false")) multiplexer_8 (
    .in0(MemToReg_in), .in1(1'b0), .out(multiplexer_8_out), .sel(CLR));
  Pull_Resistor #(.pull(0)) pull_resistor_1 (.node(CLR));
  not not_1 (not_1_out, Stall);
  Pull_Resistor #(.pull(0)) pull_resistor_2 (.node(not_1_out));
  Register #(.width(1), .trigger("rising"), .Select("low")) register_1 (
    .D(multiplexer_1_out), .en(not_1_out), .Q(RedDst_out), .clk(CLK));  // open: clr
  Register #(.width(1), .trigger("rising"), .Select("low")) register_2 (
    .D(multiplexer_2_out), .en(not_1_out), .Q(Syscall_out), .clk(CLK));  // open: clr
  Register #(.width(1), .trigger("rising"), .Select("low")) register_3 (
    .D(multiplexer_3_out), .en(not_1_out), .Q(JMP_out), .clk(CLK));  // open: clr
  Register #(.width(1), .trigger("rising"), .Select("low")) register_4 (
    .D(multiplexer_4_out), .en(not_1_out), .Q(JR_out), .clk(CLK));  // open: clr
  Register #(.width(1), .trigger("rising"), .Select("low")) register_5 (
    .D(multiplexer_5_out), .en(not_1_out), .Q(PredictJMP_out), .clk(CLK));  // open: clr
  Register #(.width(1), .trigger("rising"), .Select("low")) register_6 (
    .D(multiplexer_6_out), .en(not_1_out), .Q(Beq_out), .clk(CLK), .clr(undriven));
  Register #(.width(1), .trigger("rising"), .Select("low")) register_7 (
    .D(multiplexer_7_out), .en(not_1_out), .Q(Bne_out), .clk(CLK));  // open: clr
  Register #(.width(1), .trigger("rising"), .Select("low")) register_8 (
    .D(multiplexer_8_out), .en(not_1_out), .Q(MemToReg_out), .clk(CLK));  // open: clr
  Multiplexer #(.select(1), .width(1), .disabled("Z"), .enable("false")) multiplexer_9 (
    .in0(AluSrcB_in), .in1(1'b0), .out(multiplexer_9_out), .sel(CLR));
  Multiplexer #(.select(1), .width(1), .disabled("Z"), .enable("false")) multiplexer_10 (
    .in0(RegWrite_in), .in1(1'b0), .out(multiplexer_10_out), .sel(CLR));
  Multiplexer #(.select(1), .width(1), .disabled("Z"), .enable("false")) multiplexer_11 (
    .in0(JAL_in), .in1(1'b0), .out(multiplexer_11_out), .sel(CLR));
  Multiplexer #(.select(1), .width(1), .disabled("Z"), .enable("false")) multiplexer_12 (
    .in0(MemWrite_in), .in1(1'b0), .out(multiplexer_12_out), .sel(CLR));
  Multiplexer #(.select(1), .width(1), .disabled("Z"), .enable("false")) multiplexer_13 (
    .in0(SLLV_in), .in1(1'b0), .out(multiplexer_13_out), .sel(CLR));
  Multiplexer #(.select(1), .width(1), .disabled("Z"), .enable("false")) multiplexer_14 (
    .in0(LUI_in), .in1(1'b0), .out(multiplexer_14_out), .sel(CLR));
  Multiplexer #(.select(1), .width(1), .disabled("Z"), .enable("false")) multiplexer_15 (
    .in0(SB_in), .in1(1'b0), .out(multiplexer_15_out), .sel(CLR));
  Multiplexer #(.select(1), .width(1), .disabled("Z"), .enable("false")) multiplexer_16 (
    .in0(BGTZ_in), .in1(1'b0), .out(multiplexer_16_out), .sel(CLR));
  Pull_Resistor #(.pull(0)) pull_resistor_3 (.node(CLR));
  not not_2 (not_2_out, Stall);
  Pull_Resistor #(.pull(0)) pull_resistor_4 (.node(not_2_out));
  Register #(.width(1), .trigger("rising"), .Select("low")) register_9 (
    .D(multiplexer_9_out), .en(not_2_out), .Q(AluSrcB_out), .clk(CLK));  // open: clr
  Register #(.width(1), .trigger("rising"), .Select("low")) register_10 (
    .D(multiplexer_10_out), .en(not_2_out), .Q(RegWrite_out), .clk(CLK));  // open: clr
  Register #(.width(1), .trigger("rising"), .Select("low")) register_11 (
    .D(multiplexer_11_out), .en(not_2_out), .Q(JAL_out), .clk(CLK));  // open: clr
  Register #(.width(1), .trigger("rising"), .Select("low")) register_12 (
    .D(multiplexer_12_out), .en(not_2_out), .Q(MemWrite_out), .clk(CLK));  // open: clr
  Register #(.width(1), .trigger("rising"), .Select("low")) register_13 (
    .D(multiplexer_13_out), .en(not_2_out), .Q(SLLV_out), .clk(CLK), .clr(CLK));
  Register #(.width(1), .trigger("rising"), .Select("low")) register_14 (
    .D(multiplexer_14_out), .en(not_2_out), .Q(LUI_out), .clk(CLK), .clr(undriven_2));
  Register #(.width(1), .trigger("rising"), .Select("low")) register_15 (
    .D(multiplexer_15_out), .en(not_2_out), .Q(SB_out), .clk(CLK));  // open: clr
  Register #(.width(1), .trigger("rising"), .Select("low")) register_16 (
    .D(multiplexer_16_out), .en(not_2_out), .Q(BGTZ_out), .clk(CLK));  // open: clr
  Multiplexer #(.select(1), .width(5), .disabled("Z"), .enable("false")) multiplexer_17 (
    .in0(Shamt_in), .in1({5{1'b0}}), .out(multiplexer_17_out), .sel(CLR));
  Multiplexer #(.select(1), .width(4), .disabled("Z"), .enable("false")) multiplexer_18 (
    .in0(AluOp_in), .in1(4'b0000), .out(multiplexer_18_out), .sel(CLR));
  Multiplexer #(.select(1), .width(32), .disabled("Z"), .enable("false")) multiplexer_19 (
    .in0(IR_in), .in1({32{1'b0}}), .out(multiplexer_19_out), .sel(CLR));
  Multiplexer #(.select(1), .width(32), .disabled("Z"), .enable("false")) multiplexer_20 (
    .in0(PC_in), .in1({32{1'b0}}), .out(multiplexer_20_out), .sel(CLR));
  Multiplexer #(.select(1), .width(32), .disabled("Z"), .enable("false")) multiplexer_21 (
    .in0(A_in), .in1({32{1'b0}}), .out(multiplexer_21_out), .sel(CLR));
  Multiplexer #(.select(1), .width(32), .disabled("Z"), .enable("false")) multiplexer_22 (
    .in0(B_in), .in1({32{1'b0}}), .out(multiplexer_22_out), .sel(CLR));
  Multiplexer #(.select(1), .width(32), .disabled("Z"), .enable("false")) multiplexer_23 (
    .in0(Imm_in), .in1({32{1'b0}}), .out(multiplexer_23_out), .sel(CLR));
  Pull_Resistor #(.pull(0)) pull_resistor_5 (.node(CLR));
  Pull_Resistor #(.pull(0)) pull_resistor_6 (.node(pull_resistor_6_node));
  not not_3 (pull_resistor_6_node, Stall);
  Register #(.width(5), .trigger("rising"), .Select("low")) register_17 (
    .D(multiplexer_17_out), .en(pull_resistor_6_node), .Q(Shamt_out), .clk(CLK));  // open: clr
  Register #(.width(4), .trigger("rising"), .Select("low")) register_18 (
    .D(multiplexer_18_out), .en(pull_resistor_6_node), .Q(AluOp_out), .clk(CLK));  // open: clr
  Register #(.width(32), .trigger("rising"), .Select("low")) register_19 (
    .D(multiplexer_19_out), .en(pull_resistor_6_node), .Q(IR_out), .clk(CLK));  // open: clr
  Register #(.width(32), .trigger("rising"), .Select("low")) register_20 (
    .D(multiplexer_20_out), .en(pull_resistor_6_node), .Q(PC_out), .clk(CLK));  // open: clr
  Register #(.width(32), .trigger("rising"), .Select("low")) register_21 (
    .D(multiplexer_21_out), .en(pull_resistor_6_node), .Q(A_out), .clk(CLK));  // open: clr
  Register #(.width(32), .trigger("rising"), .Select("low")) register_22 (
    .D(multiplexer_22_out), .en(pull_resistor_6_node), .Q(B_out), .clk(CLK));  // open: clr
  Register #(.width(32), .trigger("rising"), .Select("low")) register_23 (
    .D(multiplexer_23_out), .en(pull_resistor_6_node), .Q(Imm_out), .clk(CLK));  // open: clr
endmodule

module ID_EX (
  input  ERET_in,
  input  RedDst_in,
  input  AluSrcB_in,
  input  [4:0] Shamt_in,
  input  Syscall_in,
  input  RegWrite_in,
  input  JMP_in,
  input  JAL_in,
  input  [3:0] AluOp_in,
  input  JR_in,
  input  MemWrite_in,
  input  [31:0] IR_in,
  input  PredictJMP_in,
  input  SLLV_in,
  input  [31:0] PC_in,
  input  Beq_in,
  input  LUI_in,
  input  Bne_in,
  input  SB_in,
  input  [31:0] A_in,
  input  MemToReg_in,
  input  BGTZ_in,
  input  [31:0] B_in,
  input  [31:0] Imm_in,
  input  CLR,
  input  Stall,
  input  CLK,
  output ERET_OUT,
  output RedDst_out,
  output AluSrcB_out,
  output Syscall_out,
  output RegWrite_out,
  output [4:0] Shamt_out,
  output JMP_out,
  output JAL_out,
  output [3:0] AluOp_out,
  output JR_out,
  output MemWrite_out,
  output [31:0] IR_out,
  output PredictJMP_out,
  output SLLV_out,
  output [31:0] PC_out,
  output Beq_out,
  output LUI_out,
  output [31:0] A_out,
  output Bne_out,
  output SB_out,
  output MemToReg_out,
  output BGTZ_out,
  output [31:0] B_out,
  output [31:0] Imm_out
);

  wire multiplexer_1_out, multiplexer_2_out, multiplexer_3_out, multiplexer_4_out, multiplexer_5_out,
       multiplexer_6_out, multiplexer_7_out, multiplexer_8_out, multiplexer_9_out, multiplexer_10_out,
       multiplexer_11_out, multiplexer_12_out, multiplexer_13_out, multiplexer_14_out, multiplexer_15_out,
       multiplexer_16_out, multiplexer_17_out, not_2_out, pull_resistor_2_node, pull_resistor_6_node,
       undriven, undriven_2;
  wire [3:0] multiplexer_19_out;
  wire [4:0] multiplexer_18_out;
  wire [31:0] multiplexer_20_out, multiplexer_21_out, multiplexer_22_out, multiplexer_23_out,
       multiplexer_24_out;

  Multiplexer #(.select(1), .width(1), .disabled("Z"), .enable("false")) multiplexer_1 (
    .in0(RedDst_in), .in1(1'b0), .out(multiplexer_1_out), .sel(CLR));
  Multiplexer #(.select(1), .width(1), .disabled("Z"), .enable("false")) multiplexer_2 (
    .in0(Syscall_in), .in1(1'b0), .out(multiplexer_2_out), .sel(CLR));
  Multiplexer #(.select(1), .width(1), .disabled("Z"), .enable("false")) multiplexer_3 (
    .in0(JMP_in), .in1(1'b0), .out(multiplexer_3_out), .sel(CLR));
  Multiplexer #(.select(1), .width(1), .disabled("Z"), .enable("false")) multiplexer_4 (
    .in0(JR_in), .in1(1'b0), .out(multiplexer_4_out), .sel(CLR));
  Multiplexer #(.select(1), .width(1), .disabled("Z"), .enable("false")) multiplexer_5 (
    .in0(PredictJMP_in), .in1(1'b0), .out(multiplexer_5_out), .sel(CLR));
  Multiplexer #(.select(1), .width(1), .disabled("Z"), .enable("false")) multiplexer_6 (
    .in0(Beq_in), .in1(1'b0), .out(multiplexer_6_out), .sel(CLR));
  Multiplexer #(.select(1), .width(1), .disabled("Z"), .enable("false")) multiplexer_7 (
    .in0(Bne_in), .in1(1'b0), .out(multiplexer_7_out), .sel(CLR));
  Multiplexer #(.select(1), .width(1), .disabled("Z"), .enable("false")) multiplexer_8 (
    .in0(MemToReg_in), .in1(1'b0), .out(multiplexer_8_out), .sel(CLR));
  Pull_Resistor #(.pull(0)) pull_resistor_1 (.node(CLR));
  Pull_Resistor #(.pull(0)) pull_resistor_2 (.node(pull_resistor_2_node));
  not not_1 (pull_resistor_2_node, Stall);
  Register #(.width(1), .trigger("rising"), .Select("low")) register_1 (
    .D(multiplexer_1_out), .en(pull_resistor_2_node), .Q(RedDst_out), .clk(CLK));  // open: clr
  Register #(.width(1), .trigger("rising"), .Select("low")) register_2 (
    .D(multiplexer_2_out), .en(pull_resistor_2_node), .Q(Syscall_out), .clk(CLK));  // open: clr
  Register #(.width(1), .trigger("rising"), .Select("low")) register_3 (
    .D(multiplexer_3_out), .en(pull_resistor_2_node), .Q(JMP_out), .clk(CLK));  // open: clr
  Register #(.width(1), .trigger("rising"), .Select("low")) register_4 (
    .D(multiplexer_4_out), .en(pull_resistor_2_node), .Q(JR_out), .clk(CLK));  // open: clr
  Register #(.width(1), .trigger("rising"), .Select("low")) register_5 (
    .D(multiplexer_5_out), .en(pull_resistor_2_node), .Q(PredictJMP_out), .clk(CLK));  // open: clr
  Register #(.width(1), .trigger("rising"), .Select("low")) register_6 (
    .D(multiplexer_6_out), .en(pull_resistor_2_node), .Q(Beq_out), .clk(CLK), .clr(undriven));
  Register #(.width(1), .trigger("rising"), .Select("low")) register_7 (
    .D(multiplexer_7_out), .en(pull_resistor_2_node), .Q(Bne_out), .clk(CLK));  // open: clr
  Register #(.width(1), .trigger("rising"), .Select("low")) register_8 (
    .D(multiplexer_8_out), .en(pull_resistor_2_node), .Q(MemToReg_out), .clk(CLK));  // open: clr
  Multiplexer #(.select(1), .width(1), .disabled("Z"), .enable("false")) multiplexer_9 (
    .in0(ERET_in), .in1(1'b0), .out(multiplexer_9_out), .sel(CLR));
  Multiplexer #(.select(1), .width(1), .disabled("Z"), .enable("false")) multiplexer_10 (
    .in0(AluSrcB_in), .in1(1'b0), .out(multiplexer_10_out), .sel(CLR));
  Multiplexer #(.select(1), .width(1), .disabled("Z"), .enable("false")) multiplexer_11 (
    .in0(RegWrite_in), .in1(1'b0), .out(multiplexer_11_out), .sel(CLR));
  Multiplexer #(.select(1), .width(1), .disabled("Z"), .enable("false")) multiplexer_12 (
    .in0(JAL_in), .in1(1'b0), .out(multiplexer_12_out), .sel(CLR));
  Multiplexer #(.select(1), .width(1), .disabled("Z"), .enable("false")) multiplexer_13 (
    .in0(MemWrite_in), .in1(1'b0), .out(multiplexer_13_out), .sel(CLR));
  Multiplexer #(.select(1), .width(1), .disabled("Z"), .enable("false")) multiplexer_14 (
    .in0(SLLV_in), .in1(1'b0), .out(multiplexer_14_out), .sel(CLR));
  Multiplexer #(.select(1), .width(1), .disabled("Z"), .enable("false")) multiplexer_15 (
    .in0(LUI_in), .in1(1'b0), .out(multiplexer_15_out), .sel(CLR));
  Multiplexer #(.select(1), .width(1), .disabled("Z"), .enable("false")) multiplexer_16 (
    .in0(SB_in), .in1(1'b0), .out(multiplexer_16_out), .sel(CLR));
  Multiplexer #(.select(1), .width(1), .disabled("Z"), .enable("false")) multiplexer_17 (
    .in0(BGTZ_in), .in1(1'b0), .out(multiplexer_17_out), .sel(CLR));
  Pull_Resistor #(.pull(0)) pull_resistor_3 (.node(CLR));
  not not_2 (not_2_out, Stall);
  Pull_Resistor #(.pull(0)) pull_resistor_4 (.node(not_2_out));
  Register #(.width(1), .trigger("rising"), .Select("low")) register_9 (
    .D(multiplexer_9_out), .en(not_2_out), .Q(ERET_OUT), .clk(CLK));  // open: clr
  Register #(.width(1), .trigger("rising"), .Select("low")) register_10 (
    .D(multiplexer_10_out), .en(not_2_out), .Q(AluSrcB_out), .clk(CLK));  // open: clr
  Register #(.width(1), .trigger("rising"), .Select("low")) register_11 (
    .D(multiplexer_11_out), .en(not_2_out), .Q(RegWrite_out), .clk(CLK));  // open: clr
  Register #(.width(1), .trigger("rising"), .Select("low")) register_12 (
    .D(multiplexer_12_out), .en(not_2_out), .Q(JAL_out), .clk(CLK));  // open: clr
  Register #(.width(1), .trigger("rising"), .Select("low")) register_13 (
    .D(multiplexer_13_out), .en(not_2_out), .Q(MemWrite_out), .clk(CLK));  // open: clr
  Register #(.width(1), .trigger("rising"), .Select("low")) register_14 (
    .D(multiplexer_14_out), .en(not_2_out), .Q(SLLV_out), .clk(CLK));  // open: clr
  Register #(.width(1), .trigger("rising"), .Select("low")) register_15 (
    .D(multiplexer_15_out), .en(not_2_out), .Q(LUI_out), .clk(CLK), .clr(undriven_2));
  Register #(.width(1), .trigger("rising"), .Select("low")) register_16 (
    .D(multiplexer_16_out), .en(not_2_out), .Q(SB_out), .clk(CLK));  // open: clr
  Register #(.width(1), .trigger("rising"), .Select("low")) register_17 (
    .D(multiplexer_17_out), .en(not_2_out), .Q(BGTZ_out), .clk(CLK));  // open: clr
  Multiplexer #(.select(1), .width(5), .disabled("Z"), .enable("false")) multiplexer_18 (
    .in0(Shamt_in), .in1({5{1'b0}}), .out(multiplexer_18_out), .sel(CLR));
  Multiplexer #(.select(1), .width(4), .disabled("Z"), .enable("false")) multiplexer_19 (
    .in0(AluOp_in), .in1(4'b0000), .out(multiplexer_19_out), .sel(CLR));
  Multiplexer #(.select(1), .width(32), .disabled("Z"), .enable("false")) multiplexer_20 (
    .in0(IR_in), .in1({32{1'b0}}), .out(multiplexer_20_out), .sel(CLR));
  Multiplexer #(.select(1), .width(32), .disabled("Z"), .enable("false")) multiplexer_21 (
    .in0(PC_in), .in1({32{1'b0}}), .out(multiplexer_21_out), .sel(CLR));
  Multiplexer #(.select(1), .width(32), .disabled("Z"), .enable("false")) multiplexer_22 (
    .in0(A_in), .in1({32{1'b0}}), .out(multiplexer_22_out), .sel(CLR));
  Multiplexer #(.select(1), .width(32), .disabled("Z"), .enable("false")) multiplexer_23 (
    .in0(B_in), .in1({32{1'b0}}), .out(multiplexer_23_out), .sel(CLR));
  Multiplexer #(.select(1), .width(32), .disabled("Z"), .enable("false")) multiplexer_24 (
    .in0(Imm_in), .in1({32{1'b0}}), .out(multiplexer_24_out), .sel(CLR));
  Pull_Resistor #(.pull(0)) pull_resistor_5 (.node(CLR));
  Pull_Resistor #(.pull(0)) pull_resistor_6 (.node(pull_resistor_6_node));
  not not_3 (pull_resistor_6_node, Stall);
  Register #(.width(5), .trigger("rising"), .Select("low")) register_18 (
    .D(multiplexer_18_out), .en(pull_resistor_6_node), .Q(Shamt_out), .clk(CLK));  // open: clr
  Register #(.width(4), .trigger("rising"), .Select("low")) register_19 (
    .D(multiplexer_19_out), .en(pull_resistor_6_node), .Q(AluOp_out), .clk(CLK));  // open: clr
  Register #(.width(32), .trigger("rising"), .Select("low")) register_20 (
    .D(multiplexer_20_out), .en(pull_resistor_6_node), .Q(IR_out), .clk(CLK));  // open: clr
  Register #(.width(32), .trigger("rising"), .Select("low")) register_21 (
    .D(multiplexer_21_out), .en(pull_resistor_6_node), .Q(PC_out), .clk(CLK));  // open: clr
  Register #(.width(32), .trigger("rising"), .Select("low")) register_22 (
    .D(multiplexer_22_out), .en(pull_resistor_6_node), .Q(A_out), .clk(CLK));  // open: clr
  Register #(.width(32), .trigger("rising"), .Select("low")) register_23 (
    .D(multiplexer_23_out), .en(pull_resistor_6_node), .Q(B_out), .clk(CLK));  // open: clr
  Register #(.width(32), .trigger("rising"), .Select("low")) register_24 (
    .D(multiplexer_24_out), .en(pull_resistor_6_node), .Q(Imm_out), .clk(CLK));  // open: clr
endmodule

module EX_MEM (
  input  ERET_in,
  input  RedDst_in,
  input  AluSrcB_in,
  input  [4:0] Shamt_in,
  input  Syscall_in,
  input  RegWrite_in,
  input  JMP_in,
  input  JAL_in,
  input  [31:0] AluResult_in,
  input  JR_in,
  input  MemWrite_in,
  input  [31:0] IR_in,
  input  SignedExt_in,
  input  SLLV_in,
  input  [31:0] PC_in,
  input  Beq_in,
  input  LUI_in,
  input  Bne_in,
  input  SB_in,
  input  [31:0] A_in,
  input  MemToReg_in,
  input  BGTZ_in,
  input  [31:0] B_in,
  input  [31:0] Imm_in,
  input  CLR,
  input  Stall,
  input  CLK,
  output ERET_OUT,
  output RedDst_out,
  output AluSrcB_out,
  output Syscall_out,
  output RegWrite_out,
  output [4:0] Shamt_out,
  output JMP_out,
  output JAL_out,
  output [31:0] AluResult_out,
  output JR_out,
  output MemWrite_out,
  output [31:0] IR_out,
  output SignedExt_out,
  output SLLV_out,
  output [31:0] PC_out,
  output Beq_out,
  output LUI_out,
  output [31:0] A_out,
  output Bne_out,
  output SB_out,
  output MemToReg_out,
  output BGTZ_out,
  output [31:0] B_out,
  output [31:0] Imm_out
);

  wire multiplexer_1_out, multiplexer_2_out, multiplexer_3_out, multiplexer_4_out, multiplexer_5_out,
       multiplexer_6_out, multiplexer_7_out, multiplexer_8_out, multiplexer_9_out, multiplexer_10_out,
       multiplexer_11_out, multiplexer_12_out, multiplexer_13_out, multiplexer_14_out, multiplexer_15_out,
       multiplexer_16_out, multiplexer_17_out, not_2_out, pull_resistor_2_node, pull_resistor_6_node,
       undriven, undriven_2;
  wire [4:0] multiplexer_18_out;
  wire [31:0] multiplexer_19_out, multiplexer_20_out, multiplexer_21_out, multiplexer_22_out,
       multiplexer_23_out, multiplexer_24_out;

  Multiplexer #(.select(1), .width(1), .disabled("Z"), .enable("false")) multiplexer_1 (
    .in0(RedDst_in), .in1(1'b0), .out(multiplexer_1_out), .sel(CLR));
  Multiplexer #(.select(1), .width(1), .disabled("Z"), .enable("false")) multiplexer_2 (
    .in0(Syscall_in), .in1(1'b0), .out(multiplexer_2_out), .sel(CLR));
  Multiplexer #(.select(1), .width(1), .disabled("Z"), .enable("false")) multiplexer_3 (
    .in0(JMP_in), .in1(1'b0), .out(multiplexer_3_out), .sel(CLR));
  Multiplexer #(.select(1), .width(1), .disabled("Z"), .enable("false")) multiplexer_4 (
    .in0(JR_in), .in1(1'b0), .out(multiplexer_4_out), .sel(CLR));
  Multiplexer #(.select(1), .width(1), .disabled("Z"), .enable("false")) multiplexer_5 (
    .in0(SignedExt_in), .in1(1'b0), .out(multiplexer_5_out), .sel(CLR));
  Multiplexer #(.select(1), .width(1), .disabled("Z"), .enable("false")) multiplexer_6 (
    .in0(Beq_in), .in1(1'b0), .out(multiplexer_6_out), .sel(CLR));
  Multiplexer #(.select(1), .width(1), .disabled("Z"), .enable("false")) multiplexer_7 (
    .in0(Bne_in), .in1(1'b0), .out(multiplexer_7_out), .sel(CLR));
  Multiplexer #(.select(1), .width(1), .disabled("Z"), .enable("false")) multiplexer_8 (
    .in0(MemToReg_in), .in1(1'b0), .out(multiplexer_8_out), .sel(CLR));
  Pull_Resistor #(.pull(0)) pull_resistor_1 (.node(CLR));
  Pull_Resistor #(.pull(0)) pull_resistor_2 (.node(pull_resistor_2_node));
  not not_1 (pull_resistor_2_node, Stall);
  Register #(.width(1), .trigger("rising"), .Select("low")) register_1 (
    .D(multiplexer_1_out), .en(pull_resistor_2_node), .Q(RedDst_out), .clk(CLK));  // open: clr
  Register #(.width(1), .trigger("rising"), .Select("low")) register_2 (
    .D(multiplexer_2_out), .en(pull_resistor_2_node), .Q(Syscall_out), .clk(CLK));  // open: clr
  Register #(.width(1), .trigger("rising"), .Select("low")) register_3 (
    .D(multiplexer_3_out), .en(pull_resistor_2_node), .Q(JMP_out), .clk(CLK));  // open: clr
  Register #(.width(1), .trigger("rising"), .Select("low")) register_4 (
    .D(multiplexer_4_out), .en(pull_resistor_2_node), .Q(JR_out), .clk(CLK));  // open: clr
  Register #(.width(1), .trigger("rising"), .Select("low")) register_5 (
    .D(multiplexer_5_out), .en(pull_resistor_2_node), .Q(SignedExt_out), .clk(CLK));  // open: clr
  Register #(.width(1), .trigger("rising"), .Select("low")) register_6 (
    .D(multiplexer_6_out), .en(pull_resistor_2_node), .Q(Beq_out), .clk(CLK), .clr(undriven));
  Register #(.width(1), .trigger("rising"), .Select("low")) register_7 (
    .D(multiplexer_7_out), .en(pull_resistor_2_node), .Q(Bne_out), .clk(CLK));  // open: clr
  Register #(.width(1), .trigger("rising"), .Select("low")) register_8 (
    .D(multiplexer_8_out), .en(pull_resistor_2_node), .Q(MemToReg_out), .clk(CLK));  // open: clr
  Multiplexer #(.select(1), .width(1), .disabled("Z"), .enable("false")) multiplexer_9 (
    .in0(ERET_in), .in1(1'b0), .out(multiplexer_9_out), .sel(CLR));
  Multiplexer #(.select(1), .width(1), .disabled("Z"), .enable("false")) multiplexer_10 (
    .in0(AluSrcB_in), .in1(1'b0), .out(multiplexer_10_out), .sel(CLR));
  Multiplexer #(.select(1), .width(1), .disabled("Z"), .enable("false")) multiplexer_11 (
    .in0(RegWrite_in), .in1(1'b0), .out(multiplexer_11_out), .sel(CLR));
  Multiplexer #(.select(1), .width(1), .disabled("Z"), .enable("false")) multiplexer_12 (
    .in0(JAL_in), .in1(1'b0), .out(multiplexer_12_out), .sel(CLR));
  Multiplexer #(.select(1), .width(1), .disabled("Z"), .enable("false")) multiplexer_13 (
    .in0(MemWrite_in), .in1(1'b0), .out(multiplexer_13_out), .sel(CLR));
  Multiplexer #(.select(1), .width(1), .disabled("Z"), .enable("false")) multiplexer_14 (
    .in0(SLLV_in), .in1(1'b0), .out(multiplexer_14_out), .sel(CLR));
  Multiplexer #(.select(1), .width(1), .disabled("Z"), .enable("false")) multiplexer_15 (
    .in0(LUI_in), .in1(1'b0), .out(multiplexer_15_out), .sel(CLR));
  Multiplexer #(.select(1), .width(1), .disabled("Z"), .enable("false")) multiplexer_16 (
    .in0(SB_in), .in1(1'b0), .out(multiplexer_16_out), .sel(CLR));
  Multiplexer #(.select(1), .width(1), .disabled("Z"), .enable("false")) multiplexer_17 (
    .in0(BGTZ_in), .in1(1'b0), .out(multiplexer_17_out), .sel(CLR));
  Pull_Resistor #(.pull(0)) pull_resistor_3 (.node(CLR));
  not not_2 (not_2_out, Stall);
  Pull_Resistor #(.pull(0)) pull_resistor_4 (.node(not_2_out));
  Register #(.width(1), .trigger("rising"), .Select("low")) register_9 (
    .D(multiplexer_9_out), .en(not_2_out), .Q(ERET_OUT), .clk(CLK));  // open: clr
  Register #(.width(1), .trigger("rising"), .Select("low")) register_10 (
    .D(multiplexer_10_out), .en(not_2_out), .Q(AluSrcB_out), .clk(CLK));  // open: clr
  Register #(.width(1), .trigger("rising"), .Select("low")) register_11 (
    .D(multiplexer_11_out), .en(not_2_out), .Q(RegWrite_out), .clk(CLK));  // open: clr
  Register #(.width(1), .trigger("rising"), .Select("low")) register_12 (
    .D(multiplexer_12_out), .en(not_2_out), .Q(JAL_out), .clk(CLK));  // open: clr
  Register #(.width(1), .trigger("rising"), .Select("low")) register_13 (
    .D(multiplexer_13_out), .en(not_2_out), .Q(MemWrite_out), .clk(CLK));  // open: clr
  Register #(.width(1), .trigger("rising"), .Select("low")) register_14 (
    .D(multiplexer_14_out), .en(not_2_out), .Q(SLLV_out), .clk(CLK));  // open: clr
  Register #(.width(1), .trigger("rising"), .Select("low")) register_15 (
    .D(multiplexer_15_out), .en(not_2_out), .Q(LUI_out), .clk(CLK), .clr(undriven_2));
  Register #(.width(1), .trigger("rising"), .Select("low")) register_16 (
    .D(multiplexer_16_out), .en(not_2_out), .Q(SB_out), .clk(CLK));  // open: clr
  Register #(.width(1), .trigger("rising"), .Select("low")) register_17 (
    .D(multiplexer_17_out), .en(not_2_out), .Q(BGTZ_out), .clk(CLK));  // open: clr
  Multiplexer #(.select(1), .width(5), .disabled("Z"), .enable("false")) multiplexer_18 (
    .in0(Shamt_in), .in1({5{1'b0}}), .out(multiplexer_18_out), .sel(CLR));
  Multiplexer #(.select(1), .width(32), .disabled("Z"), .enable("false")) multiplexer_19 (
    .in0(AluResult_in), .in1({32{1'b0}}), .out(multiplexer_19_out), .sel(CLR));
  Multiplexer #(.select(1), .width(32), .disabled("Z"), .enable("false")) multiplexer_20 (
    .in0(IR_in), .in1({32{1'b0}}), .out(multiplexer_20_out), .sel(CLR));
  Multiplexer #(.select(1), .width(32), .disabled("Z"), .enable("false")) multiplexer_21 (
    .in0(PC_in), .in1({32{1'b0}}), .out(multiplexer_21_out), .sel(CLR));
  Multiplexer #(.select(1), .width(32), .disabled("Z"), .enable("false")) multiplexer_22 (
    .in0(A_in), .in1({32{1'b0}}), .out(multiplexer_22_out), .sel(CLR));
  Multiplexer #(.select(1), .width(32), .disabled("Z"), .enable("false")) multiplexer_23 (
    .in0(B_in), .in1({32{1'b0}}), .out(multiplexer_23_out), .sel(CLR));
  Multiplexer #(.select(1), .width(32), .disabled("Z"), .enable("false")) multiplexer_24 (
    .in0(Imm_in), .in1({32{1'b0}}), .out(multiplexer_24_out), .sel(CLR));
  Pull_Resistor #(.pull(0)) pull_resistor_5 (.node(CLR));
  Pull_Resistor #(.pull(0)) pull_resistor_6 (.node(pull_resistor_6_node));
  not not_3 (pull_resistor_6_node, Stall);
  Register #(.width(5), .trigger("rising"), .Select("low")) register_18 (
    .D(multiplexer_18_out), .en(pull_resistor_6_node), .Q(Shamt_out), .clk(CLK));  // open: clr
  Register #(.width(32), .trigger("rising"), .Select("low")) register_19 (
    .D(multiplexer_19_out), .en(pull_resistor_6_node), .Q(AluResult_out), .clk(CLK));  // open: clr
  Register #(.width(32), .trigger("rising"), .Select("low")) register_20 (
    .D(multiplexer_20_out), .en(pull_resistor_6_node), .Q(IR_out), .clk(CLK));  // open: clr
  Register #(.width(32), .trigger("rising"), .Select("low")) register_21 (
    .D(multiplexer_21_out), .en(pull_resistor_6_node), .Q(PC_out), .clk(CLK));  // open: clr
  Register #(.width(32), .trigger("rising"), .Select("low")) register_22 (
    .D(multiplexer_22_out), .en(pull_resistor_6_node), .Q(A_out), .clk(CLK));  // open: clr
  Register #(.width(32), .trigger("rising"), .Select("low")) register_23 (
    .D(multiplexer_23_out), .en(pull_resistor_6_node), .Q(B_out), .clk(CLK));  // open: clr
  Register #(.width(32), .trigger("rising"), .Select("low")) register_24 (
    .D(multiplexer_24_out), .en(pull_resistor_6_node), .Q(Imm_out), .clk(CLK));  // open: clr
endmodule

module MEM_WB (
  input  ERET_in,
  input  RedDst_in,
  input  AluSrcB_in,
  input  [31:0] MemData_in,
  input  Syscall_in,
  input  RegWrite_in,
  input  JMP_in,
  input  JAL_in,
  input  [31:0] AluResult_in,
  input  JR_in,
  input  MemWrite_in,
  input  [31:0] IR_in,
  input  SignedExt_in,
  input  SLLV_in,
  input  [31:0] PC_in,
  input  Beq_in,
  input  LUI_in,
  input  Bne_in,
  input  SB_in,
  input  [31:0] A_in,
  input  MemToReg_in,
  input  BGTZ_in,
  input  [31:0] B_in,
  input  [31:0] Imm_in,
  input  CLR,
  input  Stall,
  input  CLK,
  output ERET_OUT,
  output RedDst_out,
  output AluSrcB_out,
  output Syscall_out,
  output RegWrite_out,
  output [31:0] MemData_out,
  output JMP_out,
  output JAL_out,
  output [31:0] AluResult_out,
  output JR_out,
  output MemWrite_out,
  output [31:0] IR_out,
  output SignedExt_out,
  output SLLV_out,
  output [31:0] PC_out,
  output Beq_out,
  output LUI_out,
  output [31:0] A_out,
  output Bne_out,
  output SB_out,
  output MemToReg_out,
  output BGTZ_out,
  output [31:0] B_out,
  output [31:0] Imm_out
);

  wire multiplexer_1_out, multiplexer_2_out, multiplexer_3_out, multiplexer_4_out, multiplexer_5_out,
       multiplexer_6_out, multiplexer_7_out, multiplexer_8_out, multiplexer_9_out, multiplexer_10_out,
       multiplexer_11_out, multiplexer_12_out, multiplexer_13_out, multiplexer_14_out, multiplexer_15_out,
       multiplexer_16_out, multiplexer_17_out, not_2_out, pull_resistor_2_node, pull_resistor_6_node,
       undriven, undriven_2;
  wire [31:0] multiplexer_18_out, multiplexer_19_out, multiplexer_20_out, multiplexer_21_out,
       multiplexer_22_out, multiplexer_23_out, multiplexer_24_out;

  Multiplexer #(.select(1), .width(1), .disabled("Z"), .enable("false")) multiplexer_1 (
    .in0(RedDst_in), .in1(1'b0), .out(multiplexer_1_out), .sel(CLR));
  Multiplexer #(.select(1), .width(1), .disabled("Z"), .enable("false")) multiplexer_2 (
    .in0(Syscall_in), .in1(1'b0), .out(multiplexer_2_out), .sel(CLR));
  Multiplexer #(.select(1), .width(1), .disabled("Z"), .enable("false")) multiplexer_3 (
    .in0(JMP_in), .in1(1'b0), .out(multiplexer_3_out), .sel(CLR));
  Multiplexer #(.select(1), .width(1), .disabled("Z"), .enable("false")) multiplexer_4 (
    .in0(JR_in), .in1(1'b0), .out(multiplexer_4_out), .sel(CLR));
  Multiplexer #(.select(1), .width(1), .disabled("Z"), .enable("false")) multiplexer_5 (
    .in0(SignedExt_in), .in1(1'b0), .out(multiplexer_5_out), .sel(CLR));
  Multiplexer #(.select(1), .width(1), .disabled("Z"), .enable("false")) multiplexer_6 (
    .in0(Beq_in), .in1(1'b0), .out(multiplexer_6_out), .sel(CLR));
  Multiplexer #(.select(1), .width(1), .disabled("Z"), .enable("false")) multiplexer_7 (
    .in0(Bne_in), .in1(1'b0), .out(multiplexer_7_out), .sel(CLR));
  Multiplexer #(.select(1), .width(1), .disabled("Z"), .enable("false")) multiplexer_8 (
    .in0(MemToReg_in), .in1(1'b0), .out(multiplexer_8_out), .sel(CLR));
  Pull_Resistor #(.pull(0)) pull_resistor_1 (.node(CLR));
  Pull_Resistor #(.pull(0)) pull_resistor_2 (.node(pull_resistor_2_node));
  not not_1 (pull_resistor_2_node, Stall);
  Register #(.width(1), .trigger("rising"), .Select("low")) register_1 (
    .D(multiplexer_1_out), .en(pull_resistor_2_node), .Q(RedDst_out), .clk(CLK));  // open: clr
  Register #(.width(1), .trigger("rising"), .Select("low")) register_2 (
    .D(multiplexer_2_out), .en(pull_resistor_2_node), .Q(Syscall_out), .clk(CLK));  // open: clr
  Register #(.width(1), .trigger("rising"), .Select("low")) register_3 (
    .D(multiplexer_3_out), .en(pull_resistor_2_node), .Q(JMP_out), .clk(CLK));  // open: clr
  Register #(.width(1), .trigger("rising"), .Select("low")) register_4 (
    .D(multiplexer_4_out), .en(pull_resistor_2_node), .Q(JR_out), .clk(CLK));  // open: clr
  Register #(.width(1), .trigger("rising"), .Select("low")) register_5 (
    .D(multiplexer_5_out), .en(pull_resistor_2_node), .Q(SignedExt_out), .clk(CLK), .clr(CLK));
  Register #(.width(1), .trigger("rising"), .Select("low")) register_6 (
    .D(multiplexer_6_out), .en(pull_resistor_2_node), .Q(Beq_out), .clk(CLK), .clr(undriven));
  Register #(.width(1), .trigger("rising"), .Select("low")) register_7 (
    .D(multiplexer_7_out), .en(pull_resistor_2_node), .Q(Bne_out), .clk(CLK));  // open: clr
  Register #(.width(1), .trigger("rising"), .Select("low")) register_8 (
    .D(multiplexer_8_out), .en(pull_resistor_2_node), .Q(MemToReg_out), .clk(CLK));  // open: clr
  Multiplexer #(.select(1), .width(1), .disabled("Z"), .enable("false")) multiplexer_9 (
    .in0(ERET_in), .in1(1'b0), .out(multiplexer_9_out), .sel(CLR));
  Multiplexer #(.select(1), .width(1), .disabled("Z"), .enable("false")) multiplexer_10 (
    .in0(AluSrcB_in), .in1(1'b0), .out(multiplexer_10_out), .sel(CLR));
  Multiplexer #(.select(1), .width(1), .disabled("Z"), .enable("false")) multiplexer_11 (
    .in0(RegWrite_in), .in1(1'b0), .out(multiplexer_11_out), .sel(CLR));
  Multiplexer #(.select(1), .width(1), .disabled("Z"), .enable("false")) multiplexer_12 (
    .in0(JAL_in), .in1(1'b0), .out(multiplexer_12_out), .sel(CLR));
  Multiplexer #(.select(1), .width(1), .disabled("Z"), .enable("false")) multiplexer_13 (
    .in0(MemWrite_in), .in1(1'b0), .out(multiplexer_13_out), .sel(CLR));
  Multiplexer #(.select(1), .width(1), .disabled("Z"), .enable("false")) multiplexer_14 (
    .in0(SLLV_in), .in1(1'b0), .out(multiplexer_14_out), .sel(CLR));
  Multiplexer #(.select(1), .width(1), .disabled("Z"), .enable("false")) multiplexer_15 (
    .in0(LUI_in), .in1(1'b0), .out(multiplexer_15_out), .sel(CLR));
  Multiplexer #(.select(1), .width(1), .disabled("Z"), .enable("false")) multiplexer_16 (
    .in0(SB_in), .in1(1'b0), .out(multiplexer_16_out), .sel(CLR));
  Multiplexer #(.select(1), .width(1), .disabled("Z"), .enable("false")) multiplexer_17 (
    .in0(BGTZ_in), .in1(1'b0), .out(multiplexer_17_out), .sel(CLR));
  Pull_Resistor #(.pull(0)) pull_resistor_3 (.node(CLR));
  not not_2 (not_2_out, Stall);
  Pull_Resistor #(.pull(0)) pull_resistor_4 (.node(not_2_out));
  Register #(.width(1), .trigger("rising"), .Select("low")) register_9 (
    .D(multiplexer_9_out), .en(not_2_out), .Q(ERET_OUT), .clk(CLK));  // open: clr
  Register #(.width(1), .trigger("rising"), .Select("low")) register_10 (
    .D(multiplexer_10_out), .en(not_2_out), .Q(AluSrcB_out), .clk(CLK));  // open: clr
  Register #(.width(1), .trigger("rising"), .Select("low")) register_11 (
    .D(multiplexer_11_out), .en(not_2_out), .Q(RegWrite_out), .clk(CLK));  // open: clr
  Register #(.width(1), .trigger("rising"), .Select("low")) register_12 (
    .D(multiplexer_12_out), .en(not_2_out), .Q(JAL_out), .clk(CLK));  // open: clr
  Register #(.width(1), .trigger("rising"), .Select("low")) register_13 (
    .D(multiplexer_13_out), .en(not_2_out), .Q(MemWrite_out), .clk(CLK));  // open: clr
  Register #(.width(1), .trigger("rising"), .Select("low")) register_14 (
    .D(multiplexer_14_out), .en(not_2_out), .Q(SLLV_out), .clk(CLK), .clr(CLK));
  Register #(.width(1), .trigger("rising"), .Select("low")) register_15 (
    .D(multiplexer_15_out), .en(not_2_out), .Q(LUI_out), .clk(CLK), .clr(undriven_2));
  Register #(.width(1), .trigger("rising"), .Select("low")) register_16 (
    .D(multiplexer_16_out), .en(not_2_out), .Q(SB_out), .clk(CLK));  // open: clr
  Register #(.width(1), .trigger("rising"), .Select("low")) register_17 (
    .D(multiplexer_17_out), .en(not_2_out), .Q(BGTZ_out), .clk(CLK));  // open: clr
  Multiplexer #(.select(1), .width(32), .disabled("Z"), .enable("false")) multiplexer_18 (
    .in0(MemData_in), .in1({32{1'b0}}), .out(multiplexer_18_out), .sel(CLR));
  Multiplexer #(.select(1), .width(32), .disabled("Z"), .enable("false")) multiplexer_19 (
    .in0(AluResult_in), .in1({32{1'b0}}), .out(multiplexer_19_out), .sel(CLR));
  Multiplexer #(.select(1), .width(32), .disabled("Z"), .enable("false")) multiplexer_20 (
    .in0(IR_in), .in1({32{1'b0}}), .out(multiplexer_20_out), .sel(CLR));
  Multiplexer #(.select(1), .width(32), .disabled("Z"), .enable("false")) multiplexer_21 (
    .in0(PC_in), .in1({32{1'b0}}), .out(multiplexer_21_out), .sel(CLR));
  Multiplexer #(.select(1), .width(32), .disabled("Z"), .enable("false")) multiplexer_22 (
    .in0(A_in), .in1({32{1'b0}}), .out(multiplexer_22_out), .sel(CLR));
  Multiplexer #(.select(1), .width(32), .disabled("Z"), .enable("false")) multiplexer_23 (
    .in0(B_in), .in1({32{1'b0}}), .out(multiplexer_23_out), .sel(CLR));
  Multiplexer #(.select(1), .width(32), .disabled("Z"), .enable("false")) multiplexer_24 (
    .in0(Imm_in), .in1({32{1'b0}}), .out(multiplexer_24_out), .sel(CLR));
  Pull_Resistor #(.pull(0)) pull_resistor_5 (.node(CLR));
  Pull_Resistor #(.pull(0)) pull_resistor_6 (.node(pull_resistor_6_node));
  not not_3 (pull_resistor_6_node, Stall);
  Register #(.width(32), .trigger("rising"), .Select("low")) register_18 (
    .D(multiplexer_18_out), .en(pull_resistor_6_node), .Q(MemData_out), .clk(CLK));  // open: clr
  Register #(.width(32), .trigger("rising"), .Select("low")) register_19 (
    .D(multiplexer_19_out), .en(pull_resistor_6_node), .Q(AluResult_out), .clk(CLK));  // open: clr
  Register #(.width(32), .trigger("rising"), .Select("low")) register_20 (
    .D(multiplexer_20_out), .en(pull_resistor_6_node), .Q(IR_out), .clk(CLK));  // open: clr
  Register #(.width(32), .trigger("rising"), .Select("low")) register_21 (
    .D(multiplexer_21_out), .en(pull_resistor_6_node), .Q(PC_out), .clk(CLK));  // open: clr
  Register #(.width(32), .trigger("rising"), .Select("low")) register_22 (
    .D(multiplexer_22_out), .en(pull_resistor_6_node), .Q(A_out), .clk(CLK));  // open: clr
  Register #(.width(32), .trigger("rising"), .Select("low")) register_23 (
    .D(multiplexer_23_out), .en(pull_resistor_6_node), .Q(B_out), .clk(CLK));  // open: clr
  Register #(.width(32), .trigger("rising"), .Select("low")) register_24 (
    .D(multiplexer_24_out), .en(pull_resistor_6_node), .Q(Imm_out), .clk(CLK));  // open: clr
endmodule
module \源寄存器使用判断  (
  input  OP0,
  input  OP1,
  input  OP2,
  input  OP3,
  input  OP4,
  input  OP5,
  input  F0,
  input  F1,
  input  F2,
  input  F3,
  input  F4,
  input  F5,
  output R1_used,
  output R2_used
);

  wire and_1_out, and_2_out, and_3_out, and_4_out, and_5_out, and_6_out, and_7_out, and_8_out, and_9_out,
       and_10_out, and_11_out, and_12_out, and_13_out, and_14_out, and_15_out, and_16_out, and_17_out,
       and_18_out, and_19_out, and_20_out, and_21_out, and_22_out, and_23_out, and_24_out, and_25_out,
       and_26_out, and_27_out, and_28_out, and_29_out, and_30_out, and_31_out, and_32_out, and_33_out,
       and_34_out, and_35_out, and_36_out, and_37_out, and_38_out, and_39_out, not_1_out, not_2_out,
       not_3_out, not_4_out, not_5_out, not_6_out, not_7_out, not_8_out, not_9_out, not_10_out, not_11_out,
       not_12_out, not_13_out, not_14_out, not_15_out, not_16_out, not_17_out, not_18_out, not_19_out,
       not_20_out, not_21_out, not_22_out, not_23_out, not_24_out, not_25_out, not_26_out, not_27_out,
       not_28_out, not_29_out, not_30_out, not_31_out, not_32_out, not_33_out, not_34_out, not_35_out,
       not_36_out, not_37_out, not_38_out, not_39_out, not_40_out, not_41_out, not_42_out, not_43_out,
       not_44_out, not_45_out, not_46_out, not_47_out, not_48_out, not_49_out, not_50_out, not_51_out,
       not_52_out, not_53_out, not_54_out, not_55_out, not_56_out, not_57_out, not_58_out, not_59_out,
       not_60_out, not_61_out, not_62_out, not_63_out, not_64_out, not_65_out, not_66_out, not_67_out,
       not_68_out, not_69_out, not_70_out, not_71_out, not_72_out, not_73_out, not_74_out, not_75_out,
       not_76_out, not_77_out, not_78_out, not_79_out, not_80_out, not_81_out, not_82_out, not_83_out,
       not_84_out, not_85_out, not_86_out, not_87_out, not_88_out, not_89_out, not_90_out, not_91_out,
       not_92_out, not_93_out, not_94_out, not_95_out, not_96_out, not_97_out, not_98_out, not_99_out,
       not_100_out, not_101_out, not_102_out, not_103_out, not_104_out, not_105_out, not_106_out,
       not_107_out, not_108_out, not_109_out, not_110_out, not_111_out, not_112_out, not_113_out,
       not_114_out, not_115_out, not_116_out, not_117_out, not_118_out, not_119_out, not_120_out,
       not_121_out, not_122_out, not_123_out, not_124_out, not_125_out, not_126_out, not_127_out,
       not_128_out, not_129_out, not_130_out, not_131_out, not_132_out, not_133_out, not_134_out,
       not_135_out, not_136_out, not_137_out, not_138_out, not_139_out, not_140_out, not_141_out,
       not_142_out, not_143_out, not_144_out, not_145_out, not_146_out, not_147_out, not_148_out,
       not_149_out, not_150_out, not_151_out, not_152_out, not_153_out, not_154_out, not_155_out,
       not_156_out, not_157_out, not_158_out, not_159_out, not_160_out, not_161_out, not_162_out,
       not_163_out, not_164_out, not_165_out, not_166_out, not_167_out, not_168_out, not_169_out,
       not_170_out, not_171_out, not_172_out, not_173_out, not_174_out, not_175_out, not_176_out,
       not_177_out, not_178_out, not_179_out, not_180_out, not_181_out, not_182_out, not_183_out,
       not_184_out, not_185_out, not_186_out, not_187_out, not_188_out, not_189_out, not_190_out,
       not_191_out, not_192_out, not_193_out, not_194_out, not_195_out, not_196_out, not_197_out,
       not_198_out, not_199_out, not_200_out, not_201_out, not_202_out, not_203_out, not_204_out,
       not_205_out, not_206_out, not_207_out, not_208_out, not_209_out, not_210_out, not_211_out,
       not_212_out, not_213_out, not_214_out, not_215_out, not_216_out, not_217_out, not_218_out,
       not_219_out, not_220_out, not_221_out, not_222_out, not_223_out, not_224_out, not_225_out,
       not_226_out, not_227_out, not_228_out, not_229_out, not_230_out, not_231_out, not_232_out,
       not_233_out, not_234_out, not_235_out, not_236_out, not_237_out, not_238_out, not_239_out,
       not_240_out, not_241_out, not_242_out, not_243_out, not_244_out, not_245_out, not_246_out,
       not_247_out, not_248_out, not_249_out, not_250_out, not_251_out, not_252_out, not_253_out,
       not_254_out, not_255_out, not_256_out, not_257_out, not_258_out, not_259_out, not_260_out,
       not_261_out, not_262_out, not_263_out, not_264_out, not_265_out, not_266_out, not_267_out,
       not_268_out, not_269_out, not_270_out, not_271_out, not_272_out, not_273_out, not_274_out,
       not_275_out, not_276_out, not_277_out, not_278_out, not_279_out, not_280_out, not_281_out,
       not_282_out, not_283_out, not_284_out, not_285_out, not_286_out, not_287_out, not_288_out,
       not_289_out, not_290_out, not_291_out, not_292_out, not_293_out, not_294_out, not_295_out,
       not_296_out, not_297_out, not_298_out, not_299_out;

  not not_1 (not_1_out, OP5);
  not not_2 (not_2_out, OP4);
  not not_3 (not_3_out, OP3);
  not not_4 (not_4_out, OP2);
  not not_5 (not_5_out, OP1);
  not not_6 (not_6_out, OP0);
  not not_7 (not_7_out, F5);
  not not_8 (not_8_out, F4);
  not not_9 (not_9_out, F3);
  not not_10 (not_10_out, F2);
  not not_11 (not_11_out, F0);
  not not_12 (not_12_out, OP5);
  not not_13 (not_13_out, OP4);
  not not_14 (not_14_out, OP3);
  not not_15 (not_15_out, OP2);
  not not_16 (not_16_out, OP1);
  not not_17 (not_17_out, OP0);
  not not_18 (not_18_out, F4);
  not not_19 (not_19_out, F3);
  not not_20 (not_20_out, F2);
  not not_21 (not_21_out, F1);
  not not_22 (not_22_out, F0);
  not not_23 (not_23_out, OP5);
  not not_24 (not_24_out, OP4);
  not not_25 (not_25_out, OP3);
  not not_26 (not_26_out, OP2);
  not not_27 (not_27_out, OP1);
  not not_28 (not_28_out, OP0);
  not not_29 (not_29_out, F4);
  not not_30 (not_30_out, F3);
  not not_31 (not_31_out, F2);
  not not_32 (not_32_out, F1);
  not not_33 (not_33_out, OP5);
  not not_34 (not_34_out, OP4);
  not not_35 (not_35_out, OP3);
  not not_36 (not_36_out, OP2);
  not not_37 (not_37_out, OP1);
  not not_38 (not_38_out, OP0);
  not not_39 (not_39_out, F4);
  not not_40 (not_40_out, F3);
  not not_41 (not_41_out, F2);
  not not_42 (not_42_out, F0);
  not not_43 (not_43_out, OP5);
  not not_44 (not_44_out, OP4);
  not not_45 (not_45_out, OP3);
  not not_46 (not_46_out, OP2);
  not not_47 (not_47_out, OP1);
  not not_48 (not_48_out, OP0);
  not not_49 (not_49_out, F4);
  not not_50 (not_50_out, F3);
  not not_51 (not_51_out, F1);
  not not_52 (not_52_out, F0);
  not not_53 (not_53_out, OP5);
  not not_54 (not_54_out, OP4);
  not not_55 (not_55_out, OP3);
  not not_56 (not_56_out, OP2);
  not not_57 (not_57_out, OP1);
  not not_58 (not_58_out, OP0);
  not not_59 (not_59_out, F4);
  not not_60 (not_60_out, F3);
  not not_61 (not_61_out, F1);
  not not_62 (not_62_out, OP5);
  not not_63 (not_63_out, OP4);
  not not_64 (not_64_out, OP3);
  not not_65 (not_65_out, OP2);
  not not_66 (not_66_out, OP1);
  not not_67 (not_67_out, OP0);
  not not_68 (not_68_out, F4);
  not not_69 (not_69_out, F3);
  not not_70 (not_70_out, OP5);
  not not_71 (not_71_out, OP4);
  not not_72 (not_72_out, OP3);
  not not_73 (not_73_out, OP2);
  not not_74 (not_74_out, OP1);
  not not_75 (not_75_out, OP0);
  not not_76 (not_76_out, F4);
  not not_77 (not_77_out, F2);
  not not_78 (not_78_out, F0);
  not not_79 (not_79_out, OP5);
  not not_80 (not_80_out, OP4);
  not not_81 (not_81_out, OP3);
  not not_82 (not_82_out, OP2);
  not not_83 (not_83_out, OP1);
  not not_84 (not_84_out, OP0);
  not not_85 (not_85_out, F4);
  not not_86 (not_86_out, F2);
  not not_87 (not_87_out, OP5);
  not not_88 (not_88_out, OP4);
  not not_89 (not_89_out, OP3);
  not not_90 (not_90_out, OP2);
  not not_91 (not_91_out, OP1);
  not not_92 (not_92_out, OP0);
  not not_93 (not_93_out, F5);
  not not_94 (not_94_out, F4);
  not not_95 (not_95_out, F2);
  not not_96 (not_96_out, F1);
  not not_97 (not_97_out, F0);
  not not_98 (not_98_out, OP5);
  not not_99 (not_99_out, OP4);
  not not_100 (not_100_out, OP3);
  not not_101 (not_101_out, OP2);
  not not_102 (not_102_out, OP1);
  not not_103 (not_103_out, OP0);
  not not_104 (not_104_out, F5);
  not not_105 (not_105_out, F4);
  not not_106 (not_106_out, F1);
  not not_107 (not_107_out, F0);
  not not_108 (not_108_out, OP5);
  not not_109 (not_109_out, OP4);
  not not_110 (not_110_out, OP3);
  not not_111 (not_111_out, OP1);
  not not_112 (not_112_out, OP0);
  not not_113 (not_113_out, OP5);
  not not_114 (not_114_out, OP4);
  not not_115 (not_115_out, OP3);
  not not_116 (not_116_out, OP1);
  not not_117 (not_117_out, OP5);
  not not_118 (not_118_out, OP4);
  not not_119 (not_119_out, OP2);
  not not_120 (not_120_out, OP1);
  not not_121 (not_121_out, OP0);
  not not_122 (not_122_out, OP5);
  not not_123 (not_123_out, OP4);
  not not_124 (not_124_out, OP1);
  not not_125 (not_125_out, OP0);
  not not_126 (not_126_out, OP5);
  not not_127 (not_127_out, OP4);
  not not_128 (not_128_out, OP2);
  not not_129 (not_129_out, OP1);
  not not_130 (not_130_out, OP5);
  not not_131 (not_131_out, OP4);
  not not_132 (not_132_out, OP2);
  not not_133 (not_133_out, OP0);
  not not_134 (not_134_out, OP5);
  not not_135 (not_135_out, OP4);
  not not_136 (not_136_out, OP1);
  not not_137 (not_137_out, OP4);
  not not_138 (not_138_out, OP3);
  not not_139 (not_139_out, OP2);
  not not_140 (not_140_out, OP4);
  not not_141 (not_141_out, OP2);
  not not_142 (not_142_out, OP5);
  not not_143 (not_143_out, OP4);
  not not_144 (not_144_out, OP3);
  not not_145 (not_145_out, OP2);
  not not_146 (not_146_out, OP1);
  not not_147 (not_147_out, OP0);
  not not_148 (not_148_out, F5);
  not not_149 (not_149_out, F4);
  not not_150 (not_150_out, F3);
  not not_151 (not_151_out, F1);
  not not_152 (not_152_out, F0);
  not not_153 (not_153_out, OP4);
  not not_154 (not_154_out, OP2);
  not not_155 (not_155_out, OP1);
  not not_156 (not_156_out, OP0);
  not not_157 (not_157_out, OP5);
  not not_158 (not_158_out, OP4);
  not not_159 (not_159_out, OP3);
  not not_160 (not_160_out, OP5);
  not not_161 (not_161_out, OP4);
  not not_162 (not_162_out, OP3);
  not not_163 (not_163_out, OP2);
  not not_164 (not_164_out, OP1);
  not not_165 (not_165_out, OP0);
  not not_166 (not_166_out, F5);
  not not_167 (not_167_out, F4);
  not not_168 (not_168_out, F3);
  not not_169 (not_169_out, F2);
  not not_170 (not_170_out, F1);
  not not_171 (not_171_out, F0);
  not not_172 (not_172_out, OP5);
  not not_173 (not_173_out, OP4);
  not not_174 (not_174_out, OP3);
  not not_175 (not_175_out, OP2);
  not not_176 (not_176_out, OP1);
  not not_177 (not_177_out, OP0);
  not not_178 (not_178_out, F5);
  not not_179 (not_179_out, F4);
  not not_180 (not_180_out, F3);
  not not_181 (not_181_out, F2);
  not not_182 (not_182_out, OP5);
  not not_183 (not_183_out, OP4);
  not not_184 (not_184_out, OP3);
  not not_185 (not_185_out, OP2);
  not not_186 (not_186_out, OP1);
  not not_187 (not_187_out, OP0);
  not not_188 (not_188_out, F5);
  not not_189 (not_189_out, F4);
  not not_190 (not_190_out, F3);
  not not_191 (not_191_out, F2);
  not not_192 (not_192_out, F0);
  not not_193 (not_193_out, OP5);
  not not_194 (not_194_out, OP4);
  not not_195 (not_195_out, OP3);
  not not_196 (not_196_out, OP2);
  not not_197 (not_197_out, OP1);
  not not_198 (not_198_out, OP0);
  not not_199 (not_199_out, F4);
  not not_200 (not_200_out, F3);
  not not_201 (not_201_out, F2);
  not not_202 (not_202_out, F1);
  not not_203 (not_203_out, F0);
  not not_204 (not_204_out, OP5);
  not not_205 (not_205_out, OP4);
  not not_206 (not_206_out, OP3);
  not not_207 (not_207_out, OP2);
  not not_208 (not_208_out, OP1);
  not not_209 (not_209_out, OP0);
  not not_210 (not_210_out, F4);
  not not_211 (not_211_out, F3);
  not not_212 (not_212_out, F2);
  not not_213 (not_213_out, F1);
  not not_214 (not_214_out, OP5);
  not not_215 (not_215_out, OP4);
  not not_216 (not_216_out, OP3);
  not not_217 (not_217_out, OP2);
  not not_218 (not_218_out, OP1);
  not not_219 (not_219_out, OP0);
  not not_220 (not_220_out, F4);
  not not_221 (not_221_out, F3);
  not not_222 (not_222_out, F2);
  not not_223 (not_223_out, F0);
  not not_224 (not_224_out, OP5);
  not not_225 (not_225_out, OP4);
  not not_226 (not_226_out, OP3);
  not not_227 (not_227_out, OP2);
  not not_228 (not_228_out, OP1);
  not not_229 (not_229_out, OP0);
  not not_230 (not_230_out, F4);
  not not_231 (not_231_out, F3);
  not not_232 (not_232_out, F1);
  not not_233 (not_233_out, F0);
  not not_234 (not_234_out, OP5);
  not not_235 (not_235_out, OP4);
  not not_236 (not_236_out, OP3);
  not not_237 (not_237_out, OP2);
  not not_238 (not_238_out, OP1);
  not not_239 (not_239_out, OP0);
  not not_240 (not_240_out, F4);
  not not_241 (not_241_out, F3);
  not not_242 (not_242_out, F1);
  not not_243 (not_243_out, OP5);
  not not_244 (not_244_out, OP4);
  not not_245 (not_245_out, OP3);
  not not_246 (not_246_out, OP2);
  not not_247 (not_247_out, OP1);
  not not_248 (not_248_out, OP0);
  not not_249 (not_249_out, F4);
  not not_250 (not_250_out, F3);
  not not_251 (not_251_out, OP5);
  not not_252 (not_252_out, OP4);
  not not_253 (not_253_out, OP3);
  not not_254 (not_254_out, OP2);
  not not_255 (not_255_out, OP1);
  not not_256 (not_256_out, OP0);
  not not_257 (not_257_out, F4);
  not not_258 (not_258_out, F2);
  not not_259 (not_259_out, F0);
  not not_260 (not_260_out, OP5);
  not not_261 (not_261_out, OP4);
  not not_262 (not_262_out, OP3);
  not not_263 (not_263_out, OP2);
  not not_264 (not_264_out, OP1);
  not not_265 (not_265_out, OP0);
  not not_266 (not_266_out, F4);
  not not_267 (not_267_out, F2);
  not not_268 (not_268_out, OP5);
  not not_269 (not_269_out, OP4);
  not not_270 (not_270_out, OP3);
  not not_271 (not_271_out, OP2);
  not not_272 (not_272_out, OP1);
  not not_273 (not_273_out, OP0);
  not not_274 (not_274_out, F5);
  not not_275 (not_275_out, F4);
  not not_276 (not_276_out, F1);
  not not_277 (not_277_out, F0);
  not not_278 (not_278_out, OP5);
  not not_279 (not_279_out, OP4);
  not not_280 (not_280_out, OP3);
  not not_281 (not_281_out, OP1);
  not not_282 (not_282_out, OP0);
  not not_283 (not_283_out, OP5);
  not not_284 (not_284_out, OP4);
  not not_285 (not_285_out, OP3);
  not not_286 (not_286_out, OP1);
  not not_287 (not_287_out, OP4);
  not not_288 (not_288_out, OP2);
  not not_289 (not_289_out, OP5);
  not not_290 (not_290_out, OP4);
  not not_291 (not_291_out, OP3);
  not not_292 (not_292_out, OP2);
  not not_293 (not_293_out, OP1);
  not not_294 (not_294_out, OP0);
  not not_295 (not_295_out, F5);
  not not_296 (not_296_out, F4);
  not not_297 (not_297_out, F3);
  not not_298 (not_298_out, F1);
  not not_299 (not_299_out, F0);
  and and_1 (and_1_out, not_1_out, not_2_out, not_3_out, not_4_out, not_5_out, not_6_out, not_7_out, not_8_out, not_9_out, not_10_out, F1, not_11_out);
  and and_2 (and_2_out, not_12_out, not_13_out, not_14_out, not_15_out, not_16_out, not_17_out, F5, not_18_out, not_19_out, not_20_out, not_21_out, not_22_out);
  and and_3 (and_3_out, not_23_out, not_24_out, not_25_out, not_26_out, not_27_out, not_28_out, F5, not_29_out, not_30_out, not_31_out, not_32_out, F0);
  and and_4 (and_4_out, not_33_out, not_34_out, not_35_out, not_36_out, not_37_out, not_38_out, F5, not_39_out, not_40_out, not_41_out, F1, not_42_out);
  and and_5 (and_5_out, not_43_out, not_44_out, not_45_out, not_46_out, not_47_out, not_48_out, F5, not_49_out, not_50_out, F2, not_51_out, not_52_out);
  and and_6 (and_6_out, not_53_out, not_54_out, not_55_out, not_56_out, not_57_out, not_58_out, F5, not_59_out, not_60_out, F2, not_61_out, F0);
  and and_7 (and_7_out, not_62_out, not_63_out, not_64_out, not_65_out, not_66_out, not_67_out, F5, not_68_out, not_69_out, F2, F1, F0);
  and and_8 (and_8_out, not_70_out, not_71_out, not_72_out, not_73_out, not_74_out, not_75_out, F5, not_76_out, F3, not_77_out, F1, not_78_out);
  and and_9 (and_9_out, not_79_out, not_80_out, not_81_out, not_82_out, not_83_out, not_84_out, F5, not_85_out, F3, not_86_out, F1, F0);
  and and_10 (and_10_out, not_87_out, not_88_out, not_89_out, not_90_out, not_91_out, not_92_out, not_93_out, not_94_out, F3, not_95_out, not_96_out, not_97_out);
  and and_11 (and_11_out, not_98_out, not_99_out, not_100_out, not_101_out, not_102_out, not_103_out, not_104_out, not_105_out, F3, F2, not_106_out, not_107_out);
  and and_12 (and_12_out, not_108_out, not_109_out, not_110_out, OP2, not_111_out, not_112_out);
  and and_13 (and_13_out, not_113_out, not_114_out, not_115_out, OP2, not_116_out, OP0);
  and and_14 (and_14_out, not_117_out, not_118_out, OP3, not_119_out, not_120_out, not_121_out);
  and and_15 (and_15_out, not_122_out, not_123_out, OP3, OP2, not_124_out, not_125_out);
  and and_16 (and_16_out, not_126_out, not_127_out, OP3, not_128_out, not_129_out, OP0);
  and and_17 (and_17_out, not_130_out, not_131_out, OP3, not_132_out, OP1, not_133_out);
  and and_18 (and_18_out, not_134_out, not_135_out, OP3, OP2, not_136_out, OP0);
  and and_19 (and_19_out, OP5, not_137_out, not_138_out, not_139_out, OP1, OP0);
  and and_20 (and_20_out, OP5, not_140_out, OP3, not_141_out, OP1, OP0);
  and and_21 (and_21_out, not_142_out, not_143_out, not_144_out, not_145_out, not_146_out, not_147_out, not_148_out, not_149_out, not_150_out, F2, not_151_out, not_152_out);
  and and_22 (and_22_out, OP5, not_153_out, OP3, not_154_out, not_155_out, not_156_out);
  and and_23 (and_23_out, not_157_out, not_158_out, not_159_out, OP2, OP1, OP0);
  and and_24 (and_24_out, not_160_out, not_161_out, not_162_out, not_163_out, not_164_out, not_165_out, not_166_out, not_167_out, not_168_out, not_169_out, not_170_out, not_171_out);
  and and_25 (and_25_out, not_172_out, not_173_out, not_174_out, not_175_out, not_176_out, not_177_out, not_178_out, not_179_out, not_180_out, not_181_out, F1, F0);
  and and_26 (and_26_out, not_182_out, not_183_out, not_184_out, not_185_out, not_186_out, not_187_out, not_188_out, not_189_out, not_190_out, not_191_out, F1, not_192_out);
  and and_27 (and_27_out, not_193_out, not_194_out, not_195_out, not_196_out, not_197_out, not_198_out, F5, not_199_out, not_200_out, not_201_out, not_202_out, not_203_out);
  and and_28 (and_28_out, not_204_out, not_205_out, not_206_out, not_207_out, not_208_out, not_209_out, F5, not_210_out, not_211_out, not_212_out, not_213_out, F0);
  and and_29 (and_29_out, not_214_out, not_215_out, not_216_out, not_217_out, not_218_out, not_219_out, F5, not_220_out, not_221_out, not_222_out, F1, not_223_out);
  and and_30 (and_30_out, not_224_out, not_225_out, not_226_out, not_227_out, not_228_out, not_229_out, F5, not_230_out, not_231_out, F2, not_232_out, not_233_out);
  and and_31 (and_31_out, not_234_out, not_235_out, not_236_out, not_237_out, not_238_out, not_239_out, F5, not_240_out, not_241_out, F2, not_242_out, F0);
  and and_32 (and_32_out, not_243_out, not_244_out, not_245_out, not_246_out, not_247_out, not_248_out, F5, not_249_out, not_250_out, F2, F1, F0);
  and and_33 (and_33_out, not_251_out, not_252_out, not_253_out, not_254_out, not_255_out, not_256_out, F5, not_257_out, F3, not_258_out, F1, not_259_out);
  and and_34 (and_34_out, not_260_out, not_261_out, not_262_out, not_263_out, not_264_out, not_265_out, F5, not_266_out, F3, not_267_out, F1, F0);
  and and_35 (and_35_out, not_268_out, not_269_out, not_270_out, not_271_out, not_272_out, not_273_out, not_274_out, not_275_out, F3, F2, not_276_out, not_277_out);
  and and_36 (and_36_out, not_278_out, not_279_out, not_280_out, OP2, not_281_out, not_282_out);
  and and_37 (and_37_out, not_283_out, not_284_out, not_285_out, OP2, not_286_out, OP0);
  and and_38 (and_38_out, OP5, not_287_out, OP3, not_288_out, OP1, OP0);
  and and_39 (and_39_out, not_289_out, not_290_out, not_291_out, not_292_out, not_293_out, not_294_out, not_295_out, not_296_out, not_297_out, F2, not_298_out, not_299_out);
  or or_1 (R1_used, and_1_out, and_2_out, and_3_out, and_4_out, and_5_out, and_6_out, and_7_out, and_8_out, and_9_out, and_10_out, and_11_out, and_12_out, and_13_out, and_14_out, and_15_out, and_16_out, and_17_out, and_18_out, and_19_out, and_20_out, and_21_out, and_22_out, and_23_out);
  or or_2 (R2_used, and_24_out, and_25_out, and_26_out, and_27_out, and_28_out, and_29_out, and_30_out, and_31_out, and_32_out, and_33_out, and_34_out, and_35_out, and_36_out, and_37_out, and_38_out, and_39_out);
endmodule

module \数据相关检测  (
  input  MEM_WriteReg,
  input  EX_WriteReg,
  input  [4:0] R1_num,
  input  [4:0] MEM_WriteReg_num,
  input  [4:0] R2_num,
  input  [4:0] EX_WriteReg_num,
  input  [5:0] OP,
  input  [5:0] FUNC,
  output Correlated
);

  wire and_1_out, and_2_out, and_3_out, and_4_out, and_5_out, and_6_out, comparator_1_eq, comparator_2_eq,
       comparator_3_eq, comparator_4_eq, comparator_5_eq, comparator_6_eq, or_1_out, or_2_out,
       \源寄存器使用判断_1_r1_used , \源寄存器使用判断_1_r2_used ;

  Comparator #(.width(5), .mode("twosComplement")) comparator_1 (
    .a(R1_num), .b(MEM_WriteReg_num), .eq(comparator_1_eq));  // open: gt, lt
  Comparator #(.width(5), .mode("twosComplement")) comparator_2 (
    .a(R1_num), .b(EX_WriteReg_num), .eq(comparator_2_eq));  // open: gt, lt
  Comparator #(.width(5), .mode("twosComplement")) comparator_3 (
    .a(R1_num), .b({5{1'b0}}), .eq(comparator_3_eq));  // open: gt, lt
  Comparator #(.width(5), .mode("twosComplement")) comparator_4 (
    .a(R2_num), .b(MEM_WriteReg_num), .eq(comparator_4_eq));  // open: gt, lt
  Comparator #(.width(5), .mode("twosComplement")) comparator_5 (
    .a(R2_num), .b(EX_WriteReg_num), .eq(comparator_5_eq));  // open: gt, lt
  Comparator #(.width(5), .mode("twosComplement")) comparator_6 (
    .a(R2_num), .b({5{1'b0}}), .eq(comparator_6_eq));  // open: gt, lt
  \源寄存器使用判断  \u_源寄存器使用判断_1  (
    .OP0(OP[0]), .OP1(OP[1]), .OP2(OP[2]), .OP3(OP[3]), .OP4(OP[4]), .OP5(OP[5]), .F0(FUNC[0]), .F1(FUNC[1]),
    .F2(FUNC[2]), .F3(FUNC[3]), .F4(FUNC[4]), .F5(FUNC[5]), .R1_used(\源寄存器使用判断_1_r1_used ),
    .R2_used(\源寄存器使用判断_1_r2_used ));
  and and_1 (and_1_out, MEM_WriteReg, comparator_1_eq);
  and and_2 (and_2_out, EX_WriteReg, comparator_2_eq);
  and and_3 (and_3_out, MEM_WriteReg, comparator_4_eq);
  and and_4 (and_4_out, EX_WriteReg, comparator_5_eq);
  or or_1 (or_1_out, and_1_out, and_2_out);
  or or_2 (or_2_out, and_3_out, and_4_out);
  and and_5 (and_5_out, or_1_out, ~comparator_3_eq, \源寄存器使用判断_1_r1_used );  // AND_Gate
  and and_6 (and_6_out, or_2_out, ~comparator_6_eq, \源寄存器使用判断_1_r2_used );  // AND_Gate
  or or_3 (Correlated, and_5_out, and_6_out);
endmodule

module \重定向数据相关检测  (
  input  MEM_RegWrite,
  input  EX_RegWrite,
  input  [4:0] R1_num,
  input  [4:0] MEM_WriteReg_num,
  input  [4:0] R2_num,
  input  [4:0] EX_WriteReg_num,
  input  isLW,
  input  [5:0] OP,
  input  [5:0] FUNC,
  output [1:0] R1,
  output LoadUse,
  output [1:0] R2
);

  wire and_1_out, and_2_out, and_3_out, and_4_out, comparator_1_eq, comparator_2_eq, comparator_3_eq,
       comparator_4_eq, comparator_5_eq, comparator_6_eq, or_1_out, \源寄存器使用判断_1_r1_used ,
       \源寄存器使用判断_1_r2_used ;
  wire [1:0] and_7_out, and_8_out;

  Comparator #(.width(5), .mode("twosComplement")) comparator_1 (
    .a(R1_num), .b(MEM_WriteReg_num), .eq(comparator_1_eq));  // open: gt, lt
  Comparator #(.width(5), .mode("twosComplement")) comparator_2 (
    .a(R1_num), .b(EX_WriteReg_num), .eq(comparator_2_eq));  // open: gt, lt
  Comparator #(.width(5), .mode("twosComplement")) comparator_3 (
    .a(R1_num), .b({5{1'b0}}), .eq(comparator_3_eq));  // open: gt, lt
  Comparator #(.width(5), .mode("twosComplement")) comparator_4 (
    .a(R2_num), .b(MEM_WriteReg_num), .eq(comparator_4_eq));  // open: gt, lt
  Comparator #(.width(5), .mode("twosComplement")) comparator_5 (
    .a(R2_num), .b(EX_WriteReg_num), .eq(comparator_5_eq));  // open: gt, lt
  Comparator #(.width(5), .mode("twosComplement")) comparator_6 (
    .a(R2_num), .b({5{1'b0}}), .eq(comparator_6_eq));  // open: gt, lt
  \源寄存器使用判断  \u_源寄存器使用判断_1  (
    .OP0(OP[0]), .OP1(OP[1]), .OP2(OP[2]), .OP3(OP[3]), .OP4(OP[4]), .OP5(OP[5]), .F0(FUNC[0]), .F1(FUNC[1]),
    .F2(FUNC[2]), .F3(FUNC[3]), .F4(FUNC[4]), .F5(FUNC[5]), .R1_used(\源寄存器使用判断_1_r1_used ),
    .R2_used(\源寄存器使用判断_1_r2_used ));
  and and_1 (and_1_out, MEM_RegWrite, comparator_1_eq);
  and and_2 (and_2_out, EX_RegWrite, comparator_2_eq);
  and and_3 (and_3_out, MEM_RegWrite, comparator_4_eq);
  and and_4 (and_4_out, EX_RegWrite, comparator_5_eq);
  and and_5 (and_7_out[1], and_1_out, ~comparator_3_eq, \源寄存器使用判断_1_r1_used );  // AND_Gate
  and and_6 (and_8_out[1], and_3_out, ~comparator_6_eq, \源寄存器使用判断_1_r2_used );  // AND_Gate
  and and_7 (and_7_out[0], and_2_out, ~comparator_3_eq, \源寄存器使用判断_1_r1_used );  // AND_Gate
  and and_8 (and_8_out[0], and_4_out, ~comparator_6_eq, \源寄存器使用判断_1_r2_used );  // AND_Gate
  or or_1 (or_1_out, and_7_out[0], and_8_out[0]);
  Multiplexer #(.select(1), .width(2), .disabled("Z"), .enable("false")) multiplexer_1 (
    .in0(and_7_out), .in1(2'b00), .out(R1), .sel(LoadUse));
  and and_9 (LoadUse, or_1_out, isLW);
  Multiplexer #(.select(1), .width(2), .disabled("Z"), .enable("false")) multiplexer_2 (
    .in0(and_8_out), .in1(2'b00), .out(R2), .sel(LoadUse));
endmodule

module \重定向流水线_单级中断  (
  output RegWrite,
  output MemWrite,
  output [31:0] IF_PC,
  output [31:0] ID_PC,
  output [31:0] EX_PC,
  output [31:0] M_PC,
  output [31:0] WB_PC,
  output [31:0] RDin,
  output [31:0] MDin,
  output [31:0] LedData
);

  wire and_1_out, and_2_out, and_3_out, and_4_out, and_5_out, and_6_out, and_7_out, and_8_out, and_9_out,
       and_10_out, and_11_out, Branch, Clear, CLK, clock_1_out, clock_2_out, comparator_1_eq,
       comparator_2_eq, comparator_3_eq, comparator_4_eq, comparator_5_eq, comparator_6_eq, comparator_6_lt,
       comparator_7_gt, comparator_8_eq, d_ff_1_q, decoder_1_out1, decoder_1_out2, decoder_1_out3, En, ERET,
       EX_Beq, EX_BGTZ, EX_Bne, EX_JAL, EX_JMP, EX_JR, ex_mem_1_eret_out, ex_mem_1_memtoreg_out,
       ex_mem_1_syscall_out, EX_RegDst, EX_RegWrite, Go, id_ex_1_alusrcb_out, id_ex_1_eret_out,
       id_ex_1_memtoreg_out, id_ex_1_memwrite_out, id_ex_1_sb_out, id_ex_1_syscall_out, IE_ctrl, IR1,
       IR1_2_q, IR1_3_q, IR1_q, ir1_t, IR2, ir2_t, IR3, ir3_t, LoadUse, MEM_JAL, MEM_RegDst, MEM_RegWrite,
       MEM_SB, mem_wb_1_jal_out, mem_wb_1_memtoreg_out, mem_wb_1_reddst_out, mem_wb_1_syscall_out,
       mips_alu_1_equal, nand_1_out, not_1_out, or_1_out, or_2_out, or_4_out, or_5_out, or_7_out, or_11_out,
       or_12_out, or_13_out, or_14_out, priority_encoder_1_gs, register_4_q, register_5_q, RST, Rst1, Rst2,
       Rst3, SignedExt, undriven, undriven_3, undriven_4, W1, W2, W3, WB_ERET, \单周期硬布线控制器_1_alu_src ,
       \单周期硬布线控制器_1_beq , \单周期硬布线控制器_1_bgtz , \单周期硬布线控制器_1_bne , \单周期硬布线控制器_1_jal , \单周期硬布线控制器_1_jmp ,
       \单周期硬布线控制器_1_jr , \单周期硬布线控制器_1_lui , \单周期硬布线控制器_1_memtoreg , \单周期硬布线控制器_1_memwrite ,
       \单周期硬布线控制器_1_regdst , \单周期硬布线控制器_1_regwrite , \单周期硬布线控制器_1_sb , \单周期硬布线控制器_1_sllv ,
       \单周期硬布线控制器_1_syscall ;
  wire [1:0] priority_encoder_1_out, R1_Forward, R2_Forward, register_6_q, \重定向数据相关检测_1_r1 , \重定向数据相关检测_1_r2 ;
  wire [3:0] id_ex_1_aluop_out, \单周期硬布线控制器_1_alu_op ;
  wire [4:0] EX_Shamt, multiplexer_3_out, multiplexer_4_out, multiplexer_5_out, multiplexer_6_out,
       multiplexer_17_out, multiplexer_19_out, R1_num, R2_num, undriven_2;
  wire [5:0] Func;
  wire [12:0] CNT_num;
  wire [15:0] \LoadUse次数 , \总周期数 , \插入气泡数 , \无条件分支数 , \条件分支成功数 ;
  wire [15:8] ram_1_data_2;
  wire [31:0] adder_2_out, adder_3_out, adder_4_out, bit_extender_1_out, bit_extender_2_out,
       controlled_buffer_2_out, EPC, EX_A, EX_AluA, EX_B, EX_B_mux, EX_Imm, EX_IR, ex_mem_1_a_out, IF_IR,
       MEM_AluResult, MEM_IR, mem_wb_1_a_out, mem_wb_1_aluresult_out, mem_wb_1_b_out, mem_wb_1_memdata_out,
       mips_alu_1_result, mips_regifile_1_r1, mips_regifile_1_r2, multiplexer_1_out, multiplexer_2_out,
       multiplexer_9_out, multiplexer_12_out, multiplexer_14_out, multiplexer_15_out, multiplexer_16_out,
       PC_4, ram_1_data, shifter_1_out, WB_IR, \中断入口地址 ;
  wire [31:6] ID_IR;

  Button \u_总复位  (.out(RST));
  Button _1 (.out(IR1));
  Button _2 (.out(IR2));
  Button _3 (.out(IR3));
  // Probe on \总周期数 
  // Probe on \总周期数 
  Button \u_继续运行  (.out(Go));
  LED #(.active("true")) led_1 (.in(W1));
  LED #(.active("true")) led_2 (.in(W2));
  LED #(.active("true")) led_3 (.in(W3));
  Multiplexer #(.select(1), .width(32), .disabled("Z"), .enable("false")) multiplexer_1 (
    .in0(controlled_buffer_2_out), .in1(\中断入口地址 ), .out(multiplexer_1_out), .sel(IE_ctrl));
  Multiplexer #(.select(1), .width(32), .disabled("Z"), .enable("false")) multiplexer_2 (
    .in0(multiplexer_1_out), .in1(EPC), .out(multiplexer_2_out), .sel(WB_ERET));
  Hex_Digit_Display hex_digit_display_1 (.value(LedData[31:28]));  // open: dp
  // Probe on IF_PC[19:0]
  // Mips_Probe mips_probe_1: pin names not known; wires that end beside it: IF_IR
  Comparator #(.width(16), .mode("twosComplement")) comparator_1 (
    .a(16'h23b), .b(\总周期数 ), .eq(comparator_1_eq));  // open: gt, lt
  Comparator #(.width(16), .mode("twosComplement")) comparator_2 (
    .a(\总周期数 ), .b(16'h1), .eq(comparator_2_eq));  // open: gt, lt
  Comparator #(.width(16), .mode("twosComplement")) comparator_3 (
    .a(\总周期数 ), .b(16'h4), .eq(comparator_3_eq));  // open: gt, lt
  Comparator #(.width(16), .mode("twosComplement")) comparator_4 (
    .a(\总周期数 ), .b(16'h7), .eq(comparator_4_eq));  // open: gt, lt
  and and_1 (and_1_out, ~LoadUse, En);  // AND_Gate
  Hex_Digit_Display hex_digit_display_2 (.value(LedData[23:20]));  // open: dp
  Hex_Digit_Display hex_digit_display_3 (.value(LedData[27:24]));  // open: dp
  // Probe on ID_PC[19:0]
  // Mips_Probe mips_probe_2: pin names not known; wires that end beside it: {ID_IR, Func}
  or or_1 (or_1_out, comparator_1_eq, comparator_2_eq);
  assign IR1 = or_1_out ? ~CLK : 1'bz;  // Controlled_Inverter controlled_inverter_1
  assign IR2 = comparator_3_eq ? ~CLK : 1'bz;  // Controlled_Inverter controlled_inverter_2
  assign IR3 = comparator_4_eq ? ~CLK : 1'bz;  // Controlled_Inverter controlled_inverter_3
  Register #(.width(32), .trigger("rising"), .Select("low")) PC (
    .D(multiplexer_2_out), .en(and_1_out), .Q(IF_PC), .clk(CLK));  // open: clr
  Hex_Digit_Display hex_digit_display_4 (.value(LedData[19:16]));  // open: dp
  Hex_Digit_Display hex_digit_display_5 (.value(LedData[15:12]));  // open: dp
  Pull_Resistor #(.pull(0)) pull_resistor_1 (.node(IR1));
  Pull_Resistor #(.pull(0)) pull_resistor_2 (.node(IR2));
  Pull_Resistor #(.pull(0)) pull_resistor_3 (.node(IR3));
  Adder #(.width(32)) adder_1 (.a(32'h4), .b(IF_PC), .out(PC_4));  // open: cin, cout
  Hex_Digit_Display hex_digit_display_6 (.value(LedData[11:8]));  // open: dp
  Hex_Digit_Display hex_digit_display_7 (.value(LedData[7:4]));  // open: dp
  Clock #(.highDuration(1), .lowDuration(1)) clock_1 (.out(clock_1_out));
  // Probe on EX_PC[19:0]
  // Mips_Probe mips_probe_3: pin names not known; wires that end beside it: clock_1_out, EX_IR, CLK
  Hex_Digit_Display hex_digit_display_8 (.value(LedData[3:0]));  // open: dp
  // Mips_Probe mips_probe_4: pin names not known; wires that end beside it: IF_IR
  ROM #(.addrWidth(10), .dataWidth(32), .Select("low")) rom_1 (.addr(IF_PC[11:2]), .data(IF_IR));
  // Probe on \总周期数 
  // Probe on M_PC[19:0]
  // Mips_Probe mips_probe_5: pin names not known; wires that end beside it: MEM_IR
  or or_2 (or_2_out, IE_ctrl, Clear, RST, WB_ERET);
  Multiplexer #(.select(1), .width(5), .disabled("Z"), .enable("false")) multiplexer_3 (
    .in0(MEM_IR[20:16]), .in1(MEM_IR[15:11]), .out(multiplexer_3_out), .sel(MEM_RegDst));
  Multiplexer #(.select(1), .width(5), .disabled("Z"), .enable("false")) multiplexer_4 (
    .in0(EX_IR[20:16]), .in1(EX_IR[15:11]), .out(multiplexer_4_out), .sel(EX_RegDst));
  // Probe on \总周期数 
  // Probe on \无条件分支数 
  // Probe on \条件分支成功数 
  // Probe on \插入气泡数 
  // Probe on \LoadUse次数 
  IF_ID if_id_1 (
    .IR_in(IF_IR), .PC_in(IF_PC), .IR_out({ID_IR, Func}), .PC_out(ID_PC), .CLR(or_2_out), .Stall(LoadUse),
    .CLK(CLK));  // open: RedDst_in, AluSrcB_in, Shamt_in, Syscall_in, RegWrite_in, JMP_in, AluOp_in, JAL_in, JR_in, MemWrite_in, PredictJMP_in, SLLV_in, Beq_in, LUI_in, Bne_in, A_in, SB_in, MemToReg_in, BGTZ_in, B_in, Imm_in, RedDst_out, AluSrcB_out, Syscall_out, Shamt_out, RegWrite_out, JMP_out, AluOp_out, JAL_out, JR_out, MemWrite_out, PredictJMP_out, SLLV_out, Beq_out, A_out, LUI_out, Bne_out, SB_out, MemToReg_out, B_out, BGTZ_out, Imm_out
  Multiplexer #(.select(1), .width(5), .disabled("Z"), .enable("false")) multiplexer_5 (
    .in0(multiplexer_4_out), .in1({5{1'b1}}), .out(multiplexer_5_out), .sel(EX_JAL));
  // Probe on IF_PC[11:0]
  // Probe on WB_PC[19:0]
  // Mips_Probe mips_probe_6: pin names not known; wires that end beside it: WB_IR
  Multiplexer #(.select(1), .width(5), .disabled("Z"), .enable("false")) multiplexer_6 (
    .in0(multiplexer_3_out), .in1({5{1'b1}}), .out(multiplexer_6_out), .sel(MEM_JAL));
  // Probe on EX_PC[11:0]
  // Probe on ID_PC[11:0]
  \单周期硬布线控制器  \u_单周期硬布线控制器_1  (
    .Func(Func), .OP(ID_IR[31:26]), .ALU_OP(\单周期硬布线控制器_1_alu_op ), .MemToReg(\单周期硬布线控制器_1_memtoreg ),
    .MemWrite(\单周期硬布线控制器_1_memwrite ), .ALU_SRC(\单周期硬布线控制器_1_alu_src ), .RegWrite(\单周期硬布线控制器_1_regwrite ),
    .SysCALL(\单周期硬布线控制器_1_syscall ), .SignedExt(SignedExt), .RegDst(\单周期硬布线控制器_1_regdst ),
    .JR(\单周期硬布线控制器_1_jr ), .JMP(\单周期硬布线控制器_1_jmp ), .Beq(\单周期硬布线控制器_1_beq ), .JAL(\单周期硬布线控制器_1_jal ),
    .Bne(\单周期硬布线控制器_1_bne ), .SLLV(\单周期硬布线控制器_1_sllv ), .LUI(\单周期硬布线控制器_1_lui ), .SB(\单周期硬布线控制器_1_sb ),
    .BGTZ(\单周期硬布线控制器_1_bgtz ));  // open: in_3, MFC0, MTC0
  Comparator #(.width(6), .mode("twosComplement")) comparator_5 (
    .a(EX_IR[31:26]), .b(6'b100011), .eq(comparator_5_eq));  // open: gt, lt
  // Probe on M_PC[11:0]
  D_Flip_Flop #(.trigger("high"), .Pre_Clr_Positions("LEGACY"), .NegatePresetClear("false"), .enable("true"), .NewFFLayout("false")) d_ff_1 (.Q(d_ff_1_q));  // open: clk, D, Qn, preset, en, reset
  // Probe on 13'hc
  Multiplexer #(.select(1), .width(5), .disabled("Z"), .enable("false")) multiplexer_7 (
    .in0(ID_IR[25:21]), .in1(5'b00100), .out(R1_num), .sel(\单周期硬布线控制器_1_syscall ));
  Multiplexer #(.select(1), .width(5), .disabled("Z"), .enable("false")) multiplexer_8 (
    .in0(ID_IR[20:16]), .in1(5'b00010), .out(R2_num), .sel(\单周期硬布线控制器_1_syscall ));
  // Probe on WB_PC[11:0]
  Comparator #(.width(13), .mode("twosComplement")) comparator_6 (
    .a(CNT_num), .b(13'hc), .eq(comparator_6_eq), .lt(comparator_6_lt));  // open: gt
  Clock #(.highDuration(1), .lowDuration(1)) clock_2 (.out(clock_2_out));
  assign bit_extender_1_out = {{16{1'b0}}, {ID_IR[15:6], Func}};  // Bit_Extender bit_extender_1
  assign bit_extender_2_out = {{16{ID_IR[15]}}, {ID_IR[15:6], Func}};  // Bit_Extender bit_extender_2
  \重定向数据相关检测  \u_重定向数据相关检测_1  (
    .R1_num(R1_num), .MEM_WriteReg_num(multiplexer_6_out), .R2_num(R2_num),
    .EX_WriteReg_num(multiplexer_5_out), .isLW(comparator_5_eq), .OP(ID_IR[31:26]), .FUNC(Func),
    .R1(\重定向数据相关检测_1_r1 ), .LoadUse(LoadUse), .R2(\重定向数据相关检测_1_r2 ), .MEM_RegWrite(MEM_RegWrite),
    .EX_RegWrite(EX_RegWrite));
  nand nand_1 (nand_1_out, d_ff_1_q, comparator_6_eq);
  Counter #(.width(13), .max('h1fff), .ongoal("stay"), .trigger("rising"), .behavior("old")) counter_1 (
    .count(comparator_6_lt), .Q(CNT_num), .clk(clock_2_out));  // open: load, D, carry, clr, preset
  MIPS_Regifile mips_regifile_1 (
    .Din(RDin), .Clk(CLK), .R1(mips_regifile_1_r1), .R2(mips_regifile_1_r2), .WE(RegWrite),
    .W_num(multiplexer_19_out), .R1_num(R1_num), .R2_num(R2_num));
  assign CLK = nand_1_out ? clock_2_out : 1'bz;  // Controlled_Buffer controlled_buffer_1
  Multiplexer #(.select(1), .width(32), .disabled("Z"), .enable("false")) multiplexer_9 (
    .in0(bit_extender_1_out), .in1(bit_extender_2_out), .out(multiplexer_9_out), .sel(SignedExt));
  Register #(.width(2), .trigger("rising"), .Select("low")) register_1 (
    .D(\重定向数据相关检测_1_r1 ), .Q(R1_Forward), .clk(CLK));  // open: en, clr
  Register #(.width(2), .trigger("rising"), .Select("low")) register_2 (
    .D(\重定向数据相关检测_1_r2 ), .Q(R2_Forward), .clk(CLK));  // open: en, clr
  Pull_Resistor #(.pull(1)) pull_resistor_4 (.node(CLK));
  Multiplexer #(.select(2), .width(32), .disabled("Z"), .enable("false")) multiplexer_10 (
    .in0(EX_B), .in1(MEM_AluResult), .in2(RDin), .in3(MEM_AluResult), .out(EX_B_mux), .sel(R2_Forward));
  Shifter #(.width(32), .shift("ll")) shifter_1 (.in(EX_Imm), .\dist (5'b00010), .out(shifter_1_out));
  Adder #(.width(32)) adder_2 (.a(EX_PC), .b(32'h4), .out(adder_2_out));  // open: cin, cout
  or or_3 (Clear, EX_JMP, Branch);
  not not_1 (not_1_out, Clear);
  Counter #(.width(16), .max('hffff), .ongoal("wrap"), .trigger("rising"), .behavior("new")) counter_2 (
    .Q(\总周期数 ), .clk(and_2_out));  // open: load, D, count, carry, clr, preset, down
  and and_2 (and_2_out, En, CLK);
  Multiplexer #(.select(2), .width(32), .disabled("Z"), .enable("false")) multiplexer_11 (
    .in0(EX_A), .in1(MEM_AluResult), .in2(RDin), .in3(MEM_AluResult), .out(EX_AluA), .sel(R1_Forward));
  ID_EX id_ex_1 (
    .RedDst_in(\单周期硬布线控制器_1_regdst ), .AluSrcB_in(\单周期硬布线控制器_1_alu_src ), .Shamt_in(ID_IR[10:6]),
    .Syscall_in(\单周期硬布线控制器_1_syscall ), .RegWrite_in(\单周期硬布线控制器_1_regwrite ), .JMP_in(\单周期硬布线控制器_1_jmp ),
    .JAL_in(\单周期硬布线控制器_1_jal ), .AluOp_in(\单周期硬布线控制器_1_alu_op ), .JR_in(\单周期硬布线控制器_1_jr ),
    .MemWrite_in(\单周期硬布线控制器_1_memwrite ), .IR_in({ID_IR, Func}), .SLLV_in(\单周期硬布线控制器_1_sllv ), .PC_in(ID_PC),
    .Beq_in(\单周期硬布线控制器_1_beq ), .LUI_in(\单周期硬布线控制器_1_lui ), .Bne_in(\单周期硬布线控制器_1_bne ),
    .SB_in(\单周期硬布线控制器_1_sb ), .A_in(mips_regifile_1_r1), .MemToReg_in(\单周期硬布线控制器_1_memtoreg ),
    .BGTZ_in(\单周期硬布线控制器_1_bgtz ), .B_in(mips_regifile_1_r2), .Imm_in(multiplexer_9_out),
    .RedDst_out(EX_RegDst), .AluSrcB_out(id_ex_1_alusrcb_out), .Syscall_out(id_ex_1_syscall_out),
    .RegWrite_out(EX_RegWrite), .Shamt_out(EX_Shamt), .JMP_out(EX_JMP), .JAL_out(EX_JAL),
    .AluOp_out(id_ex_1_aluop_out), .JR_out(EX_JR), .MemWrite_out(id_ex_1_memwrite_out), .IR_out(EX_IR),
    .PC_out(EX_PC), .Beq_out(EX_Beq), .A_out(EX_A), .Bne_out(EX_Bne), .SB_out(id_ex_1_sb_out),
    .MemToReg_out(id_ex_1_memtoreg_out), .BGTZ_out(EX_BGTZ), .B_out(EX_B), .Imm_out(EX_Imm), .CLR(or_4_out),
    .Stall(undriven), .CLK(CLK), .ERET_in(ERET), .ERET_OUT(id_ex_1_eret_out));  // open: PredictJMP_out, SLLV_out, LUI_out, PredictJMP_in
  or or_4 (or_4_out, IE_ctrl, Clear, LoadUse, RST, WB_ERET);
  assign controlled_buffer_2_out = EX_JR ? EX_AluA : 32'bz;  // Controlled_Buffer controlled_buffer_2
  Adder #(.width(32)) adder_3 (.a(shifter_1_out), .b(adder_2_out), .out(adder_3_out));  // open: cin, cout
  and and_3 (and_3_out, EX_JMP, ~EX_JR);  // AND_Gate
  assign controlled_buffer_2_out = and_3_out ? {EX_PC[31:28], EX_IR[25:0], 2'b00} : 32'bz;  // Controlled_Buffer controlled_buffer_3
  assign controlled_buffer_2_out = not_1_out ? PC_4 : 32'bz;  // Controlled_Buffer controlled_buffer_4
  Multiplexer #(.select(1), .width(32), .disabled("Z"), .enable("false")) multiplexer_12 (
    .in0(EX_B_mux), .in1(EX_Imm), .out(multiplexer_12_out), .sel(id_ex_1_alusrcb_out));
  assign controlled_buffer_2_out = Branch ? adder_3_out : 32'bz;  // Controlled_Buffer controlled_buffer_5
  Multiplexer #(.select(1), .width(5), .disabled("Z"), .enable("false")) multiplexer_13 (.in0(undriven_2));  // open: in1, out, sel
  Comparator #(.width(32), .mode("twosComplement")) comparator_7 (
    .a(EX_AluA), .b({32{1'b0}}), .gt(comparator_7_gt));  // open: eq, lt
  MIPS_ALU mips_alu_1 (
    .X(EX_AluA), .Y(multiplexer_12_out), .AluOP(id_ex_1_aluop_out), .Equal(mips_alu_1_equal),
    .Result(mips_alu_1_result), .shamt(EX_Shamt));  // open: Result_2
  and and_4 (and_4_out, EX_Beq, mips_alu_1_equal);
  and and_5 (and_5_out, EX_Bne, ~mips_alu_1_equal);  // AND_Gate
  and and_6 (and_6_out, comparator_7_gt, EX_BGTZ);
  or or_5 (or_5_out, RST, IE_ctrl, WB_ERET);
  or or_6 (Branch, and_4_out, and_5_out, and_6_out);
  Multiplexer #(.select(1), .width(32), .disabled("Z"), .enable("false")) multiplexer_14 (
    .in0(MDin), .in1(multiplexer_15_out), .out(multiplexer_14_out), .sel(MEM_SB));
  EX_MEM ex_mem_1 (
    .RedDst_in(EX_RegDst), .Syscall_in(id_ex_1_syscall_out), .RegWrite_in(EX_RegWrite), .JAL_in(EX_JAL),
    .AluResult_in(mips_alu_1_result), .MemWrite_in(id_ex_1_memwrite_out), .IR_in(EX_IR), .PC_in(EX_PC),
    .SB_in(id_ex_1_sb_out), .A_in(EX_AluA), .MemToReg_in(id_ex_1_memtoreg_out), .B_in(EX_B_mux),
    .RedDst_out(MEM_RegDst), .Syscall_out(ex_mem_1_syscall_out), .RegWrite_out(MEM_RegWrite),
    .JAL_out(MEM_JAL), .AluResult_out(MEM_AluResult), .MemWrite_out(MemWrite), .IR_out(MEM_IR),
    .PC_out(M_PC), .A_out(ex_mem_1_a_out), .SB_out(MEM_SB), .MemToReg_out(ex_mem_1_memtoreg_out),
    .B_out(MDin), .CLR(or_5_out), .Stall(undriven_3), .CLK(CLK), .ERET_in(id_ex_1_eret_out),
    .ERET_OUT(ex_mem_1_eret_out));  // open: AluSrcB_in, Shamt_in, JMP_in, JR_in, SignedExt_in, SLLV_in, Beq_in, LUI_in, Bne_in, BGTZ_in, Imm_in, AluSrcB_out, Shamt_out, JMP_out, JR_out, SignedExt_out, SLLV_out, Beq_out, LUI_out, Bne_out, BGTZ_out, Imm_out
  Multiplexer #(.select(2), .width(32), .disabled("Z"), .enable("false")) multiplexer_15 (
    .in0({ram_1_data[31:16], ram_1_data_2, MDin[7:0]}),
    .in1({ram_1_data[31:16], MDin[7:0], ram_1_data[7:0]}),
    .in2({ram_1_data[31:24], MDin[7:0], ram_1_data_2, ram_1_data[7:0]}),
    .in3({MDin[7:0], ram_1_data[23:16], ram_1_data_2, ram_1_data[7:0]}), .out(multiplexer_15_out),
    .sel(MEM_AluResult[1:0]));
  RAM #(.addrWidth(10), .dataWidth(32), .bus("separate"), .Select("high")) ram_1 (
    .addr(MEM_AluResult[11:2]), .din(multiplexer_14_out),
    .data({ram_1_data[31:16], ram_1_data_2, ram_1_data[7:0]}), .str(MemWrite), .clk(CLK), .ld(1'b1));  // open: sel, clr
  or or_7 (or_7_out, RST, WB_ERET);
  MEM_WB mem_wb_1 (
    .RedDst_in(MEM_RegDst), .MemData_in({ram_1_data[31:16], ram_1_data_2, ram_1_data[7:0]}),
    .Syscall_in(ex_mem_1_syscall_out), .RegWrite_in(MEM_RegWrite), .JAL_in(MEM_JAL),
    .AluResult_in(MEM_AluResult), .IR_in(MEM_IR), .PC_in(M_PC), .A_in(ex_mem_1_a_out),
    .MemToReg_in(ex_mem_1_memtoreg_out), .B_in(MDin), .RedDst_out(mem_wb_1_reddst_out),
    .Syscall_out(mem_wb_1_syscall_out), .RegWrite_out(RegWrite), .MemData_out(mem_wb_1_memdata_out),
    .JAL_out(mem_wb_1_jal_out), .AluResult_out(mem_wb_1_aluresult_out), .IR_out(WB_IR), .PC_out(WB_PC),
    .A_out(mem_wb_1_a_out), .MemToReg_out(mem_wb_1_memtoreg_out), .B_out(mem_wb_1_b_out), .CLR(or_7_out),
    .Stall(undriven_4), .CLK(CLK), .ERET_in(ex_mem_1_eret_out), .ERET_OUT(WB_ERET));  // open: AluSrcB_in, JMP_in, JR_in, MemWrite_in, SignedExt_in, SLLV_in, Beq_in, LUI_in, Bne_in, SB_in, BGTZ_in, Imm_in, AluSrcB_out, JMP_out, JR_out, MemWrite_out, SignedExt_out, SLLV_out, Beq_out, Bne_out, SB_out, BGTZ_out, Imm_out, LUI_out
  Multiplexer #(.select(1), .width(32), .disabled("Z"), .enable("false")) multiplexer_16 (
    .in0(mem_wb_1_aluresult_out), .in1(mem_wb_1_memdata_out), .out(multiplexer_16_out),
    .sel(mem_wb_1_memtoreg_out));
  Adder #(.width(32)) adder_4 (.a(WB_PC), .b(32'h4), .out(adder_4_out));  // open: cin, cout
  Multiplexer #(.select(1), .width(5), .disabled("Z"), .enable("false")) multiplexer_17 (
    .in0(WB_IR[20:16]), .in1(WB_IR[15:11]), .out(multiplexer_17_out), .sel(mem_wb_1_reddst_out));
  Multiplexer #(.select(1), .width(32), .disabled("Z"), .enable("false")) multiplexer_18 (
    .in0(multiplexer_16_out), .in1(adder_4_out), .out(RDin), .sel(mem_wb_1_jal_out));
  Multiplexer #(.select(1), .width(5), .disabled("Z"), .enable("false")) multiplexer_19 (
    .in0(multiplexer_17_out), .in1({5{1'b1}}), .out(multiplexer_19_out), .sel(mem_wb_1_jal_out));
  Comparator #(.width(32), .mode("twosComplement")) comparator_8 (
    .a(32'h22), .b(mem_wb_1_b_out), .eq(comparator_8_eq));  // open: gt, lt
  D_Flip_Flop #(.trigger("rising"), .Pre_Clr_Positions("LEGACY"), .NegatePresetClear("false"), .enable("true"), .NewFFLayout("false")) u_IR1 (
    .clk(IR1), .D(1'b1), .Q(IR1_q), .reset(ir1_t));  // open: Qn, preset, en
  or or_8 (W1, ir1_t, IR1_q);
  or or_9 (W2, ir2_t, IR1_3_q);
  D_Flip_Flop #(.trigger("rising"), .Pre_Clr_Positions("LEGACY"), .NegatePresetClear("false"), .enable("true"), .NewFFLayout("false")) IR1_2 (
    .clk(IR3), .D(1'b1), .Q(IR1_2_q), .reset(ir3_t));  // open: Qn, preset, en
  or or_10 (W3, ir3_t, IR1_2_q);
  and and_7 (and_7_out, comparator_8_eq, mem_wb_1_syscall_out);
  and and_8 (and_8_out, mem_wb_1_syscall_out, ~comparator_8_eq);  // AND_Gate
  Comparator #(.width(32), .mode("twosComplement")) comparator_9 (
    .a({ID_IR, Func}), .b(32'h42000018), .eq(ERET));  // open: gt, lt
  or or_11 (or_11_out, IR1_q, ir1_t);
  D_Flip_Flop #(.trigger("rising"), .Pre_Clr_Positions("LEGACY"), .NegatePresetClear("false"), .enable("true"), .NewFFLayout("false")) IR1_3 (
    .clk(IR2), .D(1'b1), .Q(IR1_3_q), .reset(ir2_t));  // open: Qn, preset, en
  or or_12 (or_12_out, IR1_2_q, ir3_t);
  Register #(.width(32), .trigger("rising"), .Select("low")) register_3 (
    .D(mem_wb_1_a_out), .en(and_7_out), .Q(LedData), .clk(CLK));  // open: clr
  Register #(.width(1), .trigger("rising"), .Select("low")) register_4 (
    .D(mem_wb_1_syscall_out), .en(and_8_out), .Q(register_4_q), .clk(CLK), .clr(Go));
  and and_9 (and_9_out, or_11_out, ~Rst1);  // AND_Gate
  or or_13 (or_13_out, IR1_3_q, ir2_t);
  and and_10 (and_10_out, or_13_out, ~Rst2);  // AND_Gate
  and and_11 (and_11_out, or_12_out, ~Rst3);  // AND_Gate
  not not_2 (En, register_4_q);
  D_Flip_Flop #(.trigger("rising"), .Pre_Clr_Positions("LEGACY"), .NegatePresetClear("false"), .enable("true"), .NewFFLayout("false")) IR1_4 (
    .clk(CLK), .D(and_9_out), .Q(ir1_t));  // open: Qn, preset, en, reset
  D_Flip_Flop #(.trigger("rising"), .Pre_Clr_Positions("LEGACY"), .NegatePresetClear("false"), .enable("true"), .NewFFLayout("false")) IR1_5 (
    .clk(CLK), .D(and_10_out), .Q(ir2_t));  // open: Qn, preset, en, reset
  D_Flip_Flop #(.trigger("rising"), .Pre_Clr_Positions("LEGACY"), .NegatePresetClear("false"), .enable("true"), .NewFFLayout("false")) IR1_6 (
    .clk(CLK), .D(and_11_out), .Q(ir3_t));  // open: Qn, preset, en, reset
  or or_14 (or_14_out, WB_ERET, IE_ctrl);
  Priority_Encoder #(.select(2), .disabled("Z")) priority_encoder_1 (
    .in0(1'b0), .in1(ir1_t), .in2(ir2_t), .in3(ir3_t), .out(priority_encoder_1_out),
    .gs(priority_encoder_1_gs));  // open: en_out, en_in
  Multiplexer #(.select(2), .width(32), .disabled("Z"), .enable("false")) multiplexer_20 (
    .in1(32'h30ac), .in2(32'h3150), .in3(32'h31f4), .out(\中断入口地址 ), .sel(priority_encoder_1_out));  // open: in0
  Register #(.width(1), .trigger("rising"), .Select("low")) register_5 (
    .D(IE_ctrl), .en(or_14_out), .Q(register_5_q), .clk(CLK));  // open: clr
  and and_12 (IE_ctrl, priority_encoder_1_gs, ~register_5_q);  // AND_Gate
  Register #(.width(2), .trigger("rising"), .Select("low")) register_6 (
    .D(priority_encoder_1_out), .en(IE_ctrl), .Q(register_6_q), .clk(CLK));  // open: clr
  Decoder #(.select(2), .tristate("false"), .disabled("Z"), .enable("false")) decoder_1 (
    .out1(decoder_1_out1), .out2(decoder_1_out2), .out3(decoder_1_out3), .sel(register_6_q));  // open: out0
  Register #(.width(32), .trigger("rising"), .Select("low")) register_7 (
    .D(EX_PC), .en(IE_ctrl), .Q(EPC), .clk(CLK));  // open: clr
  and and_13 (Rst1, decoder_1_out1, WB_ERET);
  and and_14 (Rst2, decoder_1_out2, WB_ERET);
  and and_15 (Rst3, decoder_1_out3, WB_ERET);

  // Other names for the same wires on the sheet: ID_IR[5:0] = Func; OP[5:0] = ID_IR[31:26]; MEM_PC[31:0] = M_PC

  // Notes on the sheet:
  //   中断源
  //   时空图监测，可删除
  //   中断等待指示
  //   单级中断测试信号模拟器
  //   数码管输出
  //   contents of rom_1 (hex, n*v repeats v):
  //   201d07d0 20100001 109fc0 139fc3 8021 2012000c 24160008 26100001 3210000f 20080008 20090001 139900
  //   2709825 132020 20020022 c 1094022 1500fff9 22100001 2018000f 2188024 108700 20080008 20090001 139902
  //   2709825 132021 20020022 c 1094022 1500fff9 108702 2c9b022 12c00001 8000c07 4020 1084027 84400
  //   3508ffff 82021 20020022 c 8000c01 afa20000 23bd0004 afa40000 23bd0004 afb00000 23bd0004 afb30000
  //   23bd0004 afb40000 23bd0004 afb50000 23bd0004 afb60000 23bd0004 20160001 20140003 20150001 168020
  //   108100 2149825 132020 20020022 c 1600fffa 295a022 1680fff7 23bdfffc 8fb60000 23bdfffc 8fb50000
  //   23bdfffc 8fb40000 23bdfffc 8fb30000 23bdfffc 8fb00000 23bdfffc 8fa40000 23bdfffc 8fa20000 42000018
  //   afa20000 23bd0004 afa40000 23bd0004 afb00000 23bd0004 afb30000 23bd0004 afb40000 23bd0004 afb50000
  //   23bd0004 afb60000 23bd0004 20160002 20140003 20150001 168020 108100 2149825 132020 20020022 c
  //   1600fffa 295a022 1680fff7 23bdfffc 8fb60000 23bdfffc 8fb50000 23bdfffc 8fb40000 23bdfffc 8fb30000
  //   23bdfffc 8fb00000 23bdfffc 8fa40000 23bdfffc 8fa20000 42000018 afa20000 23bd0004 afa40000 23bd0004
  //   afb00000 23bd0004 afb30000 23bd0004 afb40000 23bd0004 afb50000 23bd0004 afb60000 23bd0004 20160003
  //   20140003 20150001 168020 108100 2149825 132020 20020022 c 1600fffa 295a022 1680fff7 23bdfffc
  //   8fb60000 23bdfffc 8fb50000 23bdfffc 8fb40000 23bdfffc 8fb30000 23bdfffc 8fb00000 23bdfffc 8fa40000
  //   23bdfffc 8fa20000 42000018
  //   rt
  //   rd
  //   rt
  //   rd
  //   rt
  //   rd
  //   控制位
  //   rs
  //   流水调试日志用
  //   暂停节拍，不能为0
  //   戳工具置1进入计数暂停模式，ctrl+k时钟自动运行到对应节拍暂停
  //   ctrl+k关闭时钟连续运行，将控制位置零，进入单步调试模式调试
  //   可计数暂停的时钟源
  //   为方便自动评测，需要输出流水线各段保存的PC值，注意是PC不是PC+4，另外ID段寄存器写入信息，Mem段内存写入信息也要输出
endmodule

module \重定向流水线_动态预测  (
  output RegWrite,
  output MemWrite,
  output [31:0] IF_PC,
  output [31:0] ID_PC,
  output [31:0] EX_PC,
  output [31:0] M_PC,
  output [31:0] WB_PC,
  output [31:0] RDin,
  output [31:0] MDin,
  output [31:0] LedData
);

  wire and_1_out, and_2_out, and_3_out, and_4_out, and_5_out, and_6_out, and_7_out, and_8_out, Branch,
       btb_1_predictjmp, CLK, clock_1_out, clock_2_out, comparator_1_eq, comparator_2_eq, comparator_2_lt,
       comparator_3_gt, comparator_4_eq, d_ff_1_q, En, EX_Beq, EX_BGTZ, EX_Bne, EX_Branch, EX_BranchTaken,
       EX_JAL, EX_JMP, EX_JR, EX_LUI, ex_mem_1_memtoreg_out, ex_mem_1_syscall_out, EX_PredictJMP, EX_RegDst,
       EX_RegWrite, EX_SLLV, Go, id_ex_1_alusrcb_out, id_ex_1_memtoreg_out, id_ex_1_memwrite_out,
       id_ex_1_sb_out, id_ex_1_syscall_out, if_id_1_predictjmp_out, IR1, IR2, IR3, LoadUse, MEM_JAL,
       MEM_RegDst, MEM_RegWrite, MEM_SB, mem_wb_1_jal_out, mem_wb_1_memtoreg_out, mem_wb_1_reddst_out,
       mem_wb_1_syscall_out, mips_alu_1_equal, nand_1_out, not_1_out, or_1_out, or_2_out, or_5_out,
       PredictSuc, register_4_q, RST, SignedExt, W1, W2, W3, \单周期硬布线控制器_1_alu_src , \单周期硬布线控制器_1_beq ,
       \单周期硬布线控制器_1_bgtz , \单周期硬布线控制器_1_bne , \单周期硬布线控制器_1_jal , \单周期硬布线控制器_1_jmp , \单周期硬布线控制器_1_jr ,
       \单周期硬布线控制器_1_lui , \单周期硬布线控制器_1_memtoreg , \单周期硬布线控制器_1_memwrite , \单周期硬布线控制器_1_regdst ,
       \单周期硬布线控制器_1_regwrite , \单周期硬布线控制器_1_sb , \单周期硬布线控制器_1_sllv , \单周期硬布线控制器_1_syscall ;
  wire [1:0] R1_Forward, R2_Forward, \重定向数据相关检测_1_r1 , \重定向数据相关检测_1_r2 ;
  wire [3:0] id_ex_1_aluop_out, \单周期硬布线控制器_1_alu_op ;
  wire [4:0] EX_Shamt, multiplexer_4_out, multiplexer_5_out, multiplexer_6_out, multiplexer_7_out,
       multiplexer_14_out, multiplexer_19_out, multiplexer_21_out, R1_num, R2_num;
  wire [5:0] Func;
  wire [12:0] CNT_num;
  wire [15:0] \LoadUse次数 , \总周期数 , \插入气泡数 , \无条件分支数 , \条件分支成功数 ;
  wire [15:8] ram_1_data_2;
  wire [31:0] adder_3_out, adder_4_out, benchmark_data, BGTZ_data, bit_extender_1_out, bit_extender_2_out,
       btb_1_jmpaddr, EX_A, EX_AluA, EX_B, EX_B_mux, EX_BranchAddr, EX_Imm, EX_IR, ex_mem_1_a_out, EX_PC_4,
       IF_IR, LUI_data, MEM_AluResult, MEM_IR, mem_wb_1_a_out, mem_wb_1_aluresult_out, mem_wb_1_b_out,
       mem_wb_1_memdata_out, mips_alu_1_result, mips_regifile_1_r1, mips_regifile_1_r2, multiplexer_1_out,
       multiplexer_2_out, multiplexer_3_out, multiplexer_10_out, multiplexer_13_out, multiplexer_15_out,
       multiplexer_16_out, multiplexer_17_out, multiplexer_18_out, PC_4, ram_1_data, SB_data, shifter_1_out,
       SLLV_data, WB_IR;
  wire [31:6] ID_IR;

  Button \u_总复位  (.out(RST));
  Button _1 (.out(IR1));
  Button _2 (.out(IR2));
  Button _3 (.out(IR3));
  // Probe on \总周期数 
  // Probe on \总周期数 
  Multiplexer #(.select(1), .width(32), .disabled("Z"), .enable("false")) multiplexer_1 (
    .in0(EX_PC_4), .in1(EX_BranchAddr), .out(multiplexer_1_out), .sel(EX_BranchTaken));
  Button \u_继续运行  (.out(Go));
  LED #(.active("true")) led_1 (.in(W1));
  LED #(.active("true")) led_2 (.in(W2));
  LED #(.active("true")) led_3 (.in(W3));
  Multiplexer #(.select(1), .width(32), .disabled("Z"), .enable("false")) multiplexer_2 (
    .in0(multiplexer_1_out), .in1(multiplexer_3_out), .out(multiplexer_2_out), .sel(PredictSuc));
  Hex_Digit_Display hex_digit_display_1 (.value(LedData[31:28]));  // open: dp
  // Probe on IF_PC[19:0]
  // Mips_Probe mips_probe_1: pin names not known; wires that end beside it: IF_IR
  and and_1 (and_1_out, ~LoadUse, En);  // AND_Gate
  Hex_Digit_Display hex_digit_display_2 (.value(LedData[23:20]));  // open: dp
  Hex_Digit_Display hex_digit_display_3 (.value(LedData[27:24]));  // open: dp
  // Probe on ID_PC[19:0]
  // Mips_Probe mips_probe_2: pin names not known; wires that end beside it: {ID_IR, Func}
  ROM #(.addrWidth(10), .dataWidth(32), .Select("low")) benchmark (.addr(IF_PC[11:2]), .data(benchmark_data));
  ROM #(.addrWidth(10), .dataWidth(32), .Select("low")) SB (.addr(IF_PC[11:2]), .data(SB_data));
  Register #(.width(32), .trigger("rising"), .Select("low")) PC (
    .D(multiplexer_2_out), .en(and_1_out), .Q(IF_PC), .clk(CLK));  // open: clr
  Hex_Digit_Display hex_digit_display_4 (.value(LedData[19:16]));  // open: dp
  Hex_Digit_Display hex_digit_display_5 (.value(LedData[15:12]));  // open: dp
  // Switch #(.width(32)) switch_1: pin names not known; wires that end beside it: benchmark_data, IF_IR
  // Switch #(.width(32)) switch_2: pin names not known; wires that end beside it: SB_data, IF_IR
  Adder #(.width(32)) adder_1 (.a(32'h4), .b(IF_PC), .out(PC_4));  // open: cin, cout
  Hex_Digit_Display hex_digit_display_6 (.value(LedData[11:8]));  // open: dp
  Hex_Digit_Display hex_digit_display_7 (.value(LedData[7:4]));  // open: dp
  Clock #(.highDuration(1), .lowDuration(1)) clock_1 (.out(clock_1_out));
  // Probe on EX_PC[19:0]
  // Mips_Probe mips_probe_3: pin names not known; wires that end beside it: clock_1_out, EX_IR, CLK
  BTB btb_1 (
    .EX_Branch(EX_Branch), .EX_BranchTaken(EX_BranchTaken), .PC(IF_PC), .EX_PC(EX_PC),
    .EX_BranchAddr(EX_BranchAddr), .CLK(CLK), .PredictJmp(btb_1_predictjmp), .JmpAddr(btb_1_jmpaddr));
  Multiplexer #(.select(1), .width(32), .disabled("Z"), .enable("false")) multiplexer_3 (
    .in0(PC_4), .in1(btb_1_jmpaddr), .out(multiplexer_3_out), .sel(btb_1_predictjmp));
  Hex_Digit_Display hex_digit_display_8 (.value(LedData[3:0]));  // open: dp
  // Probe on \总周期数 
  // Probe on M_PC[19:0]
  // Mips_Probe mips_probe_4: pin names not known; wires that end beside it: MEM_IR
  ROM #(.addrWidth(10), .dataWidth(32), .Select("low")) SLLV (.addr(IF_PC[11:2]), .data(SLLV_data));
  ROM #(.addrWidth(10), .dataWidth(32), .Select("low")) BGTZ (.addr(IF_PC[11:2]), .data(BGTZ_data));
  Multiplexer #(.select(1), .width(5), .disabled("Z"), .enable("false")) multiplexer_4 (
    .in0(MEM_IR[20:16]), .in1(MEM_IR[15:11]), .out(multiplexer_4_out), .sel(MEM_RegDst));
  Multiplexer #(.select(1), .width(5), .disabled("Z"), .enable("false")) multiplexer_5 (
    .in0(EX_IR[20:16]), .in1(EX_IR[15:11]), .out(multiplexer_5_out), .sel(EX_RegDst));
  // Probe on \总周期数 
  // Probe on \无条件分支数 
  // Probe on \条件分支成功数 
  // Probe on \插入气泡数 
  // Probe on \LoadUse次数 
  // Switch #(.width(32)) switch_3: pin names not known; wires that end beside it: SLLV_data, IF_IR
  // Switch #(.width(32)) switch_4: pin names not known; wires that end beside it: BGTZ_data, IF_IR
  IF_ID if_id_1 (
    .IR_in(IF_IR), .PredictJMP_in(btb_1_predictjmp), .PC_in(IF_PC), .IR_out({ID_IR, Func}),
    .PredictJMP_out(if_id_1_predictjmp_out), .PC_out(ID_PC), .CLR(or_1_out), .Stall(LoadUse), .CLK(CLK));  // open: RedDst_in, AluSrcB_in, Shamt_in, Syscall_in, RegWrite_in, JMP_in, AluOp_in, JAL_in, JR_in, MemWrite_in, SLLV_in, Beq_in, LUI_in, Bne_in, A_in, SB_in, MemToReg_in, BGTZ_in, B_in, Imm_in, RedDst_out, AluSrcB_out, Syscall_out, Shamt_out, RegWrite_out, JMP_out, AluOp_out, JAL_out, JR_out, MemWrite_out, SLLV_out, Beq_out, A_out, LUI_out, Bne_out, SB_out, MemToReg_out, B_out, BGTZ_out, Imm_out
  or or_1 (or_1_out, ~PredictSuc, RST);  // OR_Gate
  Multiplexer #(.select(1), .width(5), .disabled("Z"), .enable("false")) multiplexer_6 (
    .in0(multiplexer_5_out), .in1({5{1'b1}}), .out(multiplexer_6_out), .sel(EX_JAL));
  // Probe on IF_PC[11:0]
  // Probe on WB_PC[19:0]
  // Mips_Probe mips_probe_5: pin names not known; wires that end beside it: WB_IR
  ROM #(.addrWidth(10), .dataWidth(32), .Select("low")) LUI (.addr(IF_PC[11:2]), .data(LUI_data));
  Multiplexer #(.select(1), .width(5), .disabled("Z"), .enable("false")) multiplexer_7 (
    .in0(multiplexer_4_out), .in1({5{1'b1}}), .out(multiplexer_7_out), .sel(MEM_JAL));
  // Probe on ID_PC[11:0]
  // Probe on EX_PC[11:0]
  // Switch #(.width(32)) switch_5: pin names not known; wires that end beside it: LUI_data, IF_IR
  \单周期硬布线控制器  \u_单周期硬布线控制器_1  (
    .Func(Func), .OP(ID_IR[31:26]), .ALU_OP(\单周期硬布线控制器_1_alu_op ), .MemToReg(\单周期硬布线控制器_1_memtoreg ),
    .MemWrite(\单周期硬布线控制器_1_memwrite ), .ALU_SRC(\单周期硬布线控制器_1_alu_src ), .RegWrite(\单周期硬布线控制器_1_regwrite ),
    .SysCALL(\单周期硬布线控制器_1_syscall ), .SignedExt(SignedExt), .RegDst(\单周期硬布线控制器_1_regdst ),
    .JR(\单周期硬布线控制器_1_jr ), .JMP(\单周期硬布线控制器_1_jmp ), .Beq(\单周期硬布线控制器_1_beq ), .JAL(\单周期硬布线控制器_1_jal ),
    .Bne(\单周期硬布线控制器_1_bne ), .SLLV(\单周期硬布线控制器_1_sllv ), .LUI(\单周期硬布线控制器_1_lui ), .SB(\单周期硬布线控制器_1_sb ),
    .BGTZ(\单周期硬布线控制器_1_bgtz ));  // open: in_3, MFC0, MTC0
  Comparator #(.width(6), .mode("twosComplement")) comparator_1 (
    .a(EX_IR[31:26]), .b(6'b100011), .eq(comparator_1_eq));  // open: gt, lt
  // Probe on M_PC[11:0]
  D_Flip_Flop #(.trigger("high"), .Pre_Clr_Positions("LEGACY"), .NegatePresetClear("false"), .enable("true"), .NewFFLayout("false")) d_ff_1 (.Q(d_ff_1_q));  // open: clk, D, Qn, preset, en, reset
  // Probe on 13'h45
  Multiplexer #(.select(1), .width(5), .disabled("Z"), .enable("false")) multiplexer_8 (
    .in0(ID_IR[25:21]), .in1(5'b00100), .out(R1_num), .sel(\单周期硬布线控制器_1_syscall ));
  Multiplexer #(.select(1), .width(5), .disabled("Z"), .enable("false")) multiplexer_9 (
    .in0(ID_IR[20:16]), .in1(5'b00010), .out(R2_num), .sel(\单周期硬布线控制器_1_syscall ));
  // Probe on WB_PC[11:0]
  Comparator #(.width(13), .mode("twosComplement")) comparator_2 (
    .a(CNT_num), .b(13'h45), .eq(comparator_2_eq), .lt(comparator_2_lt));  // open: gt
  Clock #(.highDuration(1), .lowDuration(1)) clock_2 (.out(clock_2_out));
  assign bit_extender_1_out = {{16{1'b0}}, {ID_IR[15:6], Func}};  // Bit_Extender bit_extender_1
  assign bit_extender_2_out = {{16{ID_IR[15]}}, {ID_IR[15:6], Func}};  // Bit_Extender bit_extender_2
  \重定向数据相关检测  \u_重定向数据相关检测_1  (
    .R1_num(R1_num), .MEM_WriteReg_num(multiplexer_7_out), .R2_num(R2_num),
    .EX_WriteReg_num(multiplexer_6_out), .isLW(comparator_1_eq), .OP(ID_IR[31:26]), .FUNC(Func),
    .R1(\重定向数据相关检测_1_r1 ), .LoadUse(LoadUse), .R2(\重定向数据相关检测_1_r2 ), .MEM_RegWrite(MEM_RegWrite),
    .EX_RegWrite(EX_RegWrite));
  nand nand_1 (nand_1_out, d_ff_1_q, comparator_2_eq);
  Counter #(.width(13), .max('h1fff), .ongoal("stay"), .trigger("rising"), .behavior("old")) counter_1 (
    .count(comparator_2_lt), .Q(CNT_num), .clk(clock_2_out));  // open: load, D, carry, clr, preset
  MIPS_Regifile mips_regifile_1 (
    .Din(RDin), .Clk(CLK), .R1(mips_regifile_1_r1), .R2(mips_regifile_1_r2), .WE(RegWrite),
    .W_num(multiplexer_21_out), .R1_num(R1_num), .R2_num(R2_num));
  assign CLK = nand_1_out ? clock_2_out : 1'bz;  // Controlled_Buffer controlled_buffer_1
  Multiplexer #(.select(1), .width(32), .disabled("Z"), .enable("false")) multiplexer_10 (
    .in0(bit_extender_1_out), .in1(bit_extender_2_out), .out(multiplexer_10_out), .sel(SignedExt));
  Register #(.width(2), .trigger("rising"), .Select("low")) register_1 (
    .D(\重定向数据相关检测_1_r1 ), .Q(R1_Forward), .clk(CLK));  // open: en, clr
  Register #(.width(2), .trigger("rising"), .Select("low")) register_2 (
    .D(\重定向数据相关检测_1_r2 ), .Q(R2_Forward), .clk(CLK));  // open: en, clr
  Pull_Resistor #(.pull(1)) pull_resistor_1 (.node(CLK));
  // Probe on mips_regifile_1_r1
  // Probe on mips_regifile_1_r2
  Multiplexer #(.select(2), .width(32), .disabled("Z"), .enable("false")) multiplexer_11 (
    .in0(EX_B), .in1(MEM_AluResult), .in2(RDin), .in3(MEM_AluResult), .out(EX_B_mux), .sel(R2_Forward));
  Shifter #(.width(32), .shift("ll")) shifter_1 (.in(EX_Imm), .\dist (5'b00010), .out(shifter_1_out));
  Adder #(.width(32)) adder_2 (.a(EX_PC), .b(32'h4), .out(EX_PC_4));  // open: cin, cout
  Counter #(.width(16), .max('hffff), .ongoal("wrap"), .trigger("rising"), .behavior("new")) counter_2 (
    .Q(\总周期数 ), .clk(and_2_out));  // open: load, D, count, carry, clr, preset, down
  and and_2 (and_2_out, En, CLK);
  Multiplexer #(.select(2), .width(32), .disabled("Z"), .enable("false")) multiplexer_12 (
    .in0(EX_A), .in1(MEM_AluResult), .in2(RDin), .in3(MEM_AluResult), .out(EX_AluA), .sel(R1_Forward));
  ID_EX id_ex_1 (
    .RedDst_in(\单周期硬布线控制器_1_regdst ), .AluSrcB_in(\单周期硬布线控制器_1_alu_src ), .Shamt_in(ID_IR[10:6]),
    .Syscall_in(\单周期硬布线控制器_1_syscall ), .RegWrite_in(\单周期硬布线控制器_1_regwrite ), .JMP_in(\单周期硬布线控制器_1_jmp ),
    .JAL_in(\单周期硬布线控制器_1_jal ), .AluOp_in(\单周期硬布线控制器_1_alu_op ), .JR_in(\单周期硬布线控制器_1_jr ),
    .MemWrite_in(\单周期硬布线控制器_1_memwrite ), .IR_in({ID_IR, Func}), .SLLV_in(\单周期硬布线控制器_1_sllv ), .PC_in(ID_PC),
    .Beq_in(\单周期硬布线控制器_1_beq ), .LUI_in(\单周期硬布线控制器_1_lui ), .Bne_in(\单周期硬布线控制器_1_bne ),
    .SB_in(\单周期硬布线控制器_1_sb ), .A_in(mips_regifile_1_r1), .MemToReg_in(\单周期硬布线控制器_1_memtoreg ),
    .BGTZ_in(\单周期硬布线控制器_1_bgtz ), .B_in(mips_regifile_1_r2), .Imm_in(multiplexer_10_out),
    .RedDst_out(EX_RegDst), .AluSrcB_out(id_ex_1_alusrcb_out), .Syscall_out(id_ex_1_syscall_out),
    .RegWrite_out(EX_RegWrite), .Shamt_out(EX_Shamt), .JMP_out(EX_JMP), .JAL_out(EX_JAL),
    .AluOp_out(id_ex_1_aluop_out), .JR_out(EX_JR), .MemWrite_out(id_ex_1_memwrite_out), .IR_out(EX_IR),
    .PredictJMP_out(EX_PredictJMP), .SLLV_out(EX_SLLV), .PC_out(EX_PC), .Beq_out(EX_Beq), .LUI_out(EX_LUI),
    .A_out(EX_A), .Bne_out(EX_Bne), .SB_out(id_ex_1_sb_out), .MemToReg_out(id_ex_1_memtoreg_out),
    .BGTZ_out(EX_BGTZ), .B_out(EX_B), .Imm_out(EX_Imm), .CLR(or_2_out), .CLK(CLK),
    .PredictJMP_in(if_id_1_predictjmp_out));  // open: Stall, ERET_in, ERET_OUT
  or or_2 (or_2_out, ~PredictSuc, LoadUse, RST);  // OR_Gate
  assign EX_BranchAddr = EX_JR ? EX_AluA : 32'bz;  // Controlled_Buffer controlled_buffer_2
  Adder #(.width(32)) adder_3 (.a(shifter_1_out), .b(EX_PC_4), .out(adder_3_out));  // open: cin, cout
  and and_3 (and_3_out, EX_JMP, ~EX_JR);  // AND_Gate
  assign EX_BranchAddr = and_3_out ? {EX_PC[31:28], EX_IR[25:0], 2'b00} : 32'bz;  // Controlled_Buffer controlled_buffer_3
  // Probe on EX_AluA
  // Probe on EX_B_mux
  Multiplexer #(.select(1), .width(32), .disabled("Z"), .enable("false")) multiplexer_13 (
    .in0(EX_B_mux), .in1(EX_Imm), .out(multiplexer_13_out), .sel(id_ex_1_alusrcb_out));
  not not_1 (not_1_out, EX_JMP);
  assign EX_BranchAddr = not_1_out ? adder_3_out : 32'bz;  // Controlled_Buffer controlled_buffer_4
  Multiplexer #(.select(1), .width(5), .disabled("Z"), .enable("false")) multiplexer_14 (
    .in0(EX_Shamt), .in1(EX_AluA[4:0]), .out(multiplexer_14_out), .sel(EX_SLLV));
  Comparator #(.width(32), .mode("twosComplement")) comparator_3 (
    .a(EX_AluA), .b({32{1'b0}}), .gt(comparator_3_gt));  // open: eq, lt
  MIPS_ALU mips_alu_1 (
    .X(EX_AluA), .Y(multiplexer_13_out), .AluOP(id_ex_1_aluop_out), .Equal(mips_alu_1_equal),
    .Result(mips_alu_1_result), .shamt(multiplexer_14_out));  // open: Result_2
  // Probe on mips_alu_1_result
  Multiplexer #(.select(1), .width(32), .disabled("Z"), .enable("false")) multiplexer_15 (
    .in0(mips_alu_1_result), .in1({EX_Imm[15:0], {16{1'b0}}}), .out(multiplexer_15_out), .sel(EX_LUI));
  or or_3 (EX_Branch, EX_Beq, EX_Bne, EX_JMP, EX_JR, EX_BGTZ);
  and and_4 (and_4_out, EX_Beq, mips_alu_1_equal);
  and and_5 (and_5_out, EX_Bne, ~mips_alu_1_equal);  // AND_Gate
  and and_6 (and_6_out, comparator_3_gt, EX_BGTZ);
  or or_4 (Branch, and_4_out, and_5_out, and_6_out);
  Multiplexer #(.select(1), .width(32), .disabled("Z"), .enable("false")) multiplexer_16 (
    .in0(MDin), .in1(multiplexer_17_out), .out(multiplexer_16_out), .sel(MEM_SB));
  EX_MEM ex_mem_1 (
    .RedDst_in(EX_RegDst), .Syscall_in(id_ex_1_syscall_out), .RegWrite_in(EX_RegWrite), .JAL_in(EX_JAL),
    .AluResult_in(multiplexer_15_out), .MemWrite_in(id_ex_1_memwrite_out), .IR_in(EX_IR), .PC_in(EX_PC),
    .SB_in(id_ex_1_sb_out), .A_in(EX_AluA), .MemToReg_in(id_ex_1_memtoreg_out), .B_in(EX_B_mux),
    .RedDst_out(MEM_RegDst), .Syscall_out(ex_mem_1_syscall_out), .RegWrite_out(MEM_RegWrite),
    .JAL_out(MEM_JAL), .AluResult_out(MEM_AluResult), .MemWrite_out(MemWrite), .IR_out(MEM_IR),
    .PC_out(M_PC), .A_out(ex_mem_1_a_out), .SB_out(MEM_SB), .MemToReg_out(ex_mem_1_memtoreg_out),
    .B_out(MDin), .CLR(RST), .CLK(CLK));  // open: AluSrcB_in, Shamt_in, JMP_in, JR_in, SignedExt_in, SLLV_in, Beq_in, LUI_in, Bne_in, BGTZ_in, Imm_in, AluSrcB_out, Shamt_out, JMP_out, JR_out, SignedExt_out, SLLV_out, Beq_out, LUI_out, Bne_out, BGTZ_out, Imm_out, Stall, ERET_in, ERET_OUT
  or or_5 (or_5_out, Branch, EX_JR, EX_JMP);
  Multiplexer #(.select(2), .width(32), .disabled("Z"), .enable("false")) multiplexer_17 (
    .in0({ram_1_data[31:16], ram_1_data_2, MDin[7:0]}),
    .in1({ram_1_data[31:16], MDin[7:0], ram_1_data[7:0]}),
    .in2({ram_1_data[31:24], MDin[7:0], ram_1_data_2, ram_1_data[7:0]}),
    .in3({MDin[7:0], ram_1_data[23:16], ram_1_data_2, ram_1_data[7:0]}), .out(multiplexer_17_out),
    .sel(MEM_AluResult[1:0]));
  or or_6 (EX_BranchTaken, Branch, or_5_out);
  xnor xnor_1 (PredictSuc, EX_PredictJMP, EX_BranchTaken);
  RAM #(.addrWidth(10), .dataWidth(32), .bus("separate"), .Select("high")) ram_1 (
    .addr(MEM_AluResult[11:2]), .din(multiplexer_16_out),
    .data({ram_1_data[31:16], ram_1_data_2, ram_1_data[7:0]}), .str(MemWrite), .clk(CLK), .ld(1'b1));  // open: sel, clr
  MEM_WB mem_wb_1 (
    .RedDst_in(MEM_RegDst), .MemData_in({ram_1_data[31:16], ram_1_data_2, ram_1_data[7:0]}),
    .Syscall_in(ex_mem_1_syscall_out), .RegWrite_in(MEM_RegWrite), .JAL_in(MEM_JAL),
    .AluResult_in(MEM_AluResult), .IR_in(MEM_IR), .PC_in(M_PC), .A_in(ex_mem_1_a_out),
    .MemToReg_in(ex_mem_1_memtoreg_out), .B_in(MDin), .RedDst_out(mem_wb_1_reddst_out),
    .Syscall_out(mem_wb_1_syscall_out), .RegWrite_out(RegWrite), .MemData_out(mem_wb_1_memdata_out),
    .JAL_out(mem_wb_1_jal_out), .AluResult_out(mem_wb_1_aluresult_out), .IR_out(WB_IR), .PC_out(WB_PC),
    .A_out(mem_wb_1_a_out), .MemToReg_out(mem_wb_1_memtoreg_out), .B_out(mem_wb_1_b_out), .CLR(RST), .CLK(CLK));  // open: AluSrcB_in, JMP_in, JR_in, MemWrite_in, SignedExt_in, SLLV_in, Beq_in, LUI_in, Bne_in, SB_in, BGTZ_in, Imm_in, AluSrcB_out, JMP_out, JR_out, MemWrite_out, SignedExt_out, SLLV_out, Beq_out, Bne_out, SB_out, BGTZ_out, Imm_out, Stall, LUI_out, ERET_in, ERET_OUT
  Multiplexer #(.select(1), .width(32), .disabled("Z"), .enable("false")) multiplexer_18 (
    .in0(mem_wb_1_aluresult_out), .in1(mem_wb_1_memdata_out), .out(multiplexer_18_out),
    .sel(mem_wb_1_memtoreg_out));
  Adder #(.width(32)) adder_4 (.a(WB_PC), .b(32'h4), .out(adder_4_out));  // open: cin, cout
  Multiplexer #(.select(1), .width(5), .disabled("Z"), .enable("false")) multiplexer_19 (
    .in0(WB_IR[20:16]), .in1(WB_IR[15:11]), .out(multiplexer_19_out), .sel(mem_wb_1_reddst_out));
  Multiplexer #(.select(1), .width(32), .disabled("Z"), .enable("false")) multiplexer_20 (
    .in0(multiplexer_18_out), .in1(adder_4_out), .out(RDin), .sel(mem_wb_1_jal_out));
  Multiplexer #(.select(1), .width(5), .disabled("Z"), .enable("false")) multiplexer_21 (
    .in0(multiplexer_19_out), .in1({5{1'b1}}), .out(multiplexer_21_out), .sel(mem_wb_1_jal_out));
  Comparator #(.width(32), .mode("twosComplement")) comparator_4 (
    .a(32'h22), .b(mem_wb_1_b_out), .eq(comparator_4_eq));  // open: gt, lt
  and and_7 (and_7_out, comparator_4_eq, mem_wb_1_syscall_out);
  and and_8 (and_8_out, mem_wb_1_syscall_out, ~comparator_4_eq);  // AND_Gate
  Register #(.width(32), .trigger("rising"), .Select("low")) register_3 (
    .D(mem_wb_1_a_out), .en(and_7_out), .Q(LedData), .clk(CLK));  // open: clr
  Register #(.width(1), .trigger("rising"), .Select("low")) register_4 (
    .D(mem_wb_1_syscall_out), .en(and_8_out), .Q(register_4_q), .clk(CLK), .clr(Go));
  not not_2 (En, register_4_q);

  // Other names for the same wires on the sheet: ID_IR[5:0] = Func; OP[5:0] = ID_IR[31:26]; IN_INS[9:0] = IF_PC[11:2];
  //   MEM_PC[31:0] = M_PC; OUT_INS[31:0] = IF_IR

  // Notes on the sheet:
  //   中断源
  //   时空图监测，可删除
  //   中断等待指示
  //   contents of benchmark (hex, n*v repeats v):
  //   20110001 8000c05 20110001 20120002 20130003 8000c09 20110001 20120002 20130003 8000c0d 20110001
  //   20120002 20130003 8000c11 20110001 20120002 20130003 c000cb8 20100001 20110001 118fc0 112020
  //   20020022 c 118882 12200001 8000c15 112020 20020022 c 20110001 118880 112020 20020022 c 12200001
  //   8000c1f 20110001 118fc0 112020 20020022 c 1188c3 112020 20020022 c 118903 112020 20020022 c 118903
  //   112020 20020022 c 118903 112020 20020022 c 118903 112020 20020022 c 118903 112020 20020022 c 118903
  //   112020 20020022 c 118903 112020 20020022 c 20100001 109fc0 139fc3 8021 2012000c 24160003 26100001
  //   3210000f 20080008 20090001 139900 2709825 132020 20020022 c 1094022 1500fff9 22100001 2018000f
  //   2188024 108700 20080008 20090001 139902 2709825 132021 20020022 c 1094022 1500fff9 108702 2c9b022
  //   12c00001 8000c50 4020 1084027 84400 3508ffff 82021 20020022 c 2010ffff 20110000 ae300000 22100001
  //   22310004 ae300000 22100001 22310004 ae300000 22100001 22310004 ae300000 22100001 22310004 ae300000
  //   22100001 22310004 ae300000 22100001 22310004 ae300000 22100001 22310004 ae300000 22100001 22310004
  //   ae300000 22100001 22310004 ae300000 22100001 22310004 ae300000 22100001 22310004 ae300000 22100001
  //   22310004 ae300000 22100001 22310004 ae300000 22100001 22310004 ae300000 22100001 22310004 ae300000
  //   22100001 22310004 22100001 8020 2011003c 8e130000 8e340000 274402a 11000002 ae330000 ae140000
  //   2231fffc 1611fff8 102020 20020022 c 22100004 2011003c 1611fff2 20020032 c 20100000 22100001 102020
  //   20020022 c 22100002 102020 20020022 c 22100003 102020 20020022 c 22100004 102020 20020022 c 22100005
  //   102020 20020022 c 22100006 102020 20020022 c 22100007 102020 20020022 c 22100008 102020 20020022
  //   20020022 c 3e00008
  //   contents of SB (hex, n*v repeats v):
  //   20090000 200b0020 20110000 20120001 a1310000 112020 20020022 c 2328820 21290001 216bffff 1560fff8
  //   200b0008 20090000 8d310000 112020 20020022 c 21290004 216bffff 1560fff9 2002000a c
  //   数码管输出
  //   rt
  //   rd
  //   rt
  //   rd
  //   contents of SLLV (hex, n*v repeats v):
  //   20080001 20090003 20110876 112020 20020022 c 200b0008 1118804 1318804 112020 20020022 c 216bffff
  //   1560fff9 2002000a c
  //   contents of BGTZ (hex, n*v repeats v):
  //   2011000f 112020 20020022 c 2231ffff 1e20fffb 2002000a c
  //   contents of LUI (hex, n*v repeats v):
  //   200b0008 3c11fedc 3631ffff 112020 20020022 c 3c11ba98 112020 c 3c117654 112020 c 3c113210 112020 c
  //   216bffff 1560fff0 2002000a c
  //   rt
  //   rd
  //   控制位
  //   rs
  //   流水调试日志用
  //   暂停节拍，不能为0
  //   戳工具置1进入计数暂停模式，ctrl+k时钟自动运行到对应节拍暂停
  //   ctrl+k关闭时钟连续运行，将控制位置零，进入单步调试模式调试
  //   可计数暂停的时钟源
  //   为方便自动评测，需要输出流水线各段保存的PC值，注意是PC不是PC+4，另外ID段寄存器写入信息，Mem段内存写入信息也要输出
endmodule

module \归并比较  (
  input  [15:0] Y,
  input  [15:0] X,
  input  [2:0] Y_num,
  input  [2:0] X_num,
  output [15:0] MAX,
  output [2:0] Max_num
);

  wire comparator_1_eq, comparator_1_gt, or_1_out;

  Multiplexer #(.select(1), .width(16), .disabled("Z"), .enable("false")) multiplexer_1 (
    .in0(Y), .in1(X), .out(MAX), .sel(or_1_out));
  Comparator #(.width(16), .mode("twosComplement")) comparator_1 (
    .a(X), .b(Y), .gt(comparator_1_gt), .eq(comparator_1_eq));  // open: lt
  or or_1 (or_1_out, comparator_1_gt, comparator_1_eq);
  Multiplexer #(.select(1), .width(3), .disabled("Z"), .enable("false")) multiplexer_2 (
    .in0(Y_num), .in1(X_num), .out(Max_num), .sel(or_1_out));
endmodule

module Pre (
  input  Jmp,
  input  [1:0] pre_in,
  output [1:0] pre_out
);

  wire and_1_out, and_2_out, and_3_out, and_4_out, not_1_out, not_2_out, not_3_out, not_4_out, not_5_out;

  not not_1 (not_1_out, pre_in[0]);
  not not_2 (not_2_out, pre_in[1]);
  not not_3 (not_3_out, pre_in[0]);
  not not_4 (not_4_out, pre_in[0]);
  not not_5 (not_5_out, Jmp);
  and and_1 (and_1_out, not_4_out, pre_in[1]);
  and and_2 (and_2_out, Jmp, pre_in[0]);
  and and_3 (and_3_out, not_5_out, pre_in[1], not_1_out);
  and and_4 (and_4_out, Jmp, not_2_out, not_3_out);
  or or_1 (pre_out[1], and_1_out, and_2_out);
  or or_2 (pre_out[0], and_3_out, and_4_out);
endmodule

module BTB (
  input  EX_Branch,
  input  EX_BranchTaken,
  input  [31:0] PC,
  input  [31:0] EX_PC,
  input  [31:0] EX_BranchAddr,
  input  CLK,
  output PredictJmp,
  output [31:0] JmpAddr
);

  wire and_17_out, and_18_out, and_19_out, and_20_out, comparator_1_eq, comparator_2_eq, comparator_3_eq,
       comparator_4_eq, comparator_5_eq, comparator_6_eq, comparator_7_eq, comparator_8_eq, comparator_9_eq,
       comparator_10_eq, comparator_11_eq, comparator_12_eq, comparator_13_eq, comparator_14_eq,
       comparator_15_eq, comparator_16_eq, comparator_17_eq, comparator_18_eq, comparator_19_eq,
       comparator_20_eq, comparator_21_eq, comparator_22_eq, comparator_23_eq, comparator_24_eq,
       comparator_25_eq, comparator_26_eq, comparator_27_eq, comparator_28_eq, comparator_29_eq,
       comparator_30_eq, comparator_31_eq, comparator_32_eq, decoder_1_out2, decoder_1_out3, EX_Hit, EX_Miss,
       Hit, L0, L0_e, L0_f, L0_U, L1, L1_e, L1_f, L1_U, L2, L2_e, L2_f, L2_U, L3, L3_e, L3_f, L3_U, L4, L4_e,
       L4_f, L4_U, L5, L5_e, L5_f, L5_U, L6, L6_e, L6_f, L6_U, L7, L7_e, L7_f, L7_U, Miss, not_1_out,
       not_2_out, not_3_out, not_4_out, not_5_out, not_6_out, not_7_out, not_8_out, or_1_out, or_2_out,
       or_3_out, or_4_out, or_5_out, or_6_out, or_7_out, or_8_out, or_19_out, Out0, Out1, Out2, Out3, Out4,
       Out5, Out6, Out7, priority_encoder_1_en_out, priority_encoder_1_gs, Upgrade0, Upgrade1, Upgrade2,
       Upgrade3, Upgrade4, Upgrade5, Upgrade6, Upgrade7, V0, V1, V2, V3, V4, V5, V6, V7;
  wire [1:0] multiplexer_1_out, multiplexer_2_out, multiplexer_3_out, Pre, Pre0, Pre1, Pre2, Pre3, Pre4,
       Pre5, Pre6, Pre7, pre_1_pre_out;
  wire [2:0] pre_num, priority_encoder_1_out, priority_encoder_3_out, \归并比较_1_max_num , \归并比较_2_max_num ,
       \归并比较_3_max_num , \归并比较_4_max_num , \归并比较_5_max_num , \归并比较_6_max_num , \归并比较_7_max_num ;
  wire [15:0] C0, C1, C2, C3, C4, C5, C6, C7, \归并比较_1_max , \归并比较_2_max , \归并比较_3_max , \归并比较_4_max ,
       \归并比较_5_max , \归并比较_6_max ;
  wire [31:0] Branch0, Branch1, Branch2, Branch3, Branch4, Branch5, Branch6, Branch7, Dst_add_2_q,
       Dst_add_3_q, Dst_add_4_q, Dst_add_5_q, Dst_add_6_q, Dst_add_7_q, Dst_add_8_q, Dst_add_q;

  Register #(.width(1), .trigger("rising"), .Select("low")) V (.D(1'b1), .en(L0), .Q(V0), .clk(CLK));  // open: clr
  Register #(.width(1), .trigger("rising"), .Select("low")) V_2 (.D(1'b1), .en(L1), .Q(V1), .clk(CLK));  // open: clr
  Register #(.width(1), .trigger("rising"), .Select("low")) V_3 (.D(1'b1), .en(L2), .Q(V2), .clk(CLK));  // open: clr
  Register #(.width(1), .trigger("rising"), .Select("low")) V_4 (.D(1'b1), .en(L3), .Q(V3), .clk(CLK));  // open: clr
  Register #(.width(1), .trigger("rising"), .Select("low")) V_5 (.D(1'b1), .en(L4), .Q(V4), .clk(CLK));  // open: clr
  Register #(.width(1), .trigger("rising"), .Select("low")) V_6 (.D(1'b1), .en(L5), .Q(V5), .clk(CLK));  // open: clr
  Register #(.width(1), .trigger("rising"), .Select("low")) V_7 (.D(1'b1), .en(L6), .Q(V6), .clk(CLK));  // open: clr
  Register #(.width(1), .trigger("rising"), .Select("low")) V_8 (.D(1'b1), .en(L7), .Q(V7), .clk(CLK));  // open: clr
  Register #(.width(32), .trigger("rising"), .Select("low")) Branch_add (
    .D(EX_PC), .en(L0), .Q(Branch0), .clk(CLK));  // open: clr
  Register #(.width(32), .trigger("rising"), .Select("low")) Branch_add_2 (
    .D(EX_PC), .en(L1), .Q(Branch1), .clk(CLK));  // open: clr
  Register #(.width(32), .trigger("rising"), .Select("low")) Branch_add_3 (
    .D(EX_PC), .en(L2), .Q(Branch2), .clk(CLK));  // open: clr
  Register #(.width(32), .trigger("rising"), .Select("low")) Branch_add_4 (
    .D(EX_PC), .en(L3), .Q(Branch3), .clk(CLK));  // open: clr
  Register #(.width(32), .trigger("rising"), .Select("low")) Branch_add_5 (
    .D(EX_PC), .en(L4), .Q(Branch4), .clk(CLK));  // open: clr
  Register #(.width(32), .trigger("rising"), .Select("low")) Branch_add_6 (
    .D(EX_PC), .en(L5), .Q(Branch5), .clk(CLK));  // open: clr
  Register #(.width(32), .trigger("rising"), .Select("low")) Branch_add_7 (
    .D(EX_PC), .en(L6), .Q(Branch6), .clk(CLK));  // open: clr
  Register #(.width(32), .trigger("rising"), .Select("low")) Branch_add_8 (
    .D(EX_PC), .en(L7), .Q(Branch7), .clk(CLK));  // open: clr
  Register #(.width(2), .trigger("rising"), .Select("low")) Pred (.D(Pre), .en(L0), .Q(Pre0), .clk(CLK));  // open: clr
  Register #(.width(2), .trigger("rising"), .Select("low")) Pred_2 (
    .D(Pre), .en(L1), .Q(Pre1), .clk(CLK));  // open: clr
  Register #(.width(2), .trigger("rising"), .Select("low")) Pred_3 (
    .D(Pre), .en(L2), .Q(Pre2), .clk(CLK));  // open: clr
  Register #(.width(2), .trigger("rising"), .Select("low")) Pred_4 (
    .D(Pre), .en(L3), .Q(Pre3), .clk(CLK));  // open: clr
  Register #(.width(2), .trigger("rising"), .Select("low")) Pred_5 (
    .D(Pre), .en(L4), .Q(Pre4), .clk(CLK));  // open: clr
  Register #(.width(2), .trigger("rising"), .Select("low")) Pred_6 (
    .D(Pre), .en(L5), .Q(Pre5), .clk(CLK));  // open: clr
  Register #(.width(2), .trigger("rising"), .Select("low")) Pred_7 (
    .D(Pre), .en(L6), .Q(Pre6), .clk(CLK));  // open: clr
  Register #(.width(2), .trigger("rising"), .Select("low")) Pred_8 (
    .D(Pre), .en(L7), .Q(Pre7), .clk(CLK));  // open: clr
  Counter #(.width(16), .max('hffff), .ongoal("wrap"), .trigger("rising"), .behavior("new")) LRU (
    .count(V0), .Q(C0), .clk(Hit), .clr(or_1_out));  // open: load, D, carry, preset, down
  Counter #(.width(16), .max('hffff), .ongoal("wrap"), .trigger("rising"), .behavior("new")) LRU_2 (
    .count(V1), .Q(C1), .clk(Hit), .clr(or_2_out));  // open: load, D, carry, preset, down
  Counter #(.width(16), .max('hffff), .ongoal("wrap"), .trigger("rising"), .behavior("new")) LRU_3 (
    .count(V2), .Q(C2), .clk(Hit), .clr(or_3_out));  // open: load, D, carry, preset, down
  Counter #(.width(16), .max('hffff), .ongoal("wrap"), .trigger("rising"), .behavior("new")) LRU_4 (
    .count(V3), .Q(C3), .clk(Hit), .clr(or_4_out));  // open: load, D, carry, preset, down
  Counter #(.width(16), .max('hffff), .ongoal("wrap"), .trigger("rising"), .behavior("new")) LRU_5 (
    .count(V4), .Q(C4), .clk(Hit), .clr(or_5_out));  // open: load, D, carry, preset, down
  Counter #(.width(16), .max('hffff), .ongoal("wrap"), .trigger("rising"), .behavior("new")) LRU_6 (
    .count(V5), .Q(C5), .clk(Hit), .clr(or_6_out));  // open: load, D, carry, preset, down
  Counter #(.width(16), .max('hffff), .ongoal("wrap"), .trigger("rising"), .behavior("new")) LRU_7 (
    .count(V6), .Q(C6), .clk(Hit), .clr(or_7_out));  // open: load, D, carry, preset, down
  Counter #(.width(16), .max('hffff), .ongoal("wrap"), .trigger("rising"), .behavior("new")) LRU_8 (
    .count(V7), .Q(C7), .clk(Hit), .clr(or_8_out));  // open: load, D, carry, preset, down
  Register #(.width(32), .trigger("rising"), .Select("low")) Dst_add (
    .D(EX_BranchAddr), .en(L0), .Q(Dst_add_q), .clk(CLK));  // open: clr
  Register #(.width(32), .trigger("rising"), .Select("low")) Dst_add_2 (
    .D(EX_BranchAddr), .en(L1), .Q(Dst_add_2_q), .clk(CLK));  // open: clr
  Register #(.width(32), .trigger("rising"), .Select("low")) Dst_add_3 (
    .D(EX_BranchAddr), .en(L2), .Q(Dst_add_3_q), .clk(CLK));  // open: clr
  Register #(.width(32), .trigger("rising"), .Select("low")) Dst_add_4 (
    .D(EX_BranchAddr), .en(L3), .Q(Dst_add_4_q), .clk(CLK));  // open: clr
  assign JmpAddr = Out0 ? Dst_add_q : 32'bz;  // Controlled_Buffer controlled_buffer_1
  or or_1 (or_1_out, Out0, Upgrade0);
  assign JmpAddr = Out1 ? Dst_add_2_q : 32'bz;  // Controlled_Buffer controlled_buffer_2
  or or_2 (or_2_out, Out1, Upgrade1);
  assign JmpAddr = Out2 ? Dst_add_3_q : 32'bz;  // Controlled_Buffer controlled_buffer_3
  or or_3 (or_3_out, Out2, Upgrade2);
  assign JmpAddr = Out3 ? Dst_add_4_q : 32'bz;  // Controlled_Buffer controlled_buffer_4
  or or_4 (or_4_out, Out3, Upgrade3);
  Register #(.width(32), .trigger("rising"), .Select("low")) Dst_add_5 (
    .D(EX_BranchAddr), .en(L4), .Q(Dst_add_5_q), .clk(CLK));  // open: clr
  assign JmpAddr = Out4 ? Dst_add_5_q : 32'bz;  // Controlled_Buffer controlled_buffer_5
  or or_5 (or_5_out, Out4, Upgrade4);
  Register #(.width(32), .trigger("rising"), .Select("low")) Dst_add_6 (
    .D(EX_BranchAddr), .en(L5), .Q(Dst_add_6_q), .clk(CLK));  // open: clr
  assign JmpAddr = Out5 ? Dst_add_6_q : 32'bz;  // Controlled_Buffer controlled_buffer_6
  or or_6 (or_6_out, Out5, Upgrade5);
  assign JmpAddr = Out6 ? Dst_add_7_q : 32'bz;  // Controlled_Buffer controlled_buffer_7
  Register #(.width(32), .trigger("rising"), .Select("low")) Dst_add_7 (
    .D(EX_BranchAddr), .en(L6), .Q(Dst_add_7_q), .clk(CLK));  // open: clr
  or or_7 (or_7_out, Out6, Upgrade6);
  Register #(.width(32), .trigger("rising"), .Select("low")) Dst_add_8 (
    .D(EX_BranchAddr), .en(L7), .Q(Dst_add_8_q), .clk(CLK));  // open: clr
  or or_8 (or_8_out, Out7, Upgrade7);
  assign JmpAddr = Out7 ? Dst_add_8_q : 32'bz;  // Controlled_Buffer controlled_buffer_8
  Comparator #(.width(32), .mode("twosComplement")) comparator_1 (
    .a(PC), .b(Branch0), .eq(comparator_1_eq));  // open: gt, lt
  Comparator #(.width(1), .mode("twosComplement")) comparator_2 (
    .a(V0), .b(1'b1), .eq(comparator_2_eq));  // open: gt, lt
  Comparator #(.width(32), .mode("twosComplement")) comparator_3 (
    .a(PC), .b(Branch1), .eq(comparator_3_eq));  // open: gt, lt
  Comparator #(.width(1), .mode("twosComplement")) comparator_4 (
    .a(V1), .b(1'b1), .eq(comparator_4_eq));  // open: gt, lt
  Comparator #(.width(32), .mode("twosComplement")) comparator_5 (
    .a(PC), .b(Branch2), .eq(comparator_5_eq));  // open: gt, lt
  Comparator #(.width(1), .mode("twosComplement")) comparator_6 (
    .a(V2), .b(1'b1), .eq(comparator_6_eq));  // open: gt, lt
  Comparator #(.width(32), .mode("twosComplement")) comparator_7 (
    .a(PC), .b(Branch3), .eq(comparator_7_eq));  // open: gt, lt
  Comparator #(.width(1), .mode("twosComplement")) comparator_8 (
    .a(V3), .b(1'b1), .eq(comparator_8_eq));  // open: gt, lt
  Comparator #(.width(32), .mode("twosComplement")) comparator_9 (
    .a(PC), .b(Branch4), .eq(comparator_9_eq));  // open: gt, lt
  Comparator #(.width(1), .mode("twosComplement")) comparator_10 (
    .a(V4), .b(1'b1), .eq(comparator_10_eq));  // open: gt, lt
  Comparator #(.width(32), .mode("twosComplement")) comparator_11 (
    .a(PC), .b(Branch5), .eq(comparator_11_eq));  // open: gt, lt
  Comparator #(.width(1), .mode("twosComplement")) comparator_12 (
    .a(V5), .b(1'b1), .eq(comparator_12_eq));  // open: gt, lt
  Comparator #(.width(32), .mode("twosComplement")) comparator_13 (
    .a(PC), .b(Branch6), .eq(comparator_13_eq));  // open: gt, lt
  Comparator #(.width(1), .mode("twosComplement")) comparator_14 (
    .a(V6), .b(1'b1), .eq(comparator_14_eq));  // open: gt, lt
  Comparator #(.width(32), .mode("twosComplement")) comparator_15 (
    .a(PC), .b(Branch7), .eq(comparator_15_eq));  // open: gt, lt
  Comparator #(.width(1), .mode("twosComplement")) comparator_16 (
    .a(V7), .b(1'b1), .eq(comparator_16_eq));  // open: gt, lt
  and and_1 (Out0, comparator_1_eq, comparator_2_eq);
  and and_2 (Out1, comparator_3_eq, comparator_4_eq);
  and and_3 (Out2, comparator_5_eq, comparator_6_eq);
  and and_4 (Out3, comparator_7_eq, comparator_8_eq);
  and and_5 (Out4, comparator_9_eq, comparator_10_eq);
  and and_6 (Out5, comparator_11_eq, comparator_12_eq);
  and and_7 (Out6, comparator_13_eq, comparator_14_eq);
  and and_8 (Out7, comparator_15_eq, comparator_16_eq);
  Comparator #(.width(32), .mode("twosComplement")) comparator_17 (
    .a(EX_PC), .b(Branch0), .eq(comparator_17_eq));  // open: gt, lt
  Comparator #(.width(1), .mode("twosComplement")) comparator_18 (
    .a(V0), .b(1'b1), .eq(comparator_18_eq));  // open: gt, lt
  Comparator #(.width(32), .mode("twosComplement")) comparator_19 (
    .a(EX_PC), .b(Branch1), .eq(comparator_19_eq));  // open: gt, lt
  Comparator #(.width(1), .mode("twosComplement")) comparator_20 (
    .a(V1), .b(1'b1), .eq(comparator_20_eq));  // open: gt, lt
  Comparator #(.width(32), .mode("twosComplement")) comparator_21 (
    .a(EX_PC), .b(Branch2), .eq(comparator_21_eq));  // open: gt, lt
  Comparator #(.width(1), .mode("twosComplement")) comparator_22 (
    .a(V2), .b(1'b1), .eq(comparator_22_eq));  // open: gt, lt
  Comparator #(.width(32), .mode("twosComplement")) comparator_23 (
    .a(EX_PC), .b(Branch3), .eq(comparator_23_eq));  // open: gt, lt
  Comparator #(.width(1), .mode("twosComplement")) comparator_24 (
    .a(V3), .b(1'b1), .eq(comparator_24_eq));  // open: gt, lt
  Comparator #(.width(32), .mode("twosComplement")) comparator_25 (
    .a(EX_PC), .b(Branch6), .eq(comparator_25_eq));  // open: gt, lt
  Comparator #(.width(1), .mode("twosComplement")) comparator_26 (
    .a(V6), .b(1'b1), .eq(comparator_26_eq));  // open: gt, lt
  Comparator #(.width(32), .mode("twosComplement")) comparator_27 (
    .a(EX_PC), .b(Branch0), .eq(comparator_27_eq));  // open: gt, lt
  Comparator #(.width(1), .mode("twosComplement")) comparator_28 (
    .a(V0), .b(1'b1), .eq(comparator_28_eq));  // open: gt, lt
  Comparator #(.width(32), .mode("twosComplement")) comparator_29 (
    .a(EX_PC), .b(Branch5), .eq(comparator_29_eq));  // open: gt, lt
  Comparator #(.width(1), .mode("twosComplement")) comparator_30 (
    .a(V5), .b(1'b1), .eq(comparator_30_eq));  // open: gt, lt
  Comparator #(.width(32), .mode("twosComplement")) comparator_31 (
    .a(EX_PC), .b(Branch7), .eq(comparator_31_eq));  // open: gt, lt
  Comparator #(.width(1), .mode("twosComplement")) comparator_32 (
    .a(V7), .b(1'b1), .eq(comparator_32_eq));  // open: gt, lt
  and and_9 (Upgrade4, comparator_27_eq, comparator_28_eq);
  not not_1 (not_1_out, V0);
  not not_2 (not_2_out, V1);
  not not_3 (not_3_out, V2);
  not not_4 (not_4_out, V3);
  not not_5 (not_5_out, V4);
  not not_6 (not_6_out, V5);
  not not_7 (not_7_out, V6);
  not not_8 (not_8_out, V7);
  \归并比较  \u_归并比较_1  (.Y(C0), .X(C1), .Y_num(3'b000), .X_num(3'b001), .MAX(\归并比较_1_max ), .Max_num(\归并比较_1_max_num ));
  \归并比较  \u_归并比较_2  (.Y(C2), .X(C3), .Y_num(3'b010), .X_num(3'b011), .MAX(\归并比较_2_max ), .Max_num(\归并比较_2_max_num ));
  and and_10 (Upgrade0, comparator_17_eq, comparator_18_eq);
  and and_11 (Upgrade1, comparator_19_eq, comparator_20_eq);
  and and_12 (Upgrade2, comparator_21_eq, comparator_22_eq);
  and and_13 (Upgrade3, comparator_23_eq, comparator_24_eq);
  and and_14 (Upgrade6, comparator_25_eq, comparator_26_eq);
  and and_15 (Upgrade5, comparator_29_eq, comparator_30_eq);
  and and_16 (Upgrade7, comparator_31_eq, comparator_32_eq);
  \归并比较  \u_归并比较_3  (.Y(C4), .X(C5), .Y_num(3'b100), .X_num(3'b101), .MAX(\归并比较_3_max ), .Max_num(\归并比较_3_max_num ));
  \归并比较  \u_归并比较_4  (.Y(C6), .X(C7), .Y_num(3'b110), .X_num(3'b111), .MAX(\归并比较_4_max ), .Max_num(\归并比较_4_max_num ));
  Priority_Encoder #(.select(3), .disabled("Z")) priority_encoder_1 (
    .in0(not_1_out), .in1(not_2_out), .in2(not_3_out), .in3(not_4_out), .in4(not_5_out), .in5(not_6_out),
    .in6(not_7_out), .in7(not_8_out), .out(priority_encoder_1_out), .gs(priority_encoder_1_gs),
    .en_out(priority_encoder_1_en_out), .en_in(EX_Miss));
  \归并比较  \u_归并比较_5  (
    .Y(\归并比较_1_max ), .X(\归并比较_2_max ), .Y_num(\归并比较_1_max_num ), .X_num(\归并比较_2_max_num ),
    .MAX(\归并比较_5_max ), .Max_num(\归并比较_5_max_num ));
  \归并比较  \u_归并比较_6  (
    .Y(\归并比较_3_max ), .X(\归并比较_4_max ), .Y_num(\归并比较_3_max_num ), .X_num(\归并比较_4_max_num ),
    .MAX(\归并比较_6_max ), .Max_num(\归并比较_6_max_num ));
  \归并比较  \u_归并比较_7  (
    .Y(\归并比较_5_max ), .X(\归并比较_6_max ), .Y_num(\归并比较_5_max_num ), .X_num(\归并比较_6_max_num ),
    .Max_num(\归并比较_7_max_num ));  // open: MAX
  and and_17 (and_17_out, priority_encoder_1_gs, EX_Branch, EX_Miss);
  Demultiplexer #(.select(3), .width(1), .tristate("false"), .disabled(0), .enable("true")) demultiplexer_1 (
    .out0(L0_e), .out1(L1_e), .out2(L2_e), .out3(L3_e), .out4(L4_e), .out5(L5_e), .out6(L6_e), .out7(L7_e),
    .in(and_17_out), .sel(priority_encoder_1_out), .en(and_17_out));
  and and_18 (and_18_out, priority_encoder_1_en_out, EX_Miss);
  Demultiplexer #(.select(3), .width(1), .tristate("false"), .disabled(0), .enable("true")) demultiplexer_2 (
    .out0(L0_f), .out1(L1_f), .out2(L2_f), .out3(L3_f), .out4(L4_f), .out5(L5_f), .out6(L6_f), .out7(L7_f),
    .in(and_19_out), .sel(\归并比较_7_max_num ), .en(and_19_out));
  and and_19 (and_19_out, and_18_out, EX_Branch, EX_Miss);
  Priority_Encoder #(.select(3), .disabled("Z")) priority_encoder_2 (
    .in0(Out0), .in1(Out1), .in2(Out2), .in3(Out3), .in4(Out4), .in5(Out6), .in6(Out5), .in7(Out7),
    .out(pre_num));  // open: gs, en_out, en_in
  not not_9 (EX_Miss, EX_Hit);
  or or_9 (EX_Hit, Upgrade0, Upgrade1, Upgrade2, Upgrade3, Upgrade4, Upgrade5, Upgrade6, Upgrade7);
  Priority_Encoder #(.select(3), .disabled("Z")) priority_encoder_3 (
    .in0(Upgrade0), .in1(Upgrade1), .in2(Upgrade2), .in3(Upgrade3), .in4(Upgrade4), .in5(Upgrade5),
    .in6(Upgrade6), .in7(Upgrade7), .out(priority_encoder_3_out));  // open: gs, en_out, en_in
  or or_10 (Hit, Out0, Out1, Out2, Out3, Out4, Out6, Out5, Out7);
  not not_10 (Miss, Hit);
  and and_20 (and_20_out, EX_Hit, EX_Branch);
  Demultiplexer #(.select(3), .width(1), .tristate("false"), .disabled(0), .enable("true")) demultiplexer_3 (
    .out0(L0_U), .out1(L1_U), .out2(L2_U), .out3(L3_U), .out4(L4_U), .out5(L5_U), .out6(L6_U), .out7(L7_U),
    .in(1'b1), .sel(priority_encoder_3_out), .en(and_20_out));
  Multiplexer #(.select(3), .width(2), .disabled(0), .enable("true")) multiplexer_1 (
    .in0(Pre0), .in1(Pre1), .in2(Pre2), .in3(Pre3), .in4(Pre4), .in5(Pre5), .in6(Pre6), .in7(Pre7),
    .out(multiplexer_1_out), .sel(priority_encoder_3_out), .en(EX_Branch));
  or or_11 (L0, L0_e, L0_f, L0_U);
  or or_12 (L1, L1_e, L1_f, L1_U);
  or or_13 (L2, L2_e, L2_f, L2_U);
  or or_14 (L3, L3_e, L3_f, L3_U);
  or or_15 (L4, L4_e, L4_f, L4_U);
  or or_16 (L5, L5_f, L5_e, L5_U);
  or or_17 (L6, L6_e, L6_f, L6_U);
  Multiplexer #(.select(1), .width(2), .disabled("Z"), .enable("false")) multiplexer_2 (
    .in0(2'b01), .in1(2'b11), .out(multiplexer_2_out), .sel(EX_BranchTaken));
  Pre pre_1 (.Jmp(EX_BranchTaken), .pre_in(multiplexer_1_out), .pre_out(pre_1_pre_out));
  or or_18 (L7, L7_e, L7_f, L7_U);
  Multiplexer #(.select(3), .width(2), .disabled("Z"), .enable("false")) multiplexer_3 (
    .in0(Pre0), .in1(Pre1), .in2(Pre2), .in3(Pre3), .in4(Pre4), .in5(Pre5), .in6(Pre6), .in7(Pre7),
    .out(multiplexer_3_out), .sel(pre_num));
  Multiplexer #(.select(1), .width(2), .disabled("Z"), .enable("false")) multiplexer_4 (
    .in0(multiplexer_2_out), .in1(pre_1_pre_out), .out(Pre), .sel(EX_Hit));
  Decoder #(.select(2), .tristate("false"), .disabled(0), .enable("true")) decoder_1 (
    .out2(decoder_1_out2), .out3(decoder_1_out3), .sel(multiplexer_3_out), .en(Hit));  // open: out0, out1
  or or_19 (or_19_out, decoder_1_out2, decoder_1_out3);
  Multiplexer #(.select(1), .width(1), .disabled("Z"), .enable("false")) multiplexer_5 (
    .in0(1'b0), .in1(1'b1), .out(PredictJmp), .sel(or_19_out));

  // Other names for the same wires on the sheet: Dst_add[31:0] = EX_BranchAddr; Dst_out[31:0] = JmpAddr;
  //   PC_in[31:0] = EX_PC
endmodule
